// Logisim project apple-pie-8bit.circ as structural Verilog: 1 circuit, main circuit 8Bit Computer
module _8Bit_Computer (
  input  Select,
  input  Manual_Pulse,
  input  in_3,
  input  in_4,
  input  in_5,
  input  in_6,
  input  in_7,
  input  in_8,
  input  in_9,
  input  in_10,
  input  ENABLE,
  input  HLT,
  input  CLEAR,
  input  ENABLE_2,
  input  LOAD,
  input  ENABLE_3,
  input  EO,
  input  LOAD_2,
  input  SU,
  input  in_20,
  input  in_21,
  input  in_22,
  input  in_23,
  input  in_24,
  input  ENABLE_4,
  input  LOAD_3,
  input  ENABLE_5,
  input  LOAD_4,
  input  ENABLE_6,
  input  LOAD_5,
  output out_31,
  output out_32,
  output out_33,
  output out_34,
  output out_35,
  output out_36,
  output out_37,
  output out_38,
  output out_39,
  output out_40,
  output out_41,
  output out_42,
  output out_43,
  output out_44,
  output out_45,
  output out_46,
  output out_47,
  output out_48,
  output out_49,
  output out_50,
  output out_51,
  output out_52,
  output out_53,
  output out_54,
  output out_55,
  output out_56,
  output out_57,
  output out_58,
  output out_59,
  output out_60,
  output out_61,
  output out_62,
  output out_63,
  output out_64,
  output out_65,
  output out_66,
  output out_67
);

  wire and_1_out, and_2_out, and_3_out, Astable_Pulse_out, not_1_out, not_2_out, or_1_out;
  wire [3:0] and_4_out, and_5_out, not_3_out, register_4_q, undriven;
  wire [7:0] register_3_q, xor_1_out;

  Clock Astable_Pulse (.out(Astable_Pulse_out));
  assign xor_1_out = {out_60, out_61, out_62, out_63, out_64, out_65, out_66, out_67} ^ {8{SU}};  // XOR_Gate xor_1, 8 bits wide
  not not_1 (not_1_out, Select);
  not not_2 (not_2_out, HLT);
  Register register_1 (
    .D({out_31, out_32, out_33, out_34, out_35, out_36, out_37, out_38}), .en(LOAD),
    .Q({out_39, out_40, out_41, out_42, out_43, out_44, out_45, out_46}), .clk(and_3_out), .clr(CLEAR));
  Adder adder_1 (
    .a({out_39, out_40, out_41, out_42, out_43, out_44, out_45, out_46}), .b(xor_1_out),
    .out({out_47, out_48, out_49, out_50, out_51, out_52, out_53, out_54}), .cin(SU), .cout(out_55));
  Register register_2 (
    .D({out_31, out_32, out_33, out_34, out_35, out_36, out_37, out_38}), .en(LOAD_3),
    .Q({out_60, out_61, out_62, out_63, out_64, out_65, out_66, out_67}), .clk(and_3_out), .clr(CLEAR));
  Register register_3 (
    .D({out_31, out_32, out_33, out_34, out_35, out_36, out_37, out_38}), .en(LOAD_5), .Q(register_3_q),
    .clk(and_3_out), .clr(CLEAR));
  LED led_1 (.in(register_3_q[7]));
  LED led_2 (.in(register_3_q[4]));
  LED led_3 (.in(register_3_q[6]));
  LED led_4 (.in(register_3_q[5]));
  and and_1 (and_1_out, Astable_Pulse_out, Select);
  and and_2 (and_2_out, not_1_out, Manual_Pulse);
  LED led_5 (.in(register_3_q[2]));
  LED led_6 (.in(register_3_q[0]));
  LED led_7 (.in(register_3_q[3]));
  LED led_8 (.in(register_3_q[1]));
  or or_1 (or_1_out, and_1_out, and_2_out);
  assign {out_31, out_32, out_33, out_34, out_35, out_36, out_37, out_38} = ENABLE_2 ? {out_39, out_40, out_41, out_42, out_43, out_44, out_45, out_46} : 8'bz;  // Controlled_Buffer controlled_buffer_1
  assign {out_31, out_32, out_33, out_34, out_35, out_36, out_37, out_38} = EO ? {out_47, out_48, out_49, out_50, out_51, out_52, out_53, out_54} : 8'bz;  // Controlled_Buffer controlled_buffer_2
  assign {out_31, out_32, out_33, out_34, out_35, out_36, out_37, out_38} = ENABLE_4 ? {out_60, out_61, out_62, out_63, out_64, out_65, out_66, out_67} : 8'bz;  // Controlled_Buffer controlled_buffer_3
  and and_3 (and_3_out, or_1_out, not_2_out);
  assign {out_31, out_32, out_33, out_34, out_35, out_36, out_37, out_38} = ENABLE_6 ? {undriven, register_3_q[3:0]} : 8'bz;  // Controlled_Buffer controlled_buffer_4
  Pull_Resistor pull_resistor_1 (.node({out_31, out_32, out_33, out_34, out_35, out_36, out_37, out_38}));
  assign {out_31, out_32, out_33, out_34, out_35, out_36, out_37, out_38} = ENABLE ? {in_3, in_4, in_5, in_6, in_7, in_8, in_9, in_10} : 8'bz;  // Controlled_Buffer controlled_buffer_5
  Register #(.width(4)) register_4 (
    .D({out_35, out_36, out_37, out_38}), .en(LOAD_2), .Q(register_4_q), .clk(and_3_out), .clr(CLEAR));
  assign not_3_out = ~{4{in_24}};  // NOT_Gate not_3, 4 bits wide
  assign {out_35, out_36, out_37, out_38} = ENABLE_3 ? register_4_q : 4'bz;  // Controlled_Buffer controlled_buffer_6
  assign and_4_out = register_4_q & not_3_out;  // AND_Gate and_4, 4 bits wide
  assign and_5_out = {in_20, in_21, in_22, in_23} & {4{in_24}};  // AND_Gate and_5, 4 bits wide
  RAM #(.addrWidth(4), .bus("separate")) ram_1 (
    .addr({out_56, out_57, out_58, out_59}), .str(LOAD_4), .clk(and_3_out), .ld(ENABLE_5), .clr(CLEAR));  // open: din, data, sel
  assign {out_56, out_57, out_58, out_59} = and_4_out | and_5_out;  // OR_Gate or_2, 4 bits wide
endmodule
