// Digital circuit accumulator.dig as structural Verilog
module accumulator (
  input  ADDR_ASSERT,
  input  XFER_ASSERT,
  input  XFER_LOAD,
  input  DBUS_ALOAD,
  input  DBUS_BLOAD,
  input  DBUS_AASSERT,
  input  DBUS_BASSERT,
  input  LHS_AASSERT,
  input  LHS_BASSERT,
  input  RHS_AASSERT,
  input  RHS_BASSERT,
  input  [7:0] DBUS_IN,
  input  [15:0] XFER_IN,
  input  CLK,
  input  CLR,
  output [7:0] DBUS_OUT,
  output [15:0] XFER_OUT,
  output [15:0] ADDR_OUT
);

  wire assert_a_xfer, assert_b_xfer, d0, d1, d2, d3, d4, d5, d6, d7, d8, d9, d10, d11, d12, d13, d14, d15,
       load_a, load_b, q0, q1, q2, q3, q4, q5, q6, q7, q8, q9, q10, q11, q12, q13, q14, q15;

  // _7408 _7408_1: pin names not known; wires that end beside it: XFER_LOAD, DBUS_ALOAD, XFER_LOAD, DBUS_BLOAD, XFER_ASSERT, LHS_AASSERT, XFER_ASSERT, RHS_BASSERT, 1'b1, 1'b0, load_a, load_b, assert_a_xfer, assert_b_xfer
  // _74173 A_Hi: pin names not known; wires that end beside it: d12, 1'b1, 1'b0, CLR, d13, d14, d15, CLK, load_a, load_a, 1'b0, 1'b0, q12, q13, q14, q15
  // _74157 A_Hi_MUX_In: pin names not known; wires that end beside it: DBUS_ALOAD, DBUS_IN[4], DBUS_IN[5], DBUS_IN[6], DBUS_IN[7], XFER_IN[12], XFER_IN[13], XFER_IN[14], XFER_IN[15], 1'b0, 1'b1, 1'b0, d12, d13, d14, d15
  // _74173 A_Lo: pin names not known; wires that end beside it: d8, 1'b1, 1'b0, CLR, d9, d10, d11, CLK, load_a, load_a, 1'b0, 1'b0, q8, q9, q10, q11
  // _74157 A_Lo_MUX_In: pin names not known; wires that end beside it: DBUS_ALOAD, DBUS_IN[0], DBUS_IN[1], DBUS_IN[2], DBUS_IN[3], XFER_IN[8], XFER_IN[9], XFER_IN[10], XFER_IN[11], 1'b0, 1'b1, 1'b0, d8, d9, d10, d11
  // _74173 B_Hi: pin names not known; wires that end beside it: d4, 1'b1, 1'b0, CLR, d5, d6, d7, CLK, load_b, load_b, 1'b0, 1'b0, q4, q5, q6, q7
  // _74157 B_Hi_MUX_In: pin names not known; wires that end beside it: DBUS_BLOAD, DBUS_IN[4], DBUS_IN[5], DBUS_IN[6], DBUS_IN[7], XFER_IN[4], XFER_IN[5], XFER_IN[6], XFER_IN[7], 1'b0, 1'b1, 1'b0, d4, d5, d6, d7
  // _74173 B_Lo: pin names not known; wires that end beside it: d0, 1'b1, 1'b0, CLR, d1, d2, d3, CLK, load_b, load_b, 1'b0, 1'b0, q0, q1, q2, q3, 1'b1, 1'b0
  // _74157 B_Lo_MUX_In: pin names not known; wires that end beside it: DBUS_BLOAD, DBUS_IN[0], DBUS_IN[1], DBUS_IN[2], DBUS_IN[3], XFER_IN[0], XFER_IN[1], XFER_IN[2], XFER_IN[3], 1'b0, 1'b1, 1'b0, d0, d1, d2, d3
  // _74245 B_to_ADDR: pin names not known; wires that end beside it: 1'b1, ADDR_ASSERT, q0, ADDR_OUT[0], q1, ADDR_OUT[1], q2, ADDR_OUT[2], q3, ADDR_OUT[3], q4, ADDR_OUT[4], q5, ADDR_OUT[5], q6, ADDR_OUT[6], q7, ADDR_OUT[7]
  // _74245 A_to_ADDR: pin names not known; wires that end beside it: 1'b1, ADDR_ASSERT, q8, ADDR_OUT[8], q9, ADDR_OUT[9], q10, ADDR_OUT[10], q11, ADDR_OUT[11], q12, ADDR_OUT[12], q13, ADDR_OUT[13], q14, ADDR_OUT[14], q15, ADDR_OUT[15], 1'b1, 1'b0
  // _74245 B_to_DBUS: pin names not known; wires that end beside it: 1'b1, DBUS_BASSERT, q0, DBUS_IN[0], q1, DBUS_IN[1], q2, DBUS_IN[2], q3, DBUS_IN[3], q4, DBUS_IN[4], q5, DBUS_IN[5], q6, DBUS_IN[6], q7, DBUS_IN[7], 1'b1
  // _74245 A_to_DBUS: pin names not known; wires that end beside it: 1'b0, 1'b1, DBUS_AASSERT, q8, DBUS_IN[0], q9, DBUS_IN[1], q10, DBUS_IN[2], q11, DBUS_IN[3], q12, DBUS_IN[4], q13, DBUS_IN[5], q14, DBUS_IN[6], q15, DBUS_IN[7], 1'b1, 1'b0
  // _74245 B_to_RHS: pin names not known; wires that end beside it: 1'b1, assert_b_xfer, q0, XFER_IN[0], q1, XFER_IN[1], q2, XFER_IN[2], q3, XFER_IN[3], q4, XFER_IN[4], q5, XFER_IN[5], q6, XFER_IN[6], q7, XFER_IN[7], 1'b1
  // _74245 A_to_RHS: pin names not known; wires that end beside it: 1'b0, 1'b1, RHS_AASSERT, q8, XFER_IN[0], q9, XFER_IN[1], q10, XFER_IN[2], q11, XFER_IN[3], q12, XFER_IN[4], q13, XFER_IN[5], q14, XFER_IN[6], q15, XFER_IN[7], 1'b1, 1'b0
  // _74245 B_to_LHS: pin names not known; wires that end beside it: 1'b1, LHS_BASSERT, q0, XFER_IN[8], q1, XFER_IN[9], q2, XFER_IN[10], q3, XFER_IN[11], q4, XFER_IN[12], q5, XFER_IN[13], q6, XFER_IN[14], q7, XFER_IN[15], 1'b1
  // _74245 A_to_LHS: pin names not known; wires that end beside it: assert_a_xfer, 1'b0, 1'b1, q8, XFER_IN[8], q9, XFER_IN[9], q10, XFER_IN[10], q11, XFER_IN[11], q12, XFER_IN[12], q13, XFER_IN[13], q14, XFER_IN[14], q15, XFER_IN[15], 1'b1, 1'b0

  assign DBUS_OUT = DBUS_IN;
  assign XFER_OUT = XFER_IN;

  // Other names for the same wires on the sheet: addr[15:0] = ADDR_OUT; addr0 = ADDR_OUT[0]; addr1 = ADDR_OUT[1];
  //   addr2 = ADDR_OUT[2]; addr3 = ADDR_OUT[3]; addr4 = ADDR_OUT[4]; addr5 = ADDR_OUT[5]; addr6 = ADDR_OUT[6];
  //   addr7 = ADDR_OUT[7]; addr8 = ADDR_OUT[8]; addr9 = ADDR_OUT[9]; addr10 = ADDR_OUT[10]; addr11 = ADDR_OUT[11];
  //   addr12 = ADDR_OUT[12]; addr13 = ADDR_OUT[13]; addr14 = ADDR_OUT[14]; addr15 = ADDR_OUT[15];
  //   assert_a_dbus = DBUS_AASSERT; assert_a_lhs = LHS_AASSERT; assert_a_rhs = RHS_AASSERT; assert_addr = ADDR_ASSERT;
  //   assert_b_dbus = DBUS_BASSERT; assert_b_lhs = LHS_BASSERT; assert_b_rhs = RHS_BASSERT; assert_xfer = XFER_ASSERT;
  //   dbus[7:0] = DBUS_IN; dbus0 = DBUS_IN[0]; dbus1 = DBUS_IN[1]; dbus2 = DBUS_IN[2]; dbus3 = DBUS_IN[3];
  //   dbus4 = DBUS_IN[4]; dbus5 = DBUS_IN[5]; dbus6 = DBUS_IN[6]; dbus7 = DBUS_IN[7]; load_a_dbus = DBUS_ALOAD;
  //   load_b_dbus = DBUS_BLOAD; load_xfer = XFER_LOAD; xfer[15:0] = XFER_IN; xfer0 = XFER_IN[0]; xfer1 = XFER_IN[1];
  //   xfer2 = XFER_IN[2]; xfer3 = XFER_IN[3]; xfer4 = XFER_IN[4]; xfer5 = XFER_IN[5]; xfer6 = XFER_IN[6];
  //   xfer7 = XFER_IN[7]; xfer8 = XFER_IN[8]; xfer9 = XFER_IN[9]; xfer10 = XFER_IN[10]; xfer11 = XFER_IN[11];
  //   xfer12 = XFER_IN[12]; xfer13 = XFER_IN[13]; xfer14 = XFER_IN[14]; xfer15 = XFER_IN[15]
endmodule
