// Digital circuit address_register.dig as structural Verilog
module address_register (
  input  [15:0] XFER_BUS_IN,
  input  CLK,
  input  CLR,
  input  XFER_LOAD,
  input  ADDR_ASSERT,
  input  XFER_ASSERT,
  input  INC,
  input  DEC,
  output [15:0] ADDR_BUS,
  output [15:0] XFER_BUS_OUT
);

  wire Bits_4_7_p2, Bits_4_7_p3, Bits_8_11_p2, Bits_8_11_p3, Bits_12_15_p2, Bits_12_15_p3, Bits_12_15_p11,
       Bits_12_15_p12, q0, q1, q2, q3, q4, q5, q6, q7, q8, q9, q10, q11, q12, q13, q14, q15;

  // _74193 Bits_12_15: pin names not known; wires that end beside it: XFER_BUS_IN[12], Bits_12_15_p2, Bits_12_15_p3, XFER_BUS_IN[13], XFER_BUS_IN[14], XFER_BUS_IN[15], CLR, XFER_LOAD, 1'b1, 1'b0, Bits_12_15_p11, Bits_12_15_p12, q12, q13, q14, q15
  // _74574 _74574_1: pin names not known; wires that end beside it: XFER_ASSERT, CLK, q8, q9, q10, q11, q12, q13, q14, q15, 1'b1, 1'b0, XFER_BUS_IN[8], XFER_BUS_IN[9], XFER_BUS_IN[10], XFER_BUS_IN[11], XFER_BUS_IN[12], XFER_BUS_IN[13], XFER_BUS_IN[14], XFER_BUS_IN[15]
  // NotConnected on Bits_12_15_p11
  // NotConnected on Bits_12_15_p12
  // _74193 Bits_8_11: pin names not known; wires that end beside it: XFER_BUS_IN[8], Bits_8_11_p2, Bits_8_11_p3, XFER_BUS_IN[9], XFER_BUS_IN[10], XFER_BUS_IN[11], CLR, XFER_LOAD, 1'b1, 1'b0, Bits_12_15_p2, Bits_12_15_p3, q8, q9, q10, q11
  // _74574 _74574_2: pin names not known; wires that end beside it: XFER_ASSERT, CLK, q0, q1, q2, q3, q4, q5, q6, q7, 1'b1, 1'b0, XFER_BUS_IN[0], XFER_BUS_IN[1], XFER_BUS_IN[2], XFER_BUS_IN[3], XFER_BUS_IN[4], XFER_BUS_IN[5], XFER_BUS_IN[6], XFER_BUS_IN[7]
  // _74574 _74574_3: pin names not known; wires that end beside it: ADDR_ASSERT, CLK, q8, q9, q10, q11, q12, q13, q14, q15, 1'b1, 1'b0, ADDR_BUS[8], ADDR_BUS[9], ADDR_BUS[10], ADDR_BUS[11], ADDR_BUS[12], ADDR_BUS[13], ADDR_BUS[14], ADDR_BUS[15]
  // _74193 Bits_4_7: pin names not known; wires that end beside it: XFER_BUS_IN[4], Bits_4_7_p2, Bits_4_7_p3, XFER_BUS_IN[5], XFER_BUS_IN[6], XFER_BUS_IN[7], CLR, XFER_LOAD, 1'b1, 1'b0, Bits_8_11_p2, Bits_8_11_p3, q4, q5, q6, q7
  // _74574 _74574_4: pin names not known; wires that end beside it: ADDR_ASSERT, CLK, q0, q1, q2, q3, q4, q5, q6, q7, 1'b1, 1'b0, ADDR_BUS[0], ADDR_BUS[1], ADDR_BUS[2], ADDR_BUS[3], ADDR_BUS[4], ADDR_BUS[5], ADDR_BUS[6], ADDR_BUS[7]
  // _74193 Bits_0_3: pin names not known; wires that end beside it: XFER_BUS_IN[0], DEC, INC, XFER_BUS_IN[1], XFER_BUS_IN[2], XFER_BUS_IN[3], CLR, XFER_LOAD, 1'b1, 1'b0, Bits_4_7_p2, Bits_4_7_p3, q0, q1, q2, q3, CLR, XFER_LOAD

  assign XFER_BUS_OUT = XFER_BUS_IN;

  // Other names for the same wires on the sheet: addr[15:0] = ADDR_BUS; addr0 = ADDR_BUS[0]; addr1 = ADDR_BUS[1];
  //   addr2 = ADDR_BUS[2]; addr3 = ADDR_BUS[3]; addr4 = ADDR_BUS[4]; addr5 = ADDR_BUS[5]; addr6 = ADDR_BUS[6];
  //   addr7 = ADDR_BUS[7]; addr8 = ADDR_BUS[8]; addr9 = ADDR_BUS[9]; addr10 = ADDR_BUS[10]; addr11 = ADDR_BUS[11];
  //   addr12 = ADDR_BUS[12]; addr13 = ADDR_BUS[13]; addr14 = ADDR_BUS[14]; addr15 = ADDR_BUS[15];
  //   xfer[15:0] = XFER_BUS_IN; xfer0 = XFER_BUS_IN[0]; xfer1 = XFER_BUS_IN[1]; xfer2 = XFER_BUS_IN[2];
  //   xfer3 = XFER_BUS_IN[3]; xfer4 = XFER_BUS_IN[4]; xfer5 = XFER_BUS_IN[5]; xfer6 = XFER_BUS_IN[6];
  //   xfer7 = XFER_BUS_IN[7]; xfer8 = XFER_BUS_IN[8]; xfer9 = XFER_BUS_IN[9]; xfer10 = XFER_BUS_IN[10];
  //   xfer11 = XFER_BUS_IN[11]; xfer12 = XFER_BUS_IN[12]; xfer13 = XFER_BUS_IN[13]; xfer14 = XFER_BUS_IN[14];
  //   xfer15 = XFER_BUS_IN[15]
endmodule
