// Digital circuit alu_logic_unit.dig as structural Verilog
module alu_logic_unit (
  input  [7:0] RHS,
  input  [7:0] LHS,
  input  LOGIC_3,
  input  LOGIC_2,
  input  LOGIC_1,
  input  LOGIC_0,
  output [7:0] LOGIC_OUT
);

  wire _74153_1_p8, _74153_1_p9, _74153_1_p10, _74153_1_p11, _74153_1_p12, _74153_1_p16, _74153_2_p8,
       _74153_2_p9, _74153_2_p10, _74153_2_p11, _74153_2_p12, _74153_2_p16, _74153_3_p16, _74153_4_p16,
       _74153_5_p8, _74153_5_p9, _74153_5_p10, _74153_5_p11, _74153_5_p12, _74153_5_p16, _74153_6_p8,
       _74153_6_p9, _74153_6_p10, _74153_6_p11, _74153_6_p12, _74153_6_p16, _74153_7_p8, _74153_7_p9,
       _74153_7_p10, _74153_7_p11, _74153_7_p12, _74153_7_p16, _74153_8_p8, _74153_8_p9, _74153_8_p10,
       _74153_8_p11, _74153_8_p12, _74153_8_p16, notconnected_13_out, notconnected_14_out,
       notconnected_15_out, notconnected_16_out, notconnected_17_out, notconnected_18_out,
       notconnected_19_out, notconnected_20_out, notconnected_21_out, notconnected_22_out;

  // _74153 _74153_1: pin names not known; wires that end beside it: LHS[7], RHS[7], 1'b1, LOGIC_0, LOGIC_1, LOGIC_2, LOGIC_3, _74153_1_p8, _74153_1_p9, _74153_1_p10, _74153_1_p11, _74153_1_p12, 1'b1, 1'b0, LOGIC_OUT[7], _74153_1_p16
  // NotConnected on _74153_1_p8
  // NotConnected on _74153_1_p9
  // NotConnected on _74153_1_p10
  // NotConnected on _74153_1_p11
  // NotConnected on _74153_1_p12
  // _74153 _74153_2: pin names not known; wires that end beside it: LHS[3], RHS[3], 1'b1, LOGIC_0, LOGIC_1, LOGIC_2, LOGIC_3, _74153_2_p8, _74153_2_p9, _74153_2_p10, _74153_2_p11, _74153_2_p12, 1'b1, 1'b0, LOGIC_OUT[3], _74153_2_p16
  // NotConnected on _74153_2_p8
  // NotConnected on _74153_2_p9
  // NotConnected on _74153_2_p10
  // NotConnected on _74153_2_p11
  // NotConnected on _74153_2_p12
  // NotConnected on _74153_1_p16
  // NotConnected on _74153_2_p16
  // NotConnected on notconnected_13_out
  // NotConnected on notconnected_14_out
  // NotConnected on notconnected_15_out
  // NotConnected on notconnected_16_out
  // NotConnected on notconnected_17_out
  // NotConnected on notconnected_18_out
  // NotConnected on notconnected_19_out
  // NotConnected on notconnected_20_out
  // NotConnected on notconnected_21_out
  // NotConnected on notconnected_22_out
  // _74153 _74153_3: pin names not known; wires that end beside it: LHS[6], RHS[6], 1'b1, LOGIC_0, LOGIC_1, LOGIC_2, LOGIC_3, notconnected_13_out, notconnected_14_out, notconnected_15_out, notconnected_16_out, notconnected_17_out, 1'b1, 1'b0, LOGIC_OUT[6], _74153_3_p16
  // _74153 _74153_4: pin names not known; wires that end beside it: LHS[2], RHS[2], 1'b1, LOGIC_0, LOGIC_1, LOGIC_2, LOGIC_3, notconnected_18_out, notconnected_19_out, notconnected_20_out, notconnected_21_out, notconnected_22_out, 1'b1, 1'b0, LOGIC_OUT[2], _74153_4_p16
  // NotConnected on _74153_3_p16
  // NotConnected on _74153_4_p16
  // _74153 _74153_5: pin names not known; wires that end beside it: LHS[5], RHS[5], 1'b1, LOGIC_0, LOGIC_1, LOGIC_2, LOGIC_3, _74153_5_p8, _74153_5_p9, _74153_5_p10, _74153_5_p11, _74153_5_p12, 1'b1, 1'b0, LOGIC_OUT[5], _74153_5_p16
  // NotConnected on _74153_5_p8
  // NotConnected on _74153_5_p9
  // NotConnected on _74153_5_p10
  // NotConnected on _74153_5_p11
  // NotConnected on _74153_5_p12
  // _74153 _74153_6: pin names not known; wires that end beside it: LHS[1], RHS[1], 1'b1, LOGIC_0, LOGIC_1, LOGIC_2, LOGIC_3, _74153_6_p8, _74153_6_p9, _74153_6_p10, _74153_6_p11, _74153_6_p12, 1'b1, 1'b0, LOGIC_OUT[1], _74153_6_p16
  // NotConnected on _74153_6_p8
  // NotConnected on _74153_6_p9
  // NotConnected on _74153_6_p10
  // NotConnected on _74153_6_p11
  // NotConnected on _74153_6_p12
  // NotConnected on _74153_5_p16
  // NotConnected on _74153_6_p16
  // _74153 _74153_7: pin names not known; wires that end beside it: LHS[4], RHS[4], 1'b1, LOGIC_0, LOGIC_1, LOGIC_2, LOGIC_3, _74153_7_p8, _74153_7_p9, _74153_7_p10, _74153_7_p11, _74153_7_p12, 1'b1, 1'b0, LOGIC_OUT[4], _74153_7_p16
  // NotConnected on _74153_7_p8
  // NotConnected on _74153_7_p9
  // NotConnected on _74153_7_p10
  // NotConnected on _74153_7_p11
  // NotConnected on _74153_7_p12
  // _74153 _74153_8: pin names not known; wires that end beside it: LHS[0], RHS[0], 1'b1, LOGIC_0, LOGIC_1, LOGIC_2, LOGIC_3, _74153_8_p8, _74153_8_p9, _74153_8_p10, _74153_8_p11, _74153_8_p12, 1'b1, 1'b0, LOGIC_OUT[0], _74153_8_p16
  // NotConnected on _74153_8_p8
  // NotConnected on _74153_8_p9
  // NotConnected on _74153_8_p10
  // NotConnected on _74153_8_p11
  // NotConnected on _74153_8_p12
  // NotConnected on _74153_7_p16
  // NotConnected on _74153_8_p16
  // Pins of 1 and 8 bits meet at LOGIC_OUT

  // Other names for the same wires on the sheet: logic0 = LOGIC_0; logic1 = LOGIC_1; logic2 = LOGIC_2;
  //   logic3 = LOGIC_3; q[7:0] = LOGIC_OUT; q0 = LOGIC_OUT[0]; q1 = LOGIC_OUT[1]; q2 = LOGIC_OUT[2];
  //   q3 = LOGIC_OUT[3]; q4 = LOGIC_OUT[4]; q5 = LOGIC_OUT[5]; q6 = LOGIC_OUT[6]; q7 = LOGIC_OUT[7]
endmodule
