// Digital circuit control_unit.dig as structural Verilog
module control_unit (
  input  OPCODE_7,
  input  IRQ,
  input  RST,
  input  EXT,
  input  F_INHIB,
  input  F_NEG,
  input  F_OVER,
  input  F_ZERO,
  input  F_CARRY,
  input  CLK,
  input  OPCODE_0,
  input  OPCODE_1,
  input  OPCODE_2,
  input  OPCODE_3,
  input  OPCODE_4,
  input  OPCODE_5,
  input  OPCODE_6,
  output XFER_ASSERT_4,
  output XFER_LOAD_0,
  output EXT_FLIP,
  output RST_USEQ,
  output CLR_RST,
  output BRK,
  output ALU_OP_4,
  output DBUS_LOAD_3,
  output DBUS_ASSERT_0,
  output DBUS_ASSERT_1,
  output DBUS_ASSERT_2,
  output DBUS_ASSERT_3,
  output DBUS_LOAD_0,
  output DBUS_LOAD_1,
  output DBUS_LOAD_2,
  output ALU_OP_0,
  output ALU_OP_1,
  output ALU_OP_2,
  output ALU_OP_3,
  output XFER_ASSERT_0,
  output XFER_ASSERT_1,
  output XFER_ASSERT_2,
  output XFER_ASSERT_3,
  output XFER_LOAD_1,
  output ADDR_ASSERT_0,
  output ADDR_ASSERT_1,
  output ADDR_ASSERT_2,
  output COUNT_INC_0,
  output COUNT_INC_1,
  output COUNT_INC_2,
  output COUNT_DEC_0,
  output COUNT_DEC_1
);

  wire sequencer_p1, sequencer_p2, sequencer_p4, sequencer_p5, sequencer_p6, sequencer_p11, sequencer_p12,
       sequencer_p16;
  wire [1:0] mode;
  wire [2:0] t_state;
  wire [7:0] ucode_2_d, ucode_3_d, ucode_4_d, ucode_d;

  // _74193 sequencer: pin names not known; wires that end beside it: sequencer_p1, sequencer_p2, CLK, sequencer_p4, sequencer_p5, sequencer_p6, RST_USEQ, 1'b1, 1'b1, 1'b0, sequencer_p11, sequencer_p12, t_state[0], t_state[1], t_state[2], sequencer_p16
  // NotConnected on sequencer_p1
  // NotConnected on sequencer_p2
  // NotConnected on sequencer_p4
  // NotConnected on sequencer_p5
  // NotConnected on sequencer_p6
  // NotConnected on sequencer_p11
  // NotConnected on sequencer_p12
  // NotConnected on sequencer_p16
  EEPROM #(.AddrBits(19), .Bits(8)) ucode (
    .A({mode, IRQ, OPCODE_7, OPCODE_6, OPCODE_5, OPCODE_4, OPCODE_3, OPCODE_2, OPCODE_1, OPCODE_0, F_CARRY, F_ZERO, F_OVER, F_NEG, F_INHIB, t_state}),
    .CS(1'b1), .WE(1'b0), .OE(1'b1), .D(ucode_d));
  EEPROM #(.AddrBits(19), .Bits(8)) ucode_2 (
    .A({mode, IRQ, OPCODE_7, OPCODE_6, OPCODE_5, OPCODE_4, OPCODE_3, OPCODE_2, OPCODE_1, OPCODE_0, F_CARRY, F_ZERO, F_OVER, F_NEG, F_INHIB, t_state}),
    .CS(1'b1), .WE(1'b0), .OE(1'b1), .D(ucode_2_d));
  // _74574 _74574_1: pin names not known; wires that end beside it: 1'b0, CLK, ucode_d[0], ucode_d[1], ucode_d[2], ucode_d[3], ucode_d[4], ucode_d[5], ucode_d[6], ucode_d[7], 1'b1, 1'b0, ALU_OP_0, ALU_OP_1, ALU_OP_2, ALU_OP_3, ALU_OP_4, XFER_ASSERT_0, XFER_ASSERT_1, XFER_ASSERT_2
  // _74574 _74574_2: pin names not known; wires that end beside it: 1'b0, CLK, ucode_2_d[0], ucode_2_d[1], ucode_2_d[2], ucode_2_d[3], ucode_2_d[4], ucode_2_d[5], ucode_2_d[6], ucode_2_d[7], 1'b1, 1'b0, DBUS_ASSERT_0, DBUS_ASSERT_1, DBUS_ASSERT_2, DBUS_ASSERT_3, DBUS_LOAD_0, DBUS_LOAD_1, DBUS_LOAD_2, DBUS_LOAD_3
  EEPROM #(.AddrBits(19), .Bits(8)) ucode_3 (
    .A({mode, IRQ, OPCODE_7, OPCODE_6, OPCODE_5, OPCODE_4, OPCODE_3, OPCODE_2, OPCODE_1, OPCODE_0, F_CARRY, F_ZERO, F_OVER, F_NEG, F_INHIB, t_state}),
    .CS(1'b1), .WE(1'b0), .OE(1'b1), .D(ucode_3_d));
  EEPROM #(.AddrBits(19), .Bits(8)) ucode_4 (
    .A({mode, IRQ, OPCODE_7, OPCODE_6, OPCODE_5, OPCODE_4, OPCODE_3, OPCODE_2, OPCODE_1, OPCODE_0, F_CARRY, F_ZERO, F_OVER, F_NEG, F_INHIB, t_state}),
    .CS(1'b1), .WE(1'b0), .OE(1'b1), .D(ucode_4_d));
  // _74574 _74574_3: pin names not known; wires that end beside it: 1'b0, CLK, ucode_3_d[0], ucode_3_d[1], ucode_3_d[2], ucode_3_d[3], ucode_3_d[4], ucode_3_d[5], ucode_3_d[6], ucode_3_d[7], 1'b1, 1'b0, COUNT_INC_1, COUNT_INC_2, COUNT_DEC_0, COUNT_DEC_1, EXT_FLIP, RST_USEQ, CLR_RST, BRK
  // _74574 _74574_4: pin names not known; wires that end beside it: 1'b0, CLK, ucode_4_d[0], ucode_4_d[1], ucode_4_d[2], ucode_4_d[3], ucode_4_d[4], ucode_4_d[5], ucode_4_d[6], ucode_4_d[7], 1'b1, 1'b0, XFER_ASSERT_3, XFER_ASSERT_4, XFER_LOAD_0, XFER_LOAD_1, ADDR_ASSERT_0, ADDR_ASSERT_1, ADDR_ASSERT_2, COUNT_INC_0

  // Other names for the same wires on the sheet: ucode_addr[18:0] = {mode, IRQ, OPCODE_7, OPCODE_6, OPCODE_5, OPCODE_4, OPCODE_3, OPCODE_2, OPCODE_1, OPCODE_0, F_CARRY, F_ZERO, F_OVER, F_NEG, F_INHIB, t_state};
  //   c_flag = F_CARRY; flags[4:0] = {F_CARRY, F_ZERO, F_OVER, F_NEG, F_INHIB}; i_flag = F_INHIB; mode_0 = mode[0];
  //   mode_1 = mode[1]; n_flag = F_NEG;
  //   opcode[7:0] = {OPCODE_7, OPCODE_6, OPCODE_5, OPCODE_4, OPCODE_3, OPCODE_2, OPCODE_1, OPCODE_0}; v_flag = F_OVER;
  //   z_flag = F_ZERO
endmodule
