// Digital circuit cpu.dig as structural Verilog
module cpu (
);

  wire a_dbus_a, a_dbus_l, addr_a, b_dbus_a, b_dbus_l, c_dbus_a, c_dbus_l, c_lhs_a, c_rhs_a, clk, clr,
       d_dbus_a, d_dbus_l, d_lhs_a, d_rhs_a, dbus_a, dbus_l, ir_dbus_l, mem_dbus_a, mem_dbus_l, xfer_a,
       xfer_l;
  wire [7:0] dbus;

  // bus_controller Bus_Controller: pin names not known; wires that end beside it: dbus_a, dbus_l, xfer_a, xfer_l, addr_a, a_dbus_a, b_dbus_a, c_dbus_a, d_dbus_a, mem_dbus_l, a_dbus_l, b_dbus_l, c_dbus_l, d_dbus_l, mem_dbus_a
  control_unit Control_Unit ();  // open: nirq, opcode, flags, nreq, clk, nrst, dbus_assert, dbus_load, alu_op, xfer_assert, xfer_load, addr_assert, count, dec_sp, nbrk, nclk, rst, dbg
  accumulator Accumulator ();  // open: addr_assert, xfer_load, a_dbus_load, b_dbus_load, a_dbus_assert, b_dbus_assert, a_lhs_assert, b_lhs_assert, a_rhs_assert, b_rhs_assert, dbus, xfer, clk, clr, addr, reg_a, reg_b
  general_purpose_register C_Register (
    .DBUS_IN(dbus), .CLK(clk), .DBUS_LOAD(c_dbus_l), .DBUS_ASSERT(c_dbus_a), .LHS_ASSERT(c_lhs_a),
    .RHS_ASSERT(c_rhs_a), .CLR(clr));  // open: LHS, RHS, DBUS_OUT
  general_purpose_register D_Register (
    .DBUS_IN(dbus), .CLK(clk), .DBUS_LOAD(d_dbus_l), .DBUS_ASSERT(d_dbus_a), .LHS_ASSERT(d_lhs_a),
    .RHS_ASSERT(d_rhs_a), .CLR(clr));  // open: LHS, RHS, DBUS_OUT
  memory_bridge Memory_Bridge (.DBUS_ASSERT(mem_dbus_a), .DBUS_LOAD(mem_dbus_l));  // open: MBUS, DBUS
  instruction_register Instruction_Register (.CLK(clk), .DBUS(dbus), .IR_LOAD(ir_dbus_l));  // open: CLR, CU_OUT
endmodule
