// Digital circuit instruction_register.dig as structural Verilog
module instruction_register (
  input  CLK,
  input  [7:0] DBUS,
  input  IR_LOAD,
  input  CLR,
  output [7:0] CU_OUT
);

  // _74173 _74173_1: pin names not known; wires that end beside it: DBUS[0], 1'b1, 1'b0, CLR, DBUS[1], DBUS[2], DBUS[3], CLK, IR_LOAD, IR_LOAD, 1'b0, 1'b0, CU_OUT[0], CU_OUT[1], CU_OUT[2], CU_OUT[3]
  // _74173 _74173_2: pin names not known; wires that end beside it: DBUS[4], 1'b1, 1'b0, CLR, DBUS[5], DBUS[6], DBUS[7], CLK, IR_LOAD, IR_LOAD, 1'b0, 1'b0, CU_OUT[4], CU_OUT[5], CU_OUT[6], CU_OUT[7]
  // Pins of 1 and 8 bits meet at CU_OUT

  // Other names for the same wires on the sheet: q0 = CU_OUT[0]; q1 = CU_OUT[1]; q2 = CU_OUT[2]; q3 = CU_OUT[3];
  //   q4 = CU_OUT[4]; q5 = CU_OUT[5]; q6 = CU_OUT[6]; q7 = CU_OUT[7]
endmodule
