// Digital circuit memory_bridge.dig as structural Verilog
module memory_bridge (
  input  DBUS_ASSERT,
  input  DBUS_LOAD,
  output [7:0] MBUS,
  output [7:0] DBUS
);

  assign DBUS[0] = DBUS_ASSERT ? MBUS[0] : 1'bz;  // Driver driver_1
  assign MBUS[0] = DBUS_LOAD ? DBUS[0] : 1'bz;  // Driver driver_2
  // Pins of 1 and 8 bits meet at MBUS
  // Pins of 1 and 8 bits meet at DBUS
endmodule
