// Logisim project apple-pie-cpu.circ as structural Verilog: 15 circuits, main circuit 8Bit Computer
// Operand Register
module _8Bit_Computer (
  input  SEL,
  input  HLT,
  input  X_In,
  input  X_Out,
  input  Y_In,
  input  Y_Out,
  input  MAR_In,
  input  TR1L_In,
  input  TR2L_In,
  input  TR1_In,
  input  TR1H_In,
  input  TR2_In,
  input  TR2H_In,
  input  TR1_Out,
  input  TR1H_Out,
  input  TR2_Out,
  input  TR2H_Out,
  input  TR1L_Out,
  input  TR2L_Out,
  input  RI,
  input  RO,
  input  SP_Inc,
  input  SP_Out,
  input  PR_Inc,
  input  PR_JMP,
  input  PC_Inc,
  input  PC_JMP,
  input  SP_Dec,
  input  PR_Out,
  input  PC_Out,
  input  OR_In,
  input  OR_In_2,
  input  IR_In,
  input  in_34,
  input  in_35,
  input  in_36,
  input  A_Out,
  input  A_In,
  input  B_Out,
  input  B_In,
  output [15:0] Addr_Bus,
  output [15:0] out_42,
  output [15:0] out_43,
  output [15:0] out_44,
  output [15:0] out_45,
  output [15:0] out_46,
  output [7:0] out_47,
  output [7:0] out_48,
  output [7:0] out_49,
  output Cout,
  output Cout_2,
  output Cout_3,
  output [7:0] out_53,
  output [15:0] out_54,
  output [7:0] out_55,
  output [7:0] out_56,
  output [5:0] out_57,
  output [7:0] out_58,
  output [7:0] out_59,
  output [7:0] out_60
);

  wire A_In_t, A_Out_t, Addr_Decoder_ram_enable, Addr_Decoder_rom_enable, ALU_AND, ALU_NOT, ALU_OR, ALU_Out,
       ALU_Sub, B_In_t, B_Out_t, C_In, C_Out, Clock_clock, CLR, CLR_out, D_In, D_Out, HLT_t, IR_In_t,
       MAN_out, MAR_In_t, Mem_Out, OR_In_t, OR_Out, Output_In, PC_Inc_t, PC_JMP_t, PC_Out_t, PR_Inc_t,
       PR_JMP_t, PR_Out_t, pull_resistor_2_node, pull_resistor_4_node, pull_resistor_5_node, RAM_In,
       SP_Dec_t, SP_Inc_t, SP_Out_t, TR1_In_t, TR1_Out_t, TR1H_In_t, TR1H_Out_t, TR1L_In_t, TR1L_Out_t,
       TR2_In_t, TR2_Out_t, TR2H_In_t, TR2H_Out_t, TR2L_In_t, TR2L_Out_t, X_In_t, X_Out_t, Y_In_t, Y_Out_t;
  wire [7:0] controlled_buffer_1_out, pull_resistor_3_node, ram_1_data, rom_1_data;
  wire [14:0] Addr_Decoder_addr_out;
  wire [15:0] pull_resistor_1_node;
  wire [23:0] output_decimal_register_1_hundreds;

  Button MAN (.out(MAN_out));
  Button u_CLR (.out(CLR_out));
  clock Clock (.Select(SEL), .Manual(MAN_out), .Halt(HLT), .Clock(Clock_clock));
  address_decoder Addr_Decoder (
    .From_MAR(out_44), .Addr_Out(Addr_Decoder_addr_out), .ROM_Enable(Addr_Decoder_rom_enable),
    .RAM_Enable(Addr_Decoder_ram_enable));
  _16bit_register Operand_Register (
    .From_Bus(Addr_Bus), .Register_In(OR_In), .Clock(Clock_clock), .Clear(CLR_out), .To_Bus(Addr_Bus),
    .Monitor(out_54), .Register_Out(OR_In_2));
  sequencer Sequencer (.CLK(Clock_clock), .CLR(CLR_out), .Decoded_Out(out_57));
  _16bit_register Memory_Addr_Register (
    .From_Bus(pull_resistor_1_node), .Register_In(MAR_In), .Clock(Clock_clock), .Clear(CLR_out),
    .To_Bus(Addr_Bus), .Monitor(out_44), .Register_Out(pull_resistor_5_node));
  Pull_Resistor pull_resistor_1 (.node(pull_resistor_1_node));
  ROM #(.addrWidth(15)) rom_1 (.addr(Addr_Decoder_addr_out), .data(rom_1_data), .sel(Addr_Decoder_rom_enable));
  RAM #(.addrWidth(15), .bus("separate")) ram_1 (
    .addr(Addr_Decoder_addr_out), .din(controlled_buffer_1_out), .data(ram_1_data), .str(RI),
    .sel(Addr_Decoder_ram_enable), .clk(Clock_clock), .ld(pull_resistor_2_node), .clr(CLR_out));
  Pull_Resistor #(.pull(1)) pull_resistor_2 (.node(pull_resistor_2_node));
  Pull_Resistor pull_resistor_3 (.node(pull_resistor_3_node));
  Pull_Resistor pull_resistor_4 (.node(pull_resistor_4_node));
  instruction_decoder Instruction_Decoder (
    .Op_Code(in_35), .Micro_Step(in_34), .Flags(in_36),
    .CTRL_0_23({TR1_Out_t, PC_JMP_t, PC_Out_t, PC_Inc_t, PR_JMP_t, PR_Out_t, PR_Inc_t, SP_Out_t, SP_Dec_t, SP_Inc_t, ALU_OR, ALU_NOT, ALU_Sub, ALU_AND, ALU_Out, B_In_t, B_Out_t, A_In_t, A_Out_t, D_In, D_Out, C_In, C_Out, Output_In}),
    .CTRL_24_46({IR_In_t, OR_Out, OR_In_t, Mem_Out, RAM_In, MAR_In_t, HLT_t, CLR, Y_Out_t, Y_In_t, X_Out_t, X_In_t, TR2H_In_t, TR2L_In_t, TR2_In_t, TR2H_Out_t, TR2L_Out_t, TR2_Out_t, TR1H_In_t, TR1L_In_t, TR1_In_t, TR1H_Out_t, TR1L_Out_t}));
  Pull_Resistor pull_resistor_5 (.node(pull_resistor_5_node));
  assign controlled_buffer_1_out = RO ? rom_1_data : 8'bz;  // Controlled_Buffer controlled_buffer_1
  assign controlled_buffer_1_out = RO ? ram_1_data : 8'bz;  // Controlled_Buffer controlled_buffer_2
  _8bit_register Instruction_Register (
    .Register_Out(pull_resistor_4_node), .From_Bus(controlled_buffer_1_out), .Register_In(IR_In),
    .Clock(Clock_clock), .Clear(CLR_out), .To_Bus(pull_resistor_3_node), .Monitor(out_53));
  // Probe on controlled_buffer_1_out
  Pull_Resistor pull_resistor_6 (.node(controlled_buffer_1_out));
  _16bit_register X_Register (
    .From_Bus(Addr_Bus), .Register_In(X_In), .Clock(Clock_clock), .Clear(CLR_out), .To_Bus(Addr_Bus),
    .Monitor(out_42), .Register_Out(X_Out));
  transfer_register Transfer_Register_1 (
    .Data_Bus(controlled_buffer_1_out), .Addr_Bus(Addr_Bus), .Register_In(TR1_In), .Register_Low_In(TR1L_In),
    .Register_High_In(TR1H_In), .Register_Out(TR1_Out), .Register_Low_Out(TR1L_Out),
    .Register_High_Out(TR1H_Out), .Clock(Clock_clock), .Clear(CLR_out), .To_Addr_Bus(Addr_Bus),
    .To_Data_Bus(controlled_buffer_1_out), .Monitor(out_45));
  _8bit_register A_Register (
    .Register_Out(A_Out), .From_Bus(controlled_buffer_1_out), .Register_In(A_In), .Clock(Clock_clock),
    .Clear(CLR_out), .To_Bus(controlled_buffer_1_out), .Monitor(out_55));
  _8bit_register C_Register (
    .Register_Out(C_Out), .From_Bus(controlled_buffer_1_out), .Register_In(C_In), .Clock(Clock_clock),
    .Clear(CLR_out), .To_Bus(controlled_buffer_1_out), .Monitor(out_58));
  output_decimal_register output_decimal_register_1 (
    .From_Bus(controlled_buffer_1_out), .Output_In(Output_In), .CLK(Clock_clock), .CLR(CLR_out),
    .Monitor(out_60), .Hundreds(output_decimal_register_1_hundreds));
  stack_pointer Stack_Pointer (
    .Monitor(out_47), .To_Bus(controlled_buffer_1_out), .INC(SP_Inc), .CLK(Clock_clock), .CLR(CLR_out),
    .Cout(Cout), .Counter_Out(SP_Out), .DEC(SP_Dec));
  alu_1 ALU ();  // open: ALU_Output, Input_A, SUB, NOT, AND, OR, To_Bus, Monitor, From_Bus, Register_In, Input_B, Clock, Clear
  _7_Segment_Display u_7_segment_display_1 (
    .g(output_decimal_register_1_hundreds[11]), .f(output_decimal_register_1_hundreds[10]),
    .a(output_decimal_register_1_hundreds[9]), .b(output_decimal_register_1_hundreds[8]),
    .e(output_decimal_register_1_hundreds[23]), .d(output_decimal_register_1_hundreds[22]),
    .c(output_decimal_register_1_hundreds[21]), .dp(output_decimal_register_1_hundreds[20]));
  _7_Segment_Display u_7_segment_display_2 (
    .g(output_decimal_register_1_hundreds[7]), .f(output_decimal_register_1_hundreds[6]),
    .a(output_decimal_register_1_hundreds[5]), .b(output_decimal_register_1_hundreds[4]),
    .e(output_decimal_register_1_hundreds[19]), .d(output_decimal_register_1_hundreds[18]),
    .c(output_decimal_register_1_hundreds[17]), .dp(output_decimal_register_1_hundreds[16]));
  _8bit_counter Page_Register (
    .From_Bus(controlled_buffer_1_out), .Monitor(out_48), .To_Bus(controlled_buffer_1_out), .JMP(PR_JMP),
    .INC(PR_Inc), .CLK(Clock_clock), .CLR(CLR_out), .Cout(Cout_2), .Counter_Out(PR_Out));
  _8bit_register B_Register (
    .Register_Out(B_Out), .From_Bus(controlled_buffer_1_out), .Register_In(B_In), .Clock(Clock_clock),
    .Clear(CLR_out), .To_Bus(controlled_buffer_1_out), .Monitor(out_56));
  _8bit_register D_Register (
    .Register_Out(D_Out), .From_Bus(controlled_buffer_1_out), .Register_In(D_In), .Clock(Clock_clock),
    .Clear(CLR_out), .To_Bus(controlled_buffer_1_out), .Monitor(out_59));
  _7_Segment_Display u_7_segment_display_3 (
    .g(output_decimal_register_1_hundreds[3]), .f(output_decimal_register_1_hundreds[2]),
    .a(output_decimal_register_1_hundreds[1]), .b(output_decimal_register_1_hundreds[0]),
    .e(output_decimal_register_1_hundreds[15]), .d(output_decimal_register_1_hundreds[14]),
    .c(output_decimal_register_1_hundreds[13]), .dp(output_decimal_register_1_hundreds[12]));
  _16bit_register Y_Register (
    .From_Bus(Addr_Bus), .Register_In(Y_In), .Clock(Clock_clock), .Clear(CLR_out), .To_Bus(Addr_Bus),
    .Monitor(out_43), .Register_Out(Y_Out));
  transfer_register Transfer_Register_2 (
    .Data_Bus(controlled_buffer_1_out), .Addr_Bus(Addr_Bus), .Register_In(TR2_In), .Register_Low_In(TR2L_In),
    .Register_High_In(TR2H_In), .Register_Out(TR2_Out), .Register_Low_Out(TR2L_Out),
    .Register_High_Out(TR2H_Out), .Clock(Clock_clock), .Clear(CLR_out), .To_Addr_Bus(Addr_Bus),
    .To_Data_Bus(controlled_buffer_1_out), .Monitor(out_46));
  _8bit_counter Program_Counter (
    .From_Bus(controlled_buffer_1_out), .Monitor(out_49), .To_Bus(controlled_buffer_1_out), .JMP(PC_JMP),
    .INC(PC_Inc), .CLK(Clock_clock), .CLR(CLR_out), .Cout(Cout_3), .Counter_Out(PC_Out));
  Pull_Resistor pull_resistor_7 (.node(Addr_Bus));
endmodule

module clock (
  input  Select,
  input  Manual,
  input  Halt,
  output Clock
);

  wire and_1_out, and_2_out, clock_1_out, not_1_out, not_2_out, or_1_out;

  Clock clock_1 (.out(clock_1_out));
  and and_1 (and_1_out, clock_1_out, Select);
  not not_1 (not_1_out, Select);
  and and_2 (and_2_out, not_1_out, Manual);
  not not_2 (not_2_out, Halt);
  or or_1 (or_1_out, and_1_out, and_2_out);
  and and_3 (Clock, or_1_out, not_2_out);
endmodule

module _8bit_register (
  input  Register_Out,
  input  [7:0] From_Bus,
  input  Register_In,
  input  Clock,
  input  Clear,
  output [7:0] To_Bus,
  output [7:0] Monitor
);

  Pull_Resistor pull_resistor_1 (.node(Register_In));
  Pull_Resistor pull_resistor_2 (.node(Clock));
  Pull_Resistor pull_resistor_3 (.node(Clear));
  Register register_1 (.D(From_Bus), .en(Register_In), .Q(Monitor), .clk(Clock), .clr(Clear));
  Pull_Resistor pull_resistor_4 (.node(Register_Out));
  assign To_Bus = Register_Out ? Monitor : 8'bz;  // Controlled_Buffer controlled_buffer_1
endmodule

module _16bit_register (
  input  Register_Out,
  input  [15:0] From_Bus,
  input  Register_In,
  input  Clock,
  input  Clear,
  output [15:0] To_Bus,
  output [15:0] Monitor
);

  Pull_Resistor pull_resistor_1 (.node(Register_In));
  Pull_Resistor pull_resistor_2 (.node(Clock));
  Pull_Resistor pull_resistor_3 (.node(Clear));
  Register #(.width(16)) register_1 (.D(From_Bus), .en(Register_In), .Q(Monitor), .clk(Clock), .clr(Clear));
  Pull_Resistor pull_resistor_4 (.node(Register_Out));
  assign To_Bus = Register_Out ? Monitor : 16'bz;  // Controlled_Buffer controlled_buffer_1
endmodule

module alu_0 (
  input  ALU_Output,
  input  [7:0] A_Input,
  input  SUB,
  input  NOT,
  input  AND,
  input  OR,
  input  [7:0] B_Input,
  output [7:0] Monitor,
  output [7:0] To_Bus
);

  wire or_1_out, or_2_out, xor_1_out;
  wire [7:0] adder_1_out, and_1_out, bit_extender_1_out, multiplexer_1_out, or_3_out, xor_2_out;

  or or_1 (or_1_out, SUB, NOT);
  or or_2 (or_2_out, AND, OR);
  assign bit_extender_1_out = {{7{or_1_out}}, or_1_out};  // Bit_Extender bit_extender_1
  xor xor_1 (xor_1_out, or_1_out, NOT);
  assign xor_2_out = bit_extender_1_out ^ B_Input;  // XOR_Gate xor_2, 8 bits wide
  Adder adder_1 (.a(A_Input), .b(xor_2_out), .out(adder_1_out), .cin(xor_1_out));  // open: cout
  assign and_1_out = A_Input & B_Input;  // AND_Gate and_1, 8 bits wide
  Multiplexer #(.width(8), .enable("false")) multiplexer_1 (
    .in0(and_1_out), .in1(or_3_out), .out(multiplexer_1_out), .sel(OR));
  assign or_3_out = A_Input | B_Input;  // OR_Gate or_3, 8 bits wide
  Multiplexer #(.width(8), .enable("false")) multiplexer_2 (
    .in0(adder_1_out), .in1(multiplexer_1_out), .out(Monitor), .sel(or_2_out));
  assign To_Bus = ALU_Output ? Monitor : 8'bz;  // Controlled_Buffer controlled_buffer_1
endmodule

module instruction_decoder (
  input  Op_Code,
  input  Micro_Step,
  input  Flags,
  output [23:0] CTRL_0_23,
  output [22:0] CTRL_24_46
);

  wire pull_resistor_1_node, pull_resistor_2_node;

  Pull_Resistor #(.pull(1)) pull_resistor_1 (.node(pull_resistor_1_node));
  Pull_Resistor #(.pull(1)) pull_resistor_2 (.node(pull_resistor_2_node));
  ROM #(.dataWidth(24)) rom_1 (.addr({8{1'b1}}), .data(CTRL_0_23), .sel(pull_resistor_1_node));
  ROM #(.dataWidth(23)) rom_2 (.addr({8{1'b1}}), .data(CTRL_24_46), .sel(pull_resistor_2_node));
endmodule

module stack_pointer (
  input  DEC,
  input  INC,
  input  CLK,
  input  CLR,
  input  Counter_Out,
  output [7:0] Monitor,
  output [7:0] To_Bus,
  output Cout
);

  wire xor_1_out;
  wire [7:0] pull_resistor_3_node;

  Pull_Resistor pull_resistor_1 (.node(DEC));
  xor xor_1 (xor_1_out, DEC, INC);
  Pull_Resistor pull_resistor_2 (.node(INC));
  Pull_Resistor pull_resistor_3 (.node(pull_resistor_3_node));
  Counter counter_1 (
    .load(DEC), .D(pull_resistor_3_node), .count(xor_1_out), .Q(Monitor), .carry(Cout), .clk(CLK), .clr(CLR));
  Pull_Resistor pull_resistor_4 (.node(Cout));
  Pull_Resistor pull_resistor_5 (.node(CLK));
  Pull_Resistor pull_resistor_6 (.node(CLR));
  assign To_Bus = Counter_Out ? Monitor : 8'bz;  // Controlled_Buffer controlled_buffer_1
  Pull_Resistor pull_resistor_7 (.node(Counter_Out));
endmodule

module _8bit_counter (
  input  [7:0] From_Bus,
  input  JMP,
  input  INC,
  input  CLK,
  input  CLR,
  input  Counter_Out,
  output [7:0] Monitor,
  output [7:0] To_Bus,
  output Cout
);

  wire [7:0] controlled_buffer_1_out;

  Pull_Resistor pull_resistor_1 (.node(JMP));
  Pull_Resistor pull_resistor_2 (.node(INC));
  Pull_Resistor pull_resistor_3 (.node(CLK));
  assign controlled_buffer_1_out = JMP ? From_Bus : 8'bz;  // Controlled_Buffer controlled_buffer_1
  Counter counter_1 (
    .load(JMP), .D(controlled_buffer_1_out), .count(INC), .Q(Monitor), .carry(Cout), .clk(CLK), .clr(CLR));
  Pull_Resistor pull_resistor_4 (.node(Cout));
  Pull_Resistor pull_resistor_5 (.node(CLR));
  assign To_Bus = Counter_Out ? Monitor : 8'bz;  // Controlled_Buffer controlled_buffer_2
  Pull_Resistor pull_resistor_6 (.node(Counter_Out));
endmodule

module output_decimal_register (
  input  [7:0] From_Bus,
  input  Output_In,
  input  CLK,
  input  CLR,
  output [7:0] Monitor,
  output [23:0] Hundreds
);

  wire pull_resistor_4_node;

  Register register_1 (.D(From_Bus), .en(Output_In), .Q(Monitor), .clk(CLK), .clr(CLR));
  Pull_Resistor pull_resistor_1 (.node(Output_In));
  Pull_Resistor pull_resistor_2 (.node(CLK));
  Pull_Resistor pull_resistor_3 (.node(CLR));
  Pull_Resistor #(.pull(1)) pull_resistor_4 (.node(pull_resistor_4_node));
  ROM #(.dataWidth(24)) rom_1 (.addr(Monitor), .data(Hundreds), .sel(pull_resistor_4_node));

  // Notes on the sheet:
  //   contents of rom_1 (hex, n*v repeats v):
  //   e007 2001 c00b 600b 200d 600e e00e 2003 e00f 200f 2e017 22011 2c01b 2601b 2201d 2601e 2e01e 22013
  //   2e01f 2201f ce0b7 c20b1 cc0bb c60bb c20bd c60be ce0be c20b3 ce0bf c20bf 6e0b7 620b1 6c0bb 660bb
  //   620bd 660be 6e0be 620b3 6e0bf 620bf 2e0d7 220d1 2c0db 260db 220dd 260de 2e0de 220d3 2e0df 220df
  //   6e0e7 620e1 6c0eb 660eb 620ed 660ee 6e0ee 620e3 6e0ef 620ef ee0e7 e20e1 ec0eb e60eb e20ed e60ee
  //   ee0ee e20e3 ee0ef e20ef 2e037 22031 2c03b 2603b 2203d 2603e 2e03e 22033 2e03f 2203f ee0f7 e20f1
  //   ec0fb e60fb e20fd e60fe ee0fe e20f3 ee0ff e20ff 2e0f7 220f1 2c0fb 260fb 220fd 260fe 2e0fe 220f3
  //   2e0ff 220ff 2ee177 2e2171 2ec17b 2e617b 2e217d 2e617e 2ee17e 2e2173 2ee17f 2e217f 22e117 222111
  //   22c11b 22611b 22211d 22611e 22e11e 222113 22e11f 22211f 2ce1b7 2c21b1 2cc1bb 2c61bb 2c21bd 2c61be
  //   2ce1be 2c21b3 2ce1bf 2c21bf 26e1b7 2621b1 26c1bb 2661bb 2621bd 2661be 26e1be 2621b3 26e1bf 2621bf
  //   22e1d7 2221d1 22c1db 2261db 2221dd 2261de 22e1de 2221d3 22e1df 2221df 26e1e7 2621e1 26c1eb 2661eb
  //   2621ed 2661ee 26e1ee 2621e3 26e1ef 2621ef 2ee1e7 2e21e1 2ec1eb 2e61eb 2e21ed 2e61ee 2ee1ee 2e21e3
  //   2ee1ef 2e21ef 22e137 222131 22c13b 22613b 22213d 22613e 22e13e 222133 22e13f 22213f 2ee1f7 2e21f1
  //   2ec1fb 2e61fb 2e21fd 2e61fe 2ee1fe 2e21f3 2ee1ff 2e21ff 22e1f7 2221f1 22c1fb 2261fb 2221fd 2261fe
  //   22e1fe 2221f3 22e1ff 2221ff ceeb77 ce2b71 cecb7b ce6b7b ce2b7d ce6b7e ceeb7e ce2b73 ceeb7f ce2b7f
  //   c2eb17 c22b11 c2cb1b c26b1b c22b1d c26b1e c2eb1e c22b13 c2eb1f c22b1f ccebb7 cc2bb1 cccbbb cc6bbb
  //   cc2bbd cc6bbe ccebbe cc2bb3 ccebbf cc2bbf c6ebb7 c62bb1 c6cbbb c66bbb c62bbd c66bbe c6ebbe c62bb3
  //   c6ebbf c62bbf c2ebd7 c22bd1 c2cbdb c26bdb c22bdd c26bde c2ebde c22bd3 c2ebdf c22bdf c6ebe7 c62be1
  //   c6cbeb c66beb c62bed c66bee
endmodule

module alu_1 (
  input  ALU_Output,
  input  [7:0] Input_A,
  input  SUB,
  input  NOT,
  input  AND,
  input  OR,
  input  [7:0] From_Bus,
  input  Register_In,
  input  Clock,
  input  Clear,
  output [7:0] Monitor,
  output [7:0] To_Bus,
  output [7:0] Input_B
);

  wire or_1_out, or_2_out, xor_1_out;
  wire [7:0] adder_1_out, and_1_out, bit_extender_1_out, multiplexer_1_out, multiplexer_2_out, or_3_out,
       xor_2_out;

  Pull_Resistor pull_resistor_1 (.node(SUB));
  Pull_Resistor pull_resistor_2 (.node(NOT));
  Pull_Resistor pull_resistor_3 (.node(AND));
  Pull_Resistor pull_resistor_4 (.node(OR));
  Pull_Resistor pull_resistor_5 (.node(Register_In));
  Pull_Resistor pull_resistor_6 (.node(Clock));
  Pull_Resistor pull_resistor_7 (.node(Clear));
  Register register_1 (.D(From_Bus), .en(Register_In), .Q(Input_B), .clk(Clock), .clr(Clear));
  or or_1 (or_1_out, AND, OR);
  or or_2 (or_2_out, SUB, NOT);
  assign bit_extender_1_out = {{7{or_2_out}}, or_2_out};  // Bit_Extender bit_extender_1
  xor xor_1 (xor_1_out, or_2_out, NOT);
  assign xor_2_out = bit_extender_1_out ^ Input_B;  // XOR_Gate xor_2, 8 bits wide
  Multiplexer #(.width(8), .enable("false")) multiplexer_1 (
    .in0(Input_A), .in1({8{1'b0}}), .out(multiplexer_1_out), .sel(NOT));
  assign and_1_out = Input_A & Input_B;  // AND_Gate and_1, 8 bits wide
  assign or_3_out = Input_A | Input_B;  // OR_Gate or_3, 8 bits wide
  Adder adder_1 (.a(multiplexer_1_out), .b(xor_2_out), .out(adder_1_out), .cin(xor_1_out));  // open: cout
  Multiplexer #(.width(8), .enable("false")) multiplexer_2 (
    .in0(and_1_out), .in1(or_3_out), .out(multiplexer_2_out), .sel(OR));
  Multiplexer #(.width(8), .enable("false")) multiplexer_3 (
    .in0(adder_1_out), .in1(multiplexer_2_out), .out(Monitor), .sel(or_1_out));
  assign To_Bus = ALU_Output ? Monitor : 8'bz;  // Controlled_Buffer controlled_buffer_1
endmodule

module alu_2 (
  input  NOT,
  input  SUB,
  input  [7:0] INPUT_A,
  input  [7:0] From_Bus,
  input  Register_In,
  input  AND,
  input  Clock,
  input  OR,
  input  Clear,
  input  LSL,
  input  LSR,
  input  ALU_Output,
  input  Update_Flags,
  output [7:0] To_Bus,
  output [7:0] Output,
  output [7:0] INPUT_B
);

  wire nor_1_out, not_1_out, or_2_out;
  wire [2:0] bit_extender_2_out;
  wire [3:0] nor_2_out;
  wire [7:0] adder_1_out, and_1_out, bit_extender_1_out, multiplexer_1_out, multiplexer_2_out,
       multiplexer_3_out, multiplexer_4_out, not_2_out, or_1_out, shifter_1_out, shifter_2_out, xor_1_out;

  Register register_1 (.D(From_Bus), .en(Register_In), .Q(INPUT_B), .clk(Clock), .clr(Clear));
  assign bit_extender_1_out = {{7{SUB}}, SUB};  // Bit_Extender bit_extender_1
  Bit_Extender #(.out_width(3)) bit_extender_2 (.in(INPUT_B), .out(bit_extender_2_out));
  not not_1 (not_1_out, NOT);
  assign not_2_out = ~INPUT_A;  // NOT_Gate not_2, 8 bits wide
  Shifter shifter_1 (.in(INPUT_A), .\dist (bit_extender_2_out), .out(shifter_1_out));
  Shifter #(.shift("lr")) shifter_2 (.in(INPUT_A), .\dist (bit_extender_2_out), .out(shifter_2_out));
  assign xor_1_out = bit_extender_1_out ^ INPUT_B;  // XOR_Gate xor_1, 8 bits wide
  assign and_1_out = INPUT_A & INPUT_B;  // AND_Gate and_1, 8 bits wide
  assign or_1_out = INPUT_A | INPUT_B;  // OR_Gate or_1, 8 bits wide
  or or_2 (or_2_out, AND, OR);
  nor nor_1 (nor_1_out, LSL, LSR);
  Multiplexer #(.width(8), .enable("false")) multiplexer_1 (
    .in0(shifter_1_out), .in1(shifter_2_out), .out(multiplexer_1_out), .sel(LSR));
  Adder adder_1 (.a(INPUT_A), .b(xor_1_out), .out(adder_1_out), .cin(SUB), .cout(nor_2_out[2]));
  Multiplexer #(.width(8), .enable("false")) multiplexer_2 (
    .in0(not_2_out), .in1(adder_1_out), .out(multiplexer_2_out), .sel(not_1_out));
  Multiplexer #(.width(8), .enable("false")) multiplexer_3 (
    .in0(and_1_out), .in1(or_1_out), .out(multiplexer_3_out), .sel(OR));
  Multiplexer #(.width(8), .enable("false")) multiplexer_4 (
    .in0(multiplexer_2_out), .in1(multiplexer_3_out), .out(multiplexer_4_out), .sel(or_2_out));
  Multiplexer #(.width(8), .enable("false")) multiplexer_5 (
    .in0(multiplexer_1_out), .in1(multiplexer_4_out), .out(Output), .sel(nor_1_out));
  assign To_Bus = ALU_Output ? Output : 8'bz;  // Controlled_Buffer controlled_buffer_1
  nor nor_2 (nor_2_out[0], Output[0], Output[1], Output[2], Output[3], Output[4], Output[5], Output[6], Output[7]);
  Register #(.width(4)) register_2 (.D(nor_2_out), .en(Update_Flags), .clk(Clock), .clr(Clear));  // open: Q
endmodule

module transfer_register (
  input  [7:0] Data_Bus,
  input  [15:0] Addr_Bus,
  input  Register_In,
  input  Register_Low_In,
  input  Register_High_In,
  input  Register_Out,
  input  Register_Low_Out,
  input  Register_High_Out,
  input  Clock,
  input  Clear,
  output [15:0] Monitor,
  output [15:0] To_Addr_Bus,
  output [7:0] To_Data_Bus
);

  wire xor_1_out, xor_2_out, xor_3_out;
  wire [7:0] multiplexer_1_out, multiplexer_2_out, multiplexer_3_out;

  Multiplexer #(.width(8), .enable("false")) multiplexer_1 (
    .in0(Addr_Bus[15:8]), .in1(Data_Bus), .out(multiplexer_1_out), .sel(Register_High_In));
  xor xor_1 (xor_1_out, Register_In, Register_High_In);
  xor xor_2 (xor_2_out, Register_Low_Out, Register_High_Out);
  Multiplexer #(.width(8), .enable("false")) multiplexer_2 (
    .in0(Addr_Bus[7:0]), .in1(Data_Bus), .out(multiplexer_2_out), .sel(Register_Low_In));
  Register High (.D(multiplexer_1_out), .en(xor_1_out), .Q(Monitor[15:8]), .clk(Clock), .clr(Clear));
  Register Low (.D(multiplexer_2_out), .en(xor_3_out), .Q(Monitor[7:0]), .clk(Clock), .clr(Clear));
  xor xor_3 (xor_3_out, Register_In, Register_Low_In);
  assign To_Data_Bus = xor_2_out ? multiplexer_3_out : 8'bz;  // Controlled_Buffer controlled_buffer_1
  Multiplexer #(.width(8)) multiplexer_3 (
    .in0(Monitor[15:8]), .in1(Monitor[7:0]), .out(multiplexer_3_out), .sel(Register_Low_Out), .en(xor_2_out));
  assign To_Addr_Bus = Register_Out ? Monitor : 16'bz;  // Controlled_Buffer controlled_buffer_2
endmodule

module address_decoder (
  input  [15:0] From_MAR,
  output [14:0] Addr_Out,
  output ROM_Enable,
  output RAM_Enable
);

  not not_1 (RAM_Enable, From_MAR[15]);

  assign Addr_Out = From_MAR[14:0];
  assign ROM_Enable = From_MAR[15];
endmodule

module sequencer (
  input  CLK,
  input  CLR,
  output [5:0] Decoded_Out
);

  wire decoder_1_out6, not_1_out, or_1_out, pull_resistor_2_node, pull_resistor_3_node;
  wire [2:0] counter_1_q, pull_resistor_1_node;
  wire [5:0] decoder_1_out0;

  not not_1 (not_1_out, CLK);
  Pull_Resistor pull_resistor_1 (.node(pull_resistor_1_node));
  Pull_Resistor pull_resistor_2 (.node(pull_resistor_2_node));
  Pull_Resistor #(.pull(1)) pull_resistor_3 (.node(pull_resistor_3_node));
  Decoder #(.select(3), .enable("false")) decoder_1 (
    .out0(decoder_1_out0[0]), .out1(decoder_1_out0[1]), .out2(decoder_1_out0[2]), .out3(decoder_1_out0[3]),
    .out4(decoder_1_out0[4]), .out5(decoder_1_out0[5]), .out6(decoder_1_out6), .sel(counter_1_q));  // open: out7
  Counter #(.width(3), .max('h7)) counter_1 (
    .load(pull_resistor_2_node), .D(pull_resistor_1_node), .count(pull_resistor_3_node), .Q(counter_1_q),
    .clk(not_1_out), .clr(or_1_out));  // open: carry
  or or_1 (or_1_out, CLR, decoder_1_out6);
  assign Decoded_Out = ~decoder_1_out0;  // NOT_Gate not_2, 6 bits wide
endmodule

module alu_3 (
  input  NOT,
  input  SUB,
  input  [7:0] INPUT_A,
  input  [7:0] INPUT_B,
  input  AND,
  input  OR,
  input  LSL,
  input  LSR,
  input  ALU_Output,
  input  Clock,
  input  Clear,
  input  Update_Flags,
  output [7:0] To_Bus,
  output [3:0] Flags,
  output [7:0] Output
);

  wire nor_1_out, not_1_out, or_1_out;
  wire [2:0] bit_extender_1_out;
  wire [3:0] nor_2_out;
  wire [7:0] adder_1_out, and_1_out, bit_extender_2_out, multiplexer_1_out, multiplexer_2_out,
       multiplexer_3_out, multiplexer_4_out, not_2_out, or_2_out, shifter_1_out, shifter_2_out, xor_1_out;

  Bit_Extender #(.out_width(3)) bit_extender_1 (.in(INPUT_B), .out(bit_extender_1_out));
  assign bit_extender_2_out = {{7{SUB}}, SUB};  // Bit_Extender bit_extender_2
  or or_1 (or_1_out, AND, OR);
  nor nor_1 (nor_1_out, LSL, LSR);
  not not_1 (not_1_out, NOT);
  assign not_2_out = ~INPUT_A;  // NOT_Gate not_2, 8 bits wide
  Shifter shifter_1 (.in(INPUT_A), .\dist (bit_extender_1_out), .out(shifter_1_out));
  Shifter #(.shift("lr")) shifter_2 (.in(INPUT_A), .\dist (bit_extender_1_out), .out(shifter_2_out));
  assign xor_1_out = bit_extender_2_out ^ INPUT_B;  // XOR_Gate xor_1, 8 bits wide
  assign and_1_out = INPUT_A & INPUT_B;  // AND_Gate and_1, 8 bits wide
  assign or_2_out = INPUT_A | INPUT_B;  // OR_Gate or_2, 8 bits wide
  Multiplexer #(.width(8), .enable("false")) multiplexer_1 (
    .in0(shifter_1_out), .in1(shifter_2_out), .out(multiplexer_1_out), .sel(LSR));
  Adder adder_1 (.a(INPUT_A), .b(xor_1_out), .out(adder_1_out), .cin(SUB), .cout(nor_2_out[2]));
  Multiplexer #(.width(8), .enable("false")) multiplexer_2 (
    .in0(not_2_out), .in1(adder_1_out), .out(multiplexer_2_out), .sel(not_1_out));
  Multiplexer #(.width(8), .enable("false")) multiplexer_3 (
    .in0(and_1_out), .in1(or_2_out), .out(multiplexer_3_out), .sel(OR));
  Multiplexer #(.width(8), .enable("false")) multiplexer_4 (
    .in0(multiplexer_2_out), .in1(multiplexer_3_out), .out(multiplexer_4_out), .sel(or_1_out));
  xor xor_2 (nor_2_out[3], SUB, nor_2_out[2]);
  Multiplexer #(.width(8), .enable("false")) multiplexer_5 (
    .in0(multiplexer_1_out), .in1(multiplexer_4_out), .out(Output), .sel(nor_1_out));
  assign To_Bus = ALU_Output ? Output : 8'bz;  // Controlled_Buffer controlled_buffer_1
  nor nor_2 (nor_2_out[0], Output[0], Output[1], Output[2], Output[3], Output[4], Output[5], Output[6], Output[7]);
  Register #(.width(4)) register_1 (
    .D({nor_2_out[3:2], Output[7], nor_2_out[0]}), .en(Update_Flags), .Q(Flags), .clk(Clock), .clr(Clear));

  // Notes on the sheet:
  //   V C N Z
endmodule
