// Logisim project graphics_card.circ as structural Verilog: 1 circuit, main circuit main
module main (
  output H_Visible,
  output HSYNC,
  output V_Visible,
  output out_4,
  output VSYNC
);

  wire and_1_out, and_2_out, and_3_out, and_4_out, and_5_out, and_6_out, and_8_out, bitselector_1_out,
       Clear_out, Clock_out, counter_1_carry, Frame_Buff_Address_carry, HCOUNT_carry, nand_1_out, nand_2_out,
       nand_3_out, nand_4_out, nand_5_out, nand_6_out, nand_7_out, nand_8_out, nand_10_out, nand_11_out,
       nand_14_out, nand_15_out, nand_17_out, not_1_out, not_2_out, not_5_out, or_1_out, or_2_out, or_3_out,
       pull_resistor_1_node, pull_resistor_3_node, pull_resistor_5_node, pull_resistor_7_node,
       pull_resistor_9_node, pull_resistor_11_node, pull_resistor_12_node, pull_resistor_14_node,
       pull_resistor_17_node, pull_resistor_19_node, pull_resistor_21_node, pull_resistor_22_node,
       pull_resistor_23_node, pull_resistor_25_node, pull_resistor_27_node, VCOUNT_carry, X_Offset_carry,
       Y_Offset_carry;
  wire [2:0] counter_1_q, pull_resistor_10_node, pull_resistor_13_node, pull_resistor_24_node, X_Offset_q,
       Y_Offset_q;
  wire [7:0] ram_1_data, rom_1_data, rom_2_data;
  wire [9:0] HCOUNT_q, not_3_out, not_4_out, pull_resistor_2_node, pull_resistor_6_node, VCOUNT_q;
  wire [12:0] Frame_Buff_Address_q, pull_resistor_18_node;

  Button Clear (.out(Clear_out));
  Clock Clock (.out(Clock_out));
  not not_1 (not_1_out, nand_4_out);
  Pull_Resistor pull_resistor_1 (.node(pull_resistor_1_node));
  Pull_Resistor pull_resistor_2 (.node(pull_resistor_2_node));
  Pull_Resistor #(.pull(1)) pull_resistor_3 (.node(pull_resistor_3_node));
  or or_1 (or_1_out, Clear_out, not_1_out);
  or or_2 (or_2_out, Clear_out, not_2_out);
  not not_2 (not_2_out, nand_8_out);
  Counter #(.width(10), .max('h3ff)) HCOUNT (
    .load(pull_resistor_1_node), .D(pull_resistor_2_node), .count(pull_resistor_3_node), .Q(HCOUNT_q),
    .carry(HCOUNT_carry), .clk(Clock_out), .clr(or_1_out));
  Pull_Resistor pull_resistor_4 (.node(HCOUNT_carry));
  Pull_Resistor pull_resistor_5 (.node(pull_resistor_5_node));
  Pull_Resistor pull_resistor_6 (.node(pull_resistor_6_node));
  Pull_Resistor #(.pull(1)) pull_resistor_7 (.node(pull_resistor_7_node));
  Counter #(.width(10), .max('h3ff)) VCOUNT (
    .load(pull_resistor_5_node), .D(pull_resistor_6_node), .count(pull_resistor_7_node), .Q(VCOUNT_q),
    .carry(VCOUNT_carry), .clk(nand_4_out), .clr(or_2_out));
  Pull_Resistor pull_resistor_8 (.node(VCOUNT_carry));
  assign not_3_out = ~HCOUNT_q;  // NOT_Gate not_3, 10 bits wide
  assign not_4_out = ~VCOUNT_q;  // NOT_Gate not_4, 10 bits wide
  and and_1 (and_1_out, not_3_out[0], not_3_out[1], not_3_out[2], not_3_out[3], HCOUNT_q[9]);
  and and_2 (and_2_out, not_3_out[8], HCOUNT_q[7]);
  and and_3 (and_3_out, VCOUNT_q[5], VCOUNT_q[6], VCOUNT_q[7], VCOUNT_q[8], not_4_out[9]);
  and and_4 (and_4_out, VCOUNT_q[0], not_4_out[1], VCOUNT_q[2], VCOUNT_q[3], not_4_out[4]);
  and and_5 (and_5_out, not_4_out[5], not_4_out[6], not_4_out[7], not_4_out[8], VCOUNT_q[9]);
  nand nand_1 (nand_1_out, and_1_out, and_2_out, not_3_out[4], not_3_out[5], not_3_out[6]);
  nand nand_2 (nand_2_out, and_1_out, and_2_out, HCOUNT_q[4], not_3_out[5], not_3_out[6]);
  nand nand_3 (nand_3_out, and_1_out, and_2_out, HCOUNT_q[4], HCOUNT_q[5], HCOUNT_q[6]);
  nand nand_4 (nand_4_out, and_1_out, not_3_out[4], HCOUNT_q[5], HCOUNT_q[6], not_3_out[7], HCOUNT_q[8]);
  nand nand_5 (nand_5_out, and_3_out, not_4_out[0], not_4_out[1], not_4_out[2], not_4_out[3], not_4_out[4]);
  nand nand_6 (nand_6_out, and_3_out, not_4_out[0], VCOUNT_q[1], not_4_out[2], VCOUNT_q[3], not_4_out[4]);
  nand nand_7 (nand_7_out, and_3_out, not_4_out[0], not_4_out[1], VCOUNT_q[2], VCOUNT_q[3], not_4_out[4]);
  nand nand_8 (nand_8_out, and_4_out, and_5_out);
  nand nand_9 (H_Visible, nand_4_out, nand_10_out);
  nand nand_10 (nand_10_out, H_Visible, nand_1_out);
  nand nand_11 (nand_11_out, nand_2_out, HSYNC);
  nand nand_12 (HSYNC, nand_11_out, nand_3_out);
  nand nand_13 (V_Visible, nand_8_out, nand_14_out);
  nand nand_14 (nand_14_out, V_Visible, nand_5_out);
  nand nand_15 (nand_15_out, nand_6_out, VSYNC);
  nand nand_16 (VSYNC, nand_15_out, nand_7_out);
  Pull_Resistor pull_resistor_9 (.node(pull_resistor_9_node));
  Pull_Resistor pull_resistor_10 (.node(pull_resistor_10_node));
  Pull_Resistor #(.pull(1)) pull_resistor_11 (.node(pull_resistor_11_node));
  Pull_Resistor pull_resistor_12 (.node(pull_resistor_12_node));
  Pull_Resistor pull_resistor_13 (.node(pull_resistor_13_node));
  Pull_Resistor #(.pull(1)) pull_resistor_14 (.node(pull_resistor_14_node));
  Counter #(.width(3), .max('h7)) X_Offset (
    .load(pull_resistor_9_node), .D(pull_resistor_10_node), .count(pull_resistor_11_node), .Q(X_Offset_q),
    .carry(X_Offset_carry), .clk(Clock_out), .clr(Clear_out));
  Pull_Resistor pull_resistor_15 (.node(X_Offset_carry));
  Counter #(.width(3), .max('h7)) Y_Offset (
    .load(pull_resistor_12_node), .D(pull_resistor_13_node), .count(pull_resistor_14_node), .Q(Y_Offset_q),
    .carry(Y_Offset_carry), .clk(nand_4_out), .clr(Clear_out));
  Pull_Resistor pull_resistor_16 (.node(Y_Offset_carry));
  Pull_Resistor pull_resistor_17 (.node(pull_resistor_17_node));
  Pull_Resistor pull_resistor_18 (.node(pull_resistor_18_node));
  Pull_Resistor #(.pull(1)) pull_resistor_19 (.node(pull_resistor_19_node));
  and and_6 (and_6_out, X_Offset_q[0], X_Offset_q[1], X_Offset_q[2]);
  Counter #(.width(13), .max('h1fff)) Frame_Buff_Address (
    .load(pull_resistor_17_node), .D(pull_resistor_18_node), .count(pull_resistor_19_node),
    .Q(Frame_Buff_Address_q), .carry(Frame_Buff_Address_carry), .clk(and_6_out), .clr(or_3_out));
  Pull_Resistor pull_resistor_20 (.node(Frame_Buff_Address_carry));
  or or_3 (or_3_out, Clear_out, not_5_out);
  not not_5 (not_5_out, nand_8_out);
  Pull_Resistor #(.pull(1)) pull_resistor_21 (.node(pull_resistor_21_node));
  Pull_Resistor #(.pull(1)) pull_resistor_22 (.node(pull_resistor_22_node));
  and and_7 (out_4, Clock_out, and_8_out);
  ROM #(.addrWidth(13)) rom_1 (.addr(Frame_Buff_Address_q), .data(rom_1_data), .sel(pull_resistor_21_node));
  ROM #(.addrWidth(11)) rom_2 (.addr({Y_Offset_q, rom_1_data}), .data(rom_2_data), .sel(pull_resistor_22_node));
  BitSelector bitselector_1 (.in(rom_2_data), .out(bitselector_1_out), .sel(X_Offset_q));
  Pull_Resistor pull_resistor_23 (.node(pull_resistor_23_node));
  Pull_Resistor pull_resistor_24 (.node(pull_resistor_24_node));
  Pull_Resistor #(.pull(1)) pull_resistor_25 (.node(pull_resistor_25_node));
  nand nand_17 (nand_17_out, Clock_out, and_8_out);
  D_Flip_Flop d_ff_1 (
    .clk(out_4), .D(bitselector_1_out), .Q(ram_1_data[7]), .reset(Clear_out));  // open: Qn, preset, en
  Counter #(.width(3), .max('h7)) counter_1 (
    .load(pull_resistor_23_node), .D(pull_resistor_24_node), .count(pull_resistor_25_node), .Q(counter_1_q),
    .carry(counter_1_carry), .clk(nand_17_out), .clr(Clear_out));
  Pull_Resistor pull_resistor_26 (.node(counter_1_carry));
  RAM #(.addrWidth(13)) ram_1 (
    .addr(Frame_Buff_Address_q), .data(ram_1_data), .sel(and_6_out), .clk(out_4), .ld(pull_resistor_27_node),
    .clr(Clear_out));
  Pull_Resistor pull_resistor_27 (.node(pull_resistor_27_node));
  D_Flip_Flop d_ff_2 (.clk(out_4), .D(ram_1_data[7]), .Q(ram_1_data[6]), .reset(Clear_out));  // open: Qn, preset, en
  and and_8 (and_8_out, counter_1_q[0], counter_1_q[1], counter_1_q[2]);
  D_Flip_Flop d_ff_3 (.clk(out_4), .D(ram_1_data[6]), .Q(ram_1_data[5]), .reset(Clear_out));  // open: Qn, preset, en
  D_Flip_Flop d_ff_4 (.clk(out_4), .D(ram_1_data[5]), .Q(ram_1_data[4]), .reset(Clear_out));  // open: Qn, preset, en
  D_Flip_Flop d_ff_5 (.clk(out_4), .D(ram_1_data[4]), .Q(ram_1_data[3]), .reset(Clear_out));  // open: Qn, preset, en
  D_Flip_Flop d_ff_6 (.clk(out_4), .D(ram_1_data[3]), .Q(ram_1_data[2]), .reset(Clear_out));  // open: Qn, preset, en
  D_Flip_Flop d_ff_7 (.clk(out_4), .D(ram_1_data[2]), .Q(ram_1_data[1]), .reset(Clear_out));  // open: Qn, preset, en
  D_Flip_Flop d_ff_8 (.clk(out_4), .D(ram_1_data[1]), .Q(ram_1_data[0]), .reset(Clear_out));  // open: Qn, preset, en

  // Notes on the sheet:
  //   Frame Buffer
  //   Font ROM
  //   contents of rom_1 (hex, n*v repeats v):
  //   0 1 2 0 8188*ff
  //   contents of rom_2 (hex, n*v repeats v):
  //   7e 6*18 0 7e 60 60 78 60 60 7e 0 3c 66 60 3c 6 66 3c
endmodule
