// Logisim project sap1.circ as structural Verilog: 1 circuit, main circuit 8Bit Computer
module _8Bit_Computer (
  input  Select,
  input  Manual_Pulse,
  input  in_3,
  input  in_4,
  input  in_5,
  input  in_6,
  input  in_7,
  input  in_8,
  input  in_9,
  input  in_10,
  input  ENABLE,
  input  HLT,
  input  CLEAR,
  input  AO,
  input  AI,
  input  PO,
  input  J,
  input  PC,
  input  EO,
  input  SU,
  input  MO,
  input  MI,
  input  BO,
  input  BI,
  input  RO,
  input  in_26,
  input  in_27,
  input  in_28,
  input  in_29,
  input  IO,
  input  II,
  input  in_32,
  input  in_33,
  input  in_34,
  input  in_35,
  input  RI,
  input  OI,
  input  in_38,
  output out_39,
  output out_40,
  output out_41,
  output out_42,
  output out_43,
  output out_44,
  output out_45,
  output out_46,
  output out_47,
  output out_48,
  output out_49,
  output out_50,
  output out_51,
  output out_52,
  output out_53,
  output out_54,
  output out_55,
  output out_56,
  output out_57,
  output out_58,
  output out_59,
  output out_60,
  output out_61,
  output out_62,
  output out_63,
  output out_64,
  output out_65,
  output out_66,
  output out_67,
  output out_68,
  output out_69,
  output out_70,
  output out_71,
  output out_72,
  output out_73,
  output out_74,
  output out_75
);

  wire and_1_out, and_2_out, and_3_out, Astable_Pulse_out, clock_1_out, counter_2_carry, not_1_out,
       not_2_out, or_1_out, pull_resistor_3_node, pull_resistor_4_node, pull_resistor_5_node;
  wire [1:0] counter_1_q;
  wire [3:0] register_4_q, undriven_2;
  wire [7:0] ram_1_data, register_3_q, register_5_q, rom_1_data, rom_2_data, rom_3_data, xor_1_out;
  wire [10:0] undriven;

  Clock #(.highDuration(30), .lowDuration(30)) Astable_Pulse (.out(Astable_Pulse_out));
  assign xor_1_out = {out_68, out_69, out_70, out_71, out_72, out_73, out_74, out_75} ^ {8{SU}};  // XOR_Gate xor_1, 8 bits wide
  LED led_1 (.in(register_3_q[7]));
  LED led_2 (.in(register_3_q[6]));
  not not_1 (not_1_out, Select);
  not not_2 (not_2_out, HLT);
  Register register_1 (
    .D({out_39, out_40, out_41, out_42, out_43, out_44, out_45, out_46}), .en(AI),
    .Q({out_51, out_52, out_53, out_54, out_55, out_56, out_57, out_58}), .clk(and_3_out), .clr(CLEAR));
  Adder adder_1 (
    .a({out_51, out_52, out_53, out_54, out_55, out_56, out_57, out_58}), .b(xor_1_out),
    .out({out_59, out_60, out_61, out_62, out_63, out_64, out_65, out_66}), .cin(SU), .cout(out_67));
  Register register_2 (
    .D({out_39, out_40, out_41, out_42, out_43, out_44, out_45, out_46}), .en(BI),
    .Q({out_68, out_69, out_70, out_71, out_72, out_73, out_74, out_75}), .clk(and_3_out), .clr(CLEAR));
  Register register_3 (
    .D({out_39, out_40, out_41, out_42, out_43, out_44, out_45, out_46}), .en(II), .Q(register_3_q),
    .clk(and_3_out), .clr(CLEAR));
  LED led_3 (.in(register_3_q[4]));
  LED led_4 (.in(register_3_q[3]));
  LED led_5 (.in(register_3_q[5]));
  LED led_6 (.in(register_3_q[2]));
  and and_1 (and_1_out, Astable_Pulse_out, Select);
  and and_2 (and_2_out, not_1_out, Manual_Pulse);
  assign {out_39, out_40, out_41, out_42, out_43, out_44, out_45, out_46} = EO ? {out_59, out_60, out_61, out_62, out_63, out_64, out_65, out_66} : 8'bz;  // Controlled_Buffer controlled_buffer_1
  assign {out_39, out_40, out_41, out_42, out_43, out_44, out_45, out_46} = BO ? {out_68, out_69, out_70, out_71, out_72, out_73, out_74, out_75} : 8'bz;  // Controlled_Buffer controlled_buffer_2
  LED led_7 (.in(register_3_q[0]));
  LED led_8 (.in(register_3_q[1]));
  or or_1 (or_1_out, and_1_out, and_2_out);
  assign {out_39, out_40, out_41, out_42, out_43, out_44, out_45, out_46} = AO ? {out_51, out_52, out_53, out_54, out_55, out_56, out_57, out_58} : 8'bz;  // Controlled_Buffer controlled_buffer_3
  assign {out_39, out_40, out_41, out_42, out_43, out_44, out_45, out_46} = IO ? {undriven_2, register_3_q[3:0]} : 8'bz;  // Controlled_Buffer controlled_buffer_4
  ROM #(.addrWidth(11)) rom_1 (.addr(undriven), .data(rom_1_data));  // open: sel
  and and_3 (and_3_out, or_1_out, not_2_out);
  ROM #(.addrWidth(11)) rom_2 (.addr(undriven), .data(rom_2_data));  // open: sel
  Pull_Resistor pull_resistor_1 (.node({out_39, out_40, out_41, out_42, out_43, out_44, out_45, out_46}));
  Counter #(.width(2), .max('h3)) counter_1 (
    .count(in_38), .Q(counter_1_q), .clk(clock_1_out));  // open: load, D, carry, clr
  Clock clock_1 (.out(clock_1_out));
  assign {out_39, out_40, out_41, out_42, out_43, out_44, out_45, out_46} = RO ? ram_1_data : 8'bz;  // Controlled_Buffer controlled_buffer_5
  assign {out_39, out_40, out_41, out_42, out_43, out_44, out_45, out_46} = ENABLE ? {in_3, in_4, in_5, in_6, in_7, in_8, in_9, in_10} : 8'bz;  // Controlled_Buffer controlled_buffer_6
  assign {out_43, out_44, out_45, out_46} = PO ? {out_47, out_48, out_49, out_50} : 4'bz;  // Controlled_Buffer controlled_buffer_7
  Counter #(.width(4), .max('hf)) counter_2 (
    .load(J), .D({out_43, out_44, out_45, out_46}), .count(PC), .Q({out_47, out_48, out_49, out_50}),
    .carry(counter_2_carry), .clk(and_3_out), .clr(CLEAR));
  Register #(.width(4)) register_4 (
    .D({out_43, out_44, out_45, out_46}), .en(MI), .Q(register_4_q), .clk(and_3_out), .clr(CLEAR));
  Register register_5 (
    .D({out_39, out_40, out_41, out_42, out_43, out_44, out_45, out_46}), .en(OI), .Q(register_5_q),
    .clk(and_3_out), .clr(CLEAR));
  Pull_Resistor pull_resistor_2 (.node(counter_2_carry));
  assign {out_43, out_44, out_45, out_46} = MO ? register_4_q : 4'bz;  // Controlled_Buffer controlled_buffer_8
  Pull_Resistor #(.pull(1)) pull_resistor_3 (.node(pull_resistor_3_node));
  Pull_Resistor #(.pull(1)) pull_resistor_4 (.node(pull_resistor_4_node));
  RAM #(.addrWidth(4), .bus("separate")) ram_1 (
    .addr(register_4_q), .din({out_39, out_40, out_41, out_42, out_43, out_44, out_45, out_46}),
    .data(ram_1_data), .str(RI), .sel(pull_resistor_3_node), .clk(and_3_out), .ld(pull_resistor_5_node),
    .clr(CLEAR));
  Pull_Resistor #(.pull(1)) pull_resistor_5 (.node(pull_resistor_5_node));
  ROM #(.addrWidth(10)) rom_3 (.addr({counter_1_q, register_5_q}), .data(rom_3_data), .sel(pull_resistor_4_node));
  _7_Segment_Display u_7_segment_display_1 (
    .g(rom_3_data[0]), .f(rom_3_data[1]), .a(rom_3_data[2]), .b(rom_3_data[3]), .e(rom_3_data[4]),
    .d(rom_3_data[5]), .c(rom_3_data[6]), .dp(rom_3_data[7]));
  _7_Segment_Display u_7_segment_display_2 (
    .g(rom_3_data[0]), .f(rom_3_data[1]), .a(rom_3_data[2]), .b(rom_3_data[3]), .e(rom_3_data[4]),
    .d(rom_3_data[5]), .c(rom_3_data[6]), .dp(rom_3_data[7]));
  _7_Segment_Display u_7_segment_display_3 (
    .g(rom_3_data[0]), .f(rom_3_data[1]), .a(rom_3_data[2]), .b(rom_3_data[3]), .e(rom_3_data[4]),
    .d(rom_3_data[5]), .c(rom_3_data[6]), .dp(rom_3_data[7]));
  _7_Segment_Display u_7_segment_display_4 (
    .g(rom_3_data[0]), .f(rom_3_data[1]), .a(rom_3_data[2]), .b(rom_3_data[3]), .e(rom_3_data[4]),
    .d(rom_3_data[5]), .c(rom_3_data[6]), .dp(rom_3_data[7]));
  _7_Segment_Display u_7_segment_display_5 (
    .g(in_26), .f(in_27), .a(in_28), .b(in_29), .e(in_32), .d(in_33), .c(in_34), .dp(in_35));

  // Notes on the sheet:
  //   Instruction Register
  //   Instruction Counter
  //   A Register
  //   ALU (Add/Sub)
  //   B Register
  //   Clock
  //   A In
  //   A Out
  //   IR In
  //   Flags Register
  //   Control Code ROM
  //   Sum Out
  //   B In
  //   B Out
  //   IR 4 LSB Out (instruction operand)
  //   Data Bus Contents
  //   MAR Out (4 LSB to bus)
  //   MAR In (4 LSB from bus)
  //   RAM Out
  //   RAM In
  //   Output Register In
  //   PC Out (4 LSB to Bus)
  //   PC In (4 LSB from Bus)
  //   Psuedo Register (temp loading to bus)
  //   Memory Address Register
  //   RAM
  //   Program Counter
  //   Output Display Control ROM
  //   contents of rom_3 (hex, n*v repeats v):
  //   7e 12 bc b6 d2 e6 ee 32 fe f2 7e 12 bc b6 d2 e6 ee 32 fe f2 7e 12 bc b6 d2 e6 ee 32 fe f2 7e 12 bc
  //   b6 d2 e6 ee 32 fe f2 7e 12 bc b6 d2 e6 ee 32 fe f2 7e 12 bc b6 d2 e6 ee 32 fe f2 7e 12 bc b6 d2 e6
  //   ee 32 fe f2 7e 12 bc b6 d2 e6 ee 32 fe f2 7e 12 bc b6 d2 e6 ee 32 fe f2 7e 12 bc b6 d2 e6 ee 32 fe
  //   f2 7e 12 bc b6 d2 e6 ee 32 fe f2 7e 12 bc b6 d2 e6 ee 32 fe f2 7e 12 bc b6 d2 e6 ee 32 fe f2 7e 12
  //   bc b6 d2 e6 ee 32 fe f2 7e 12 bc b6 d2 e6 ee 32 fe f2 7e 12 bc b6 d2 e6 ee 32 fe f2 7e 12 bc b6 d2
  //   e6 ee 32 fe f2 7e 12 bc b6 d2 e6 ee 32 fe f2 7e 12 bc b6 d2 e6 ee 32 fe f2 7e 12 bc b6 d2 e6 ee 32
  //   fe f2 7e 12 bc b6 d2 e6 ee 32 fe f2 7e 12 bc b6 d2 e6 ee 32 fe f2 7e 12 bc b6 d2 e6 ee 32 fe f2 7e
  //   12 bc b6 d2 e6 ee 32 fe f2 7e 12 bc b6 d2 e6 ee 32 fe f2 7e 12 bc b6 d2 e6 10*7e 10*12 10*bc 10*b6
  //   10*d2 10*e6 10*ee 10*32 10*fe 10*f2 10*7e 10*12 10*bc 10*b6 10*d2 10*e6 10*ee 10*32 10*fe 10*f2
  //   10*7e 10*12 10*bc 10*b6 10*d2 6*e6 100*7e 100*12 56*bc
endmodule
