// Digital circuit 74ls157.dig as structural Verilog
module _74ls157 (
  input  S,
  input  [3:0] A,
  input  [3:0] B,
  input  G,
  input  VCC,
  input  GND,
  output [3:0] Y
);

  wire [3:0] multiplexer_1_out;

  Multiplexer #(.Bits(4)) multiplexer_1 (.sel(S), .in_0(A), .in_1(B), .out(multiplexer_1_out));
  PowerSupply powersupply_1 (.VDD(VCC), .GND(GND));
  Multiplexer #(.Bits(4)) multiplexer_2 (.sel(G), .in_0(multiplexer_1_out), .in_1(4'b0000), .out(Y));

  // Notes on the sheet:
  //   S: select, pin 1
  //   G: strobe, pin 15
  //   VCC: pin 16, default 1
  //   GND: pin 8
endmodule
