// Digital circuit 74ls173.dig as structural Verilog
module _74ls173 (
  input  [3:0] D,
  input  RES,
  input  CLK,
  input  DE1,
  input  DE2,
  input  OE1,
  input  OE2,
  input  VCC,
  input  GND,
  output [3:0] Q
);

  wire nor_1_out, or_1_out;
  wire [3:0] and_1_out, and_2_out, bitextender_1_out, d_ff_as_1_q, not_1_out, or_2_out;

  PowerSupply powersupply_1 (.VDD(VCC), .GND(GND));
  or or_1 (or_1_out, DE1, DE2);
  nor nor_1 (nor_1_out, OE1, OE2);
  BitExtender #(.inputBits(1), .outputBits(4)) bitextender_1 (.in(or_1_out), .out(bitextender_1_out));
  assign not_1_out = ~bitextender_1_out;  // Not not_1, 4 bits wide
  assign and_1_out = d_ff_as_1_q & bitextender_1_out;  // And and_1, 4 bits wide
  assign and_2_out = D & not_1_out;  // And and_2, 4 bits wide
  assign or_2_out = and_1_out | and_2_out;  // Or or_2, 4 bits wide
  D_FF_AS #(.Bits(4)) d_ff_as_1 (.Set(1'b0), .D(or_2_out), .C(CLK), .Clr(RES), .Q(d_ff_as_1_q));  // open: nQ
  assign Q = nor_1_out ? d_ff_as_1_q : 4'bz;  // Driver driver_1

  // Notes on the sheet:
  //   D: pin 14
  //   RES: pin 15, default 1
  //   CLK: pin 7
  //   DE1: pin 9
  //   Q: pin 3
  //   DE2: pin 10
  //   OE1: pin 1
  //   OE2: pin 2
  //   VCC: pin 16, default 1
  //   GND: pin 8
endmodule

/* Test case:
OE1 OE2 RES CLK DE1 DE2 D0 D1 D2 D3 Q0 Q1 Q2 Q3

 0   0   1   x   x   x  x  x  x  x  0  0  0  0 
 0   0   0   1   x   x  x  x  x  x  0  0  0  0 
 0   0   0   0   x   x  x  x  x  x  0  0  0  0 

#clear ff
 0   0   0   c   0   0  0  0  0  0  0  0  0  0 

 0   0   0   c   1   x  x  x  x  x  0  0  0  0 
 0   0   0   c   x   1  x  x  x  x  0  0  0  0 


loop (n,16)
 0   0   0   c   0   0  bits(4,n)  bits(4,n) 
end loop

#clear ff
 0   0   0   c   0   0  0  0  0  0  0  0  0  0 


 0   1   x   x   x   x  x  x  x  x  z  z  z  z 
 1   0   x   x   x   x  x  x  x  x  z  z  z  z 
 1   1   x   x   x   x  x  x  x  x  z  z  z  z 
*/
