// Digital circuit 74ls245.dig as structural Verilog
module _74ls245 (
  input  DIR,
  input  nOE,
  input  [7:0] A,
  input  [7:0] B,
  input  VCC,
  input  GND
);

  wire and_1_out, and_2_out;

  PowerSupply powersupply_1 (.VDD(VCC), .GND(GND));
  and and_1 (and_1_out, DIR, ~nOE);  // And
  assign B = and_1_out ? A : 8'bz;  // Driver driver_1
  assign A = and_2_out ? B : 8'bz;  // Driver driver_2
  and and_2 (and_2_out, ~nOE, ~DIR);  // And

  // Notes on the sheet:
  //   DIR: pin 1
  //   nOE: pin 19
  //   A: pin 2
  //   B: pin 18
  //   VCC: pin 20, default 1
  //   GND: pin 10
endmodule
