// Digital circuit 74ls260.dig as structural Verilog
module _74ls260 (
  input  _1A,
  input  _2A,
  input  _3A,
  input  _4A,
  input  _5A,
  input  _1B,
  input  _2B,
  input  _3B,
  input  _4B,
  input  _5B,
  input  VCC,
  input  GND,
  output _1Y,
  output _2Y
);

  nor nor_1 (_1Y, _1A, _2A, _3A, _4A, _5A);
  nor nor_2 (_2Y, _1B, _2B, _3B, _4B, _5B);
  PowerSupply powersupply_1 (.VDD(VCC), .GND(GND));
endmodule
