// Digital circuit 74ls273.dig as structural Verilog
module _74ls273 (
  input  CP,
  input  nMR,
  input  [7:0] D,
  input  VCC,
  input  GND,
  output [7:0] Q
);

  wire not_1_out;

  not not_1 (not_1_out, nMR);
  PowerSupply powersupply_1 (.VDD(VCC), .GND(GND));
  D_FF_AS #(.Bits(8)) d_ff_as_1 (.Set(1'b0), .D(D), .C(CP), .Clr(not_1_out), .Q(Q));  // open: nQ

  // Notes on the sheet:
  //   CP: pin 11
  //   nMR: pin 1, default 1
  //   D: pin 3
  //   Q: pin 2
  //   VCC: pin 20, default 1
  //   GND: pin 10
endmodule

/* Test case:
~MR CP D Q
 0  x  x  0
 1  0  1  0
 1  1  1  1
 1  0  x  1
 1  0  0  1
 1  1  0  0
 1  0  x  0
*/
