// Digital circuit 74ls283.dig as structural Verilog
module _74ls283 (
  input  [3:0] A,
  input  [3:0] B,
  input  C_in,
  input  VCC,
  input  GND,
  output [3:0] S,
  output C_out
);

  PowerSupply powersupply_1 (.VDD(VCC), .GND(GND));
  Add #(.Bits(4)) add_1 (.a(A), .b(B), .c_i(C_in), .s(S), .c_o(C_out));

  // Notes on the sheet:
  //   C_in: pin 7
  //   VCC: pin 16, default 1
  //   GND: pin 8
  //   C_out: pin 9
endmodule

/* Test case:
# A complete test of all 512 possible additions
#

C0   A4 A3 A2 A1   B4 B3 B2 B1  C4 S4 S3 S2 S1
loop(A,16)
  loop(B,16)
0    bits(4,A)     bits(4,B)    bits(5,A+B)
1    bits(4,A)     bits(4,B)    bits(5,A+B+1)
  end loop
end loop
*/
