// Digital circuit 74ls574.dig as structural Verilog
module _74ls574 (
  input  nOC,
  input  CLK,
  input  [7:0] D,
  input  VCC,
  input  GND,
  output [7:0] Q
);

  wire [7:0] d_ff_1_q;

  D_FF #(.Bits(8)) d_ff_1 (.D(D), .C(CLK), .Q(d_ff_1_q));  // open: nQ
  PowerSupply powersupply_1 (.VDD(VCC), .GND(GND));
  assign Q = ~nOC ? d_ff_1_q : 8'bz;  // DriverInvSel driverinvsel_1

  // Notes on the sheet:
  //   nOC: pin 1, default 1
  //   CLK: pin 11
  //   VCC: pin 20, default 1
  //   GND: pin 10
endmodule
