// Digital circuit BW8comp.dig as structural Verilog
module BW8comp (
  input  crystal,
  input  _555,
  input  step,
  output r_nw,
  output nack
);

  wire clk_cpu, clk_crystal, nbrk, nRST_out;
  wire [2:0] Break_out, triple_clock_1_p9;
  wire [2:2] rst_clk_mode;
  wire [7:0] bw8cpu_1_data;
  wire [15:0] bw8cpu_1_addr;

  Button nRST (.out(nRST_out));
  Button #(.activeLow("true")) Run (.out(Break_out[0]));
  Button #(.activeLow("true")) Demo (.out(Break_out[1]));
  Button #(.activeLow("true")) Break (.out(Break_out[2]));
  reset_module reset_module_1 (.clk(clk_crystal), .nrst_in(nRST_out), .nrst(rst_clk_mode[2]));
  // Probe ~rst on rst_clk_mode[2]
  BW8cpu bw8cpu_1 (
    .VCC(1'b1), .GND(1'b0), .nIRQ(1'b1), .nREQ(1'b1), .crystal(clk_cpu), ._555(rst_clk_mode[2]),
    .ADDR(bw8cpu_1_addr), .DATA(bw8cpu_1_data), .R_nW(r_nw), .nACK(nack), .nBRK(nbrk));  // open: step
  // triple_clock triple_clock_1: pin names not known; wires that end beside it: {rst_clk_mode[2], 2'b11}, nbrk, Break_out, crystal, _555, step, clk_cpu, clk_crystal, triple_clock_1_p9
  LED u_crystal (.in(clk_crystal));
  // Probe addr on bw8cpu_1_addr
  // Probe data on bw8cpu_1_data
  LED cpu (.in(clk_cpu));
  LED Run_Mode_Active (.in(triple_clock_1_p9[0]));
  LED Demo_Mode_Active (.in(triple_clock_1_p9[1]));
  LED Break_Mode_Active (.in(triple_clock_1_p9[2]));
  ROM #(.AddrBits(16), .isProgramMemory("true"), .Bits(8)) ROM___64K (.A(bw8cpu_1_addr), .sel(1'b1), .D(bw8cpu_1_data));

  // Notes on the sheet:
  //   crystal: Hz: 5
  //   ROM___64K loads rom_image.bin
endmodule
