// Digital circuit BW8cpu.dig as structural Verilog
module BW8cpu (
  input  step,
  input  crystal,
  input  _555,
  input  VCC,
  input  GND,
  input  nREQ,
  input  nNMI,
  input  nIRQ,
  output pass,
  output fail,
  output nACK,
  output D_nC,
  output MEM_nIO,
  output R_nW,
  output [7:0] DATA,
  output [19:0] ADDR,
  output U_nS
);

  wire a_dbus_a, a_dbus_l, a_lhs_a, a_rhs_a, addr_inc, addr_xfer_a, alu_dbus_a, b_dbus_a, b_dbus_l, b_lhs_a,
       b_rhs_a, br_dbus_a, br_dbus_l, c_dbus_a, c_dbus_l, c_f, c_lhs_a, c_rhs_a, clk, clk_crystal, clr_ubr,
       comparator_1_eq, d_dbus_a, d_dbus_l, d_lhs_a, d_rhs_a, da_dbus_a, da_dbus_l, dec_sp, dp_dbus_a,
       dp_dbus_l, ext, io_addr_a, ir_dbus_l, isr_xfer_a, lsb_dbus_a, mem_dbus_a, mem_dbus_l, msb_dbus_a,
       musteq_load, nclk, noffset, not_1_out, not_2_out, not_3_out, not_4_out, not_5_out, nrst, nRST_out, oe,
       off_dbus_l, pc_addr_a, pc_inc, pc_xfer_a, pc_xfer_l, pch_dbus_l, pcl_dbus_l, ram_cs, reg_a, reg_b,
       reg_c, reg_d, reg_da, reg_dp, reset_1_out, rom_cs, rst, set_nmi_inh, set_sup, set_ubr, sp_addr_a,
       sp_dec, sp_inc, sp_xfer_a, sp_xfer_l, sph_dbus_l, spl_dbus_l, sr_dbus_a, sr_dbus_l, t_addr_a,
       th_dbus_a, th_dbus_l, th_lhs_a, tl_dbus_a, tl_dbus_l, tl_rhs_a, we, x_addr_a, x_dec, x_inc, x_xfer_a,
       x_xfer_l, xh_dbus_l, xl_dbus_l, y_addr_a, y_dec, y_inc, y_xfer_a, y_xfer_l, yh_dbus_l, yl_dbus_l;
  wire [1:0] Control_Unit_dbg_2;
  wire [2:0] addr_a, Break_out, clk_mode, count, t_state, xfer_l;
  wire [3:0] alu_op, dbus_a;
  wire [4:0] dbus_l, xfer_a;
  wire [7:0] alu_res, dbus, driver_1_out, driver_2_out, flags, lhs, opcode, reg_off, reg_th, reg_tl, rhs;
  wire [14:3] Control_Unit_dbg;
  wire [15:0] addr_t, reg_pc, reg_sp, reg_x, reg_y;

  LED led_1 (.in(clk));
  LED led_2 (.in(nrst));
  // Probe on dbus
  // Probe on {lhs, rhs}
  // Probe on ADDR
  // Probe NMI-I_f on flags[7]
  // Probe UBR_f on flags[6]
  // Probe U/~S_f on U_nS
  // Probe C_f on c_f
  // Probe Z_f on flags[3]
  // Probe V_f on flags[2]
  // Probe N_f on flags[1]
  // Probe I_f on flags[0]
  // Probe on opcode
  // Probe on t_state
  PowerSupply powersupply_1 (.VDD(VCC), .GND(GND));
  PullUp pullup_1 (.out(R_nW));
  PullUp pullup_2 (.out(MEM_nIO));
  PullDown #(.Bits(20)) pulldown_1 (.out(ADDR));
  PullDown #(.Bits(8)) pulldown_2 (.out(DATA));
  PullUp pullup_3 (.out(D_nC));
  // Probe on addr_t
  // Probe on DATA
  // Probe on reg_pc
  // Probe on reg_sp
  // Probe on reg_x
  // Probe on reg_y
  // Probe on reg_a
  // Probe on reg_b
  // Probe on reg_c
  // Probe on reg_d
  // Probe on reg_dp
  // Probe on reg_da
  // Probe on reg_tl
  // Probe on reg_th
  // Probe on reg_off
  // Probe on alu_res
  // Probe on opcode
  // Probe on ext
  instruction_register Instruction_Register (
    .dbus(dbus), .ndbus_load(ir_dbus_l), .clr(rst), .nclk(nclk), .opcode(opcode));
  Reset reset_1 (.out(reset_1_out));
  Button #(.activeLow("true")) u_nRST (.out(nRST_out));
  Button #(.activeLow("true")) Run (.out(Break_out[0]));
  Button #(.activeLow("true")) Demo (.out(Break_out[1]));
  Button #(.activeLow("true")) Break (.out(Break_out[2]));
  not not_1 (not_1_out, musteq_load);
  // Probe on {flags[7:6], U_nS, c_f, flags[3:0]}
  control_unit Control_Unit (
    .nirq(nIRQ), .opcode(opcode), .flags({flags[7:6], U_nS, c_f, flags[3:0]}), .nreq(nREQ), .nrst(nrst),
    .nnmi(nNMI), .clk(clk), .nmi_addr(16'h6), .irq_addr(16'h3), .addr_assert_int(isr_xfer_a),
    .dbus_assert(dbus_a), .dbus_load(dbus_l), .alu_op(alu_op), .xfer_assert(xfer_a), .xfer_load(xfer_l),
    .addr_assert(addr_a), .count(count), .dec_sp(dec_sp), .nclk(nclk), .noffset(noffset), .rst(rst),
    .dbg({Control_Unit_dbg_2, ext, Control_Unit_dbg, t_state}), .int_addr({lhs, rhs}), .clr_ubr(clr_ubr),
    .set_ubr(set_ubr), .set_sup(set_sup), .set_nmi_inhib(set_nmi_inh));
  and and_1 (nrst, reset_1_out, nRST_out);
  assign driver_1_out = not_1_out ? dbus : 8'bz;  // Driver driver_1
  assign driver_2_out = not_1_out ? lhs : 8'bz;  // Driver driver_2
  PullDown #(.Bits(8)) pulldown_3 (.out(driver_2_out));
  // Probe on t_state
  addr_decoding addr_decoding_1 (
    .A15(ADDR[15]), .R_nW(R_nW), .nCLK(nclk), .ROM_CS(rom_cs), .RAM_CS(ram_cs), .WE(we), .OE(oe));
  // triple_clock triple_clock_1: pin names not known; wires that end beside it: Break_out, 1'b1, {nrst, 2'b11}, crystal, _555, step, clk, clk_crystal, clk_mode
  Comparator #(.Bits(8)) comparator_1 (.a(driver_1_out), .b(driver_2_out), .eq(comparator_1_eq));  // open: gt, lt
  not not_2 (not_2_out, musteq_load);
  PullDown #(.Bits(8)) pulldown_4 (.out(driver_1_out));
  // Probe on nclk
  assign dbus = ~msb_dbus_a ? lhs : 8'bz;  // DriverInvSel driverinvsel_1
  assign dbus = ~lsb_dbus_a ? rhs : 8'bz;  // DriverInvSel driverinvsel_2
  and and_2 (pass, comparator_1_eq, not_2_out);
  and and_3 (fail, not_2_out, not_3_out);
  not not_3 (not_3_out, comparator_1_eq);
  // Probe on count
  // Probe on dec_sp
  memory_bridge Memory_Bridge (.dbus_assert(mem_dbus_a), .dbus_load(mem_dbus_l), .dbus(dbus), .mbus(DATA));
  LED u_crystal (.in(clk_crystal));
  LED cpu (.in(clk));
  LED Run_Mode_Active (.in(clk_mode[0]));
  LED Demo_Mode_Active (.in(clk_mode[1]));
  LED Break_Mode_Active (.in(clk_mode[2]));
  // Probe on addr_a
  RAMSinglePortSel #(.AddrBits(15), .Bits(8)) ramsingleportsel_1 (
    .A(ADDR[14:0]), .CS(ram_cs), .WE(we), .OE(oe), .D(DATA));
  ROM #(.AddrBits(15), .isProgramMemory("true"), .Bits(8)) rom_1 (.A(ADDR[14:0]), .sel(rom_cs), .D(DATA));
  // Probe on xfer_l
  // Probe on xfer_a
  // bus_controller Bus_Controller: pin names not known; wires that end beside it: dbus_a, xfer_l, addr_a, clk, count, dec_sp, nclk, dbus_l, xfer_a, alu_dbus_a, a_dbus_a, b_dbus_a, c_dbus_a, d_dbus_a, dp_dbus_a, da_dbus_a, th_dbus_a, tl_dbus_a, sr_dbus_a, mem_dbus_a, msb_dbus_a, lsb_dbus_a
  // Probe on alu_op
  // Probe on dbus_l
  // Probe on dbus_a
  alu Arithmetic___Logic_Unit_and_Status_Register (
    .alu_op(alu_op), .load_sr_dbus(sr_dbus_l), .assert_sr_dbus(sr_dbus_a), .clk(nclk), .clr(rst), .lhs(lhs),
    .rhs(rhs), .assert_alu_dbus(alu_dbus_a), .set_nmi_inhib(set_nmi_inh), .clr_ubr(clr_ubr),
    .set_ubr(set_ubr), .set_sup(set_sup), .flags({flags[7:6], U_nS, c_f, flags[3:0]}), .dbus(dbus),
    .q(alu_res));
  // gpr_pair A_and_B: pin names not known; wires that end beside it: a_dbus_l, b_dbus_l, c_dbus_l, d_dbus_l, dp_dbus_l, da_dbus_l, a_dbus_l, b_dbus_l, a_dbus_a, b_dbus_a, a_lhs_a, b_lhs_a, a_rhs_a, b_rhs_a, dbus, rst, nclk, reg_a, reg_b, {lhs, rhs}
  // gpr_pair C_and_D: pin names not known; wires that end beside it: pcl_dbus_l, sph_dbus_l, spl_dbus_l, xh_dbus_l, xl_dbus_l, yh_dbus_l, yl_dbus_l, pc_xfer_a, sp_xfer_a, c_dbus_l, d_dbus_l, c_dbus_a, d_dbus_a, c_lhs_a, d_lhs_a, c_rhs_a, d_rhs_a, dbus, rst, nclk, reg_c, reg_d, {lhs, rhs}
  // gpr_pair DA_and_DP: pin names not known; wires that end beside it: d_lhs_a, th_lhs_a, a_rhs_a, b_rhs_a, c_rhs_a, d_rhs_a, tl_rhs_a, pc_xfer_l, sp_xfer_l, dp_dbus_l, da_dbus_l, dp_dbus_a, da_dbus_a, 1'b1, 1'b1, 1'b1, 1'b1, dbus, rst, nclk, reg_dp, reg_da, {lhs, rhs}
  temp_reg_pair temp_reg_pair_1 (
    .nhi_dbus_load(th_dbus_l), .nlo_dbus_load(tl_dbus_l), .nhi_dbus_assert(th_dbus_a),
    .nlo_dbus_assert(tl_dbus_a), .nhi_lhs_assert(th_lhs_a), .nlo_lhs_assert(1'b1), .nhi_rhs_assert(1'b1),
    .nlo_rhs_assert(tl_rhs_a), .dbus(dbus), .clr(rst), .nclk(nclk), .naddr_assert(t_addr_a), .reg_hi(reg_th),
    .reg_lo(reg_tl), .xfer({lhs, rhs}), .addr(addr_t));
  not not_4 (not_4_out, addr_inc);
  not not_5 (not_5_out, nACK);
  address_register Program_Counter (
    .clk(clk), .clr(rst), .inc(pc_inc), .dec(1'b1), .xfer_load(pc_xfer_l), .addr_assert(pc_addr_a),
    .xfer_assert(pc_xfer_a), .dbus_load_hi(pch_dbus_l), .dbus_load_lo(pcl_dbus_l), .dbus(dbus),
    .addr(addr_t), .xfer({lhs, rhs}), .\reg (reg_pc));
  address_register Stack_Pointer (
    .clk(clk), .clr(rst), .inc(sp_inc), .dec(sp_dec), .xfer_load(sp_xfer_l), .addr_assert(sp_addr_a),
    .xfer_assert(sp_xfer_a), .dbus_load_hi(sph_dbus_l), .dbus_load_lo(spl_dbus_l), .dbus(dbus),
    .addr(addr_t), .xfer({lhs, rhs}), .\reg (reg_sp));
  address_register X_Index (
    .clk(clk), .clr(rst), .inc(x_inc), .dec(x_dec), .xfer_load(x_xfer_l), .addr_assert(x_addr_a),
    .xfer_assert(x_xfer_a), .dbus_load_hi(xh_dbus_l), .dbus_load_lo(xl_dbus_l), .dbus(dbus), .addr(addr_t),
    .xfer({lhs, rhs}), .\reg (reg_x));
  address_register Y_Index (
    .clk(clk), .clr(rst), .inc(y_inc), .dec(y_dec), .xfer_load(y_xfer_l), .addr_assert(y_addr_a),
    .xfer_assert(y_xfer_a), .dbus_load_hi(yh_dbus_l), .dbus_load_lo(yl_dbus_l), .dbus(dbus), .addr(addr_t),
    .xfer({lhs, rhs}), .\reg (reg_y));
  address_offset Address_Bridge (
    .dbus(dbus), .addr_in(addr_t), .noffset_en(noffset), .carry_en(not_4_out),
    .naddr_xfer_assert(addr_xfer_a), .nassert_addr(not_5_out), .clr(rst), .noffset_load(off_dbus_l),
    .nclock(nclk), .R_nW(mem_dbus_l), .MEM_nIO(io_addr_a), .D_nC(pc_addr_a), .nACK(nACK),
    .nload_br(br_dbus_l), .nassert_br(br_dbus_a), .U_nS(1'b0), .UBR_f(1'b0), .addr_out(ADDR),
    .xfer({lhs, rhs}), .q(reg_off), .R_nW_z(R_nW), .MEM_nIO_z(MEM_nIO), .D_nC_z(D_nC));

  // Other names for the same wires on the sheet: ack_addr_a = nACK; aout[19:0] = ADDR; low_15[14:0] = ADDR[14:0];
  //   clk_cpu = clk; d_nc_z = D_nC; i_f = flags[0]; n_f = flags[1]; v_f = flags[2]; z_f = flags[3];
  //   flags[5:4] = {U_nS, c_f}; u_ns_f = U_nS; ubr_f = flags[6]; nmi_i_f = flags[7]; mbus[7:0] = DATA;
  //   mem_nio_z = MEM_nIO; rst_clk_mode[2] = nrst; r_nw_z = R_nW; xfer[15:0] = {lhs, rhs}

  // Notes on the sheet:
  //   crystal: Hz: 50
  //   _555: Hz: 5
  //   VCC: default 1
  //   nREQ: default 1
  //   nNMI: default 1
  //   nIRQ: default 1
  //   External Pinout
  //   CLK
  //   ~RST
  //   Buses & Constants
  //   Registers
  //   rom_1 loads sim_test.bin
endmodule

/* Test case Start A:
step pass fail

program(0x01, 0xfc, 0x00)

let i = 0;
while(!(pass | fail | (i >= 100)))
    let i = i + 1;
    0 0 0
    1 x x
end while
0 1 0
*/

/* Test case Load A Imm:
step pass fail

program(0x14, 0x69, 0x01, 0xfc, 0x69)

let i = 0;
while(!(pass | fail | (i >= 100)))
    let i = i + 1;
    0 0 0
    1 x x
end while
0 1 0
*/

/* Test case Load A Abs:
step pass fail

program(0x15, 0x00, 0x08, 0x01, 0xfc, 0x69, 0x00, 0x00, 0x69)

let i = 0;
while(!(pass | fail | (i >= 100)))
    let i = i + 1;
    0 0 0
    1 x x
end while
0 1 0
*/

/* Test case Start B:
step pass fail

program(0x01, 0xfd, 0x00)

let i = 0;
while(!(pass | fail | (i >= 100)))
    let i = i + 1;
    0 0 0
    1 x x
end while
0 1 0
*/

/* Test case Load B Imm:
step pass fail

program(0x26, 0x69, 0x01, 0xfd, 0x69)

let i = 0;
while(!(pass | fail | (i >= 100)))
    let i = i + 1;
    0 0 0
    1 x x
end while
0 1 0
*/

/* Test case Start C:
step pass fail

program(0x01, 0xfe, 0x00)

let i = 0;
while(!(pass | fail | (i >= 100)))
    let i = i + 1;
    0 0 0
    1 x x
end while
0 1 0
*/

/* Test case Load C Imm:
step pass fail

program(0x38, 0x69, 0x01, 0xfe, 0x69)

let i = 0;
while(!(pass | fail | (i >= 100)))
    let i = i + 1;
    0 0 0
    1 x x
end while
0 1 0
*/

/* Test case Start D:
step pass fail

program(0x01, 0xff, 0x00)

let i = 0;
while(!(pass | fail | (i >= 100)))
    let i = i + 1;
    0 0 0
    1 x x
end while
0 1 0
*/

/* Test case Load D Imm:
step pass fail

program(0x4a, 0x69, 0x01, 0xff, 0x69)

let i = 0;
while(!(pass | fail | (i >= 100)))
    let i = i + 1;
    0 0 0
    1 x x
end while
0 1 0
*/
