// Digital circuit Bruno_AddrRes_Card.dig as structural Verilog
module Bruno_AddrRes_Card (
  input  [6:0] Control,
  output [23:0] ADDR,
  output [23:0] XFER,
  output [23:0] I,
  output inc,
  output Reg_assert,
  output [23:0] I_reg
);

  wire _74193_1_pin12, _74193_1_pin13, _74193_2_pin12, _74193_2_pin13, _74193_3_pin12, _74193_3_pin13,
       _74193_4_pin12, _74193_4_pin13, _74193_5_pin12, _74193_5_pin13;

  not not_1 (Reg_assert, Control[5]);
  _74193 _74193_1 (
    .pin1(XFER[1]), .pin2(I[1]), .pin3(I[0]), .pin4(Control[2]), .pin5(Control[3]), .pin6(I[2]), .pin7(I[3]),
    .pin8(1'b0), .pin9(XFER[3]), .pin10(XFER[2]), .pin11(Control[4]), .pin12(_74193_1_pin12),
    .pin13(_74193_1_pin13), .pin14(Control[1]), .pin15(XFER[0]), .pin16(1'b1));
  _74193 _74193_2 (
    .pin1(XFER[5]), .pin2(I[5]), .pin3(I[4]), .pin4(_74193_1_pin13), .pin5(_74193_1_pin12), .pin6(I[6]),
    .pin7(I[7]), .pin8(1'b0), .pin9(XFER[7]), .pin10(XFER[6]), .pin11(Control[4]), .pin12(_74193_2_pin12),
    .pin13(_74193_2_pin13), .pin14(Control[1]), .pin15(XFER[4]), .pin16(1'b1));
  _74574 _74574_1 (
    .pin1(Control[6]), .pin2(I[0]), .pin3(I[1]), .pin4(I[2]), .pin5(I[3]), .pin6(I[4]), .pin7(I[5]),
    .pin8(I[6]), .pin9(I[7]), .pin10(1'b0), .pin11(Control[0]), .pin12(XFER[7]), .pin13(XFER[6]),
    .pin14(XFER[5]), .pin15(XFER[4]), .pin16(XFER[3]), .pin17(XFER[2]), .pin18(XFER[1]), .pin19(XFER[0]),
    .pin20(1'b1));
  _74574 _74574_2 (
    .pin1(Control[6]), .pin2(I[8]), .pin3(I[9]), .pin4(I[10]), .pin5(I[11]), .pin6(I[12]), .pin7(I[13]),
    .pin8(I[14]), .pin9(I[15]), .pin10(1'b0), .pin11(Control[0]), .pin12(XFER[15]), .pin13(XFER[14]),
    .pin14(XFER[13]), .pin15(XFER[12]), .pin16(XFER[11]), .pin17(XFER[10]), .pin18(XFER[9]), .pin19(XFER[8]),
    .pin20(1'b1));
  _74193 _74193_3 (
    .pin1(XFER[9]), .pin2(I[9]), .pin3(I[8]), .pin4(_74193_2_pin13), .pin5(_74193_2_pin12), .pin6(I[10]),
    .pin7(I[11]), .pin8(1'b0), .pin9(XFER[11]), .pin10(XFER[10]), .pin11(Control[4]), .pin12(_74193_3_pin12),
    .pin13(_74193_3_pin13), .pin14(Control[1]), .pin15(XFER[8]), .pin16(1'b1));
  _74574 _74574_3 (
    .pin1(Control[6]), .pin2(I[16]), .pin3(I[17]), .pin4(I[18]), .pin5(I[19]), .pin6(I[20]), .pin7(I[21]),
    .pin8(I[22]), .pin9(I[23]), .pin10(1'b0), .pin11(Control[0]), .pin12(XFER[23]), .pin13(XFER[22]),
    .pin14(XFER[21]), .pin15(XFER[20]), .pin16(XFER[19]), .pin17(XFER[18]), .pin18(XFER[17]),
    .pin19(XFER[16]), .pin20(1'b1));
  _74574 _74574_4 (
    .pin1(Control[5]), .pin2(I[16]), .pin3(I[17]), .pin4(I[18]), .pin5(I[19]), .pin6(I[20]), .pin7(I[21]),
    .pin8(I[22]), .pin9(I[23]), .pin10(1'b0), .pin11(Control[0]), .pin12(ADDR[23]), .pin13(ADDR[22]),
    .pin14(ADDR[21]), .pin15(ADDR[20]), .pin16(ADDR[19]), .pin17(ADDR[18]), .pin18(ADDR[17]),
    .pin19(ADDR[16]), .pin20(1'b1));
  _74193 _74193_4 (
    .pin1(XFER[13]), .pin2(I[13]), .pin3(I[12]), .pin4(_74193_3_pin13), .pin5(_74193_3_pin12), .pin6(I[14]),
    .pin7(I[15]), .pin8(1'b0), .pin9(XFER[15]), .pin10(XFER[14]), .pin11(Control[4]), .pin12(_74193_4_pin12),
    .pin13(_74193_4_pin13), .pin14(Control[1]), .pin15(XFER[12]), .pin16(1'b1));
  _74574 _74574_5 (
    .pin1(Control[5]), .pin2(I[0]), .pin3(I[1]), .pin4(I[2]), .pin5(I[3]), .pin6(I[4]), .pin7(I[5]),
    .pin8(I[6]), .pin9(I[7]), .pin10(1'b0), .pin11(Control[0]), .pin12(ADDR[7]), .pin13(ADDR[6]),
    .pin14(ADDR[5]), .pin15(ADDR[4]), .pin16(ADDR[3]), .pin17(ADDR[2]), .pin18(ADDR[1]), .pin19(ADDR[0]),
    .pin20(1'b1));
  _74574 _74574_6 (
    .pin1(Control[5]), .pin2(I[8]), .pin3(I[9]), .pin4(I[10]), .pin5(I[11]), .pin6(I[12]), .pin7(I[13]),
    .pin8(I[14]), .pin9(I[15]), .pin10(1'b0), .pin11(Control[0]), .pin12(ADDR[15]), .pin13(ADDR[14]),
    .pin14(ADDR[13]), .pin15(ADDR[12]), .pin16(ADDR[11]), .pin17(ADDR[10]), .pin18(ADDR[9]), .pin19(ADDR[8]),
    .pin20(1'b1));
  _74193 _74193_5 (
    .pin1(XFER[17]), .pin2(I[17]), .pin3(I[16]), .pin4(_74193_4_pin13), .pin5(_74193_4_pin12), .pin6(I[18]),
    .pin7(I[19]), .pin8(1'b0), .pin9(XFER[19]), .pin10(XFER[18]), .pin11(Control[4]), .pin12(_74193_5_pin12),
    .pin13(_74193_5_pin13), .pin14(Control[1]), .pin15(XFER[16]), .pin16(1'b1));
  _74193 _74193_6 (
    .pin1(XFER[21]), .pin2(I[21]), .pin3(I[20]), .pin4(_74193_5_pin13), .pin5(_74193_5_pin12), .pin6(I[22]),
    .pin7(I[23]), .pin8(1'b0), .pin9(XFER[23]), .pin10(XFER[22]), .pin11(Control[4]), .pin14(Control[1]),
    .pin15(XFER[20]), .pin16(1'b1));  // open: pin12, pin13

  assign I_reg = ADDR;
  assign inc = Control[3];

  // Other names for the same wires on the sheet: Reg_H[7:0] = I[23:16]; Addr_L[15:0] = ADDR[15:0];
  //   Reg_L[15:0] = I[15:0]; Addr_H[7:0] = ADDR[23:16]; Xfer_H[7:0] = XFER[23:16]; Xfer_L[15:0] = XFER[15:0];
  //   Clock = Control[0]; Clear = Control[1]; Dec = Control[2]; Load = Control[4]; A_Addr = Control[5];
  //   A_Bus = Control[6]

  // Notes on the sheet:
  //   ADDR: Addr Bus
  //   XFER: Xfer Bus
  //   Control: 0: Clock
  //   1: Clear
  //   2: Dec
  //   3: Inc
  //   4: Load
  //   5: Assert Addr
  //   6: Assert Bus
endmodule
