// Digital circuit accumulator.dig as structural Verilog
module accumulator (
  input  addr_assert,
  input  xfer_load,
  input  a_dbus_load,
  input  b_dbus_load,
  input  a_dbus_assert,
  input  b_dbus_assert,
  input  a_lhs_assert,
  input  b_lhs_assert,
  input  a_rhs_assert,
  input  b_rhs_assert,
  input  [7:0] dbus,
  input  [15:0] xfer,
  input  nclr,
  output [15:0] addr,
  output [7:0] reg_a,
  output [7:0] reg_b
);

  wire load_a, load_b, load_control_p5, load_control_p6, load_control_p7, load_control_p8;
  wire [3:0] d_00, d_01, d_10, d_11;

  // _7408 load_control: pin names not known; wires that end beside it: xfer_load, a_dbus_load, xfer_load, b_dbus_load, load_control_p5, load_control_p6, load_control_p7, load_control_p8, 1'b1, 1'b0, load_a, load_b
  // NotConnected on load_control_p5
  // NotConnected on load_control_p6
  // NotConnected on load_control_p7
  // NotConnected on load_control_p8
  _74ls157 A_hi_mux_in (.S(a_dbus_load), .A(dbus[7:4]), .B(xfer[15:12]), .G(1'b0), .VCC(1'b1), .GND(1'b0), .Y(d_11));
  _74ls273 A_Register (.CP(load_a), .nMR(nclr), .D({d_11, d_10}), .VCC(1'b1), .GND(1'b0), .Q(reg_a));
  _74ls245 A_to_dbus (.DIR(1'b1), .nOE(a_dbus_assert), .A(reg_a), .B(dbus), .VCC(1'b1), .GND(1'b0));
  _74ls245 A_to_rhs (.DIR(1'b1), .nOE(a_rhs_assert), .A(reg_a), .B(xfer[7:0]), .VCC(1'b1), .GND(1'b0));
  _74ls273 B_Register (.CP(load_b), .nMR(nclr), .D({d_01, d_00}), .VCC(1'b1), .GND(1'b0), .Q(reg_b));
  _74ls157 A_lo_mux_in (.S(a_dbus_load), .A(dbus[3:0]), .B(xfer[11:8]), .G(1'b0), .VCC(1'b1), .GND(1'b0), .Y(d_10));
  _74ls245 A_to_lhs (.DIR(1'b1), .nOE(a_lhs_assert), .A(reg_a), .B(xfer[15:8]), .VCC(1'b1), .GND(1'b0));
  _74ls245 A_to_addr (.DIR(1'b1), .nOE(addr_assert), .A(reg_a), .B(addr[15:8]), .VCC(1'b1), .GND(1'b0));
  _74ls157 B_hi_mux_in (.S(b_dbus_load), .A(dbus[7:4]), .B(xfer[7:4]), .G(1'b0), .VCC(1'b1), .GND(1'b0), .Y(d_01));
  _74ls245 B_to_dbus (.DIR(1'b1), .nOE(b_dbus_assert), .A(reg_b), .B(dbus), .VCC(1'b1), .GND(1'b0));
  _74ls245 B_to_rhs (.DIR(1'b1), .nOE(b_rhs_assert), .A(reg_b), .B(xfer[7:0]), .VCC(1'b1), .GND(1'b0));
  _74ls157 B_lo_mux_in (.S(b_dbus_load), .A(dbus[3:0]), .B(xfer[3:0]), .G(1'b0), .VCC(1'b1), .GND(1'b0), .Y(d_00));
  _74ls245 B_to_lhs (.DIR(1'b1), .nOE(b_lhs_assert), .A(reg_b), .B(xfer[15:8]), .VCC(1'b1), .GND(1'b0));
  _74ls245 B_to_addr (.DIR(1'b1), .nOE(addr_assert), .A(reg_b), .B(addr[7:0]), .VCC(1'b1), .GND(1'b0));

  // Other names for the same wires on the sheet: addr_hi[7:0] = addr[15:8]; addr_lo[7:0] = addr[7:0];
  //   assert_a_dbus = a_dbus_assert; assert_a_lhs = a_lhs_assert; assert_a_rhs = a_rhs_assert;
  //   assert_addr = addr_assert; assert_b_dbus = b_dbus_assert; assert_b_lhs = b_lhs_assert;
  //   assert_b_rhs = b_rhs_assert; d_lo[7:0] = {d_01, d_00}; d_hi[7:0] = {d_11, d_10}; dbus_lo[3:0] = dbus[3:0];
  //   dbus_hi[3:0] = dbus[7:4]; lhs[7:0] = xfer[15:8]; xfer_10[3:0] = xfer[11:8]; xfer_11[3:0] = xfer[15:12];
  //   load_a_dbus = a_dbus_load; load_b_dbus = b_dbus_load; load_xfer = xfer_load; q_a[7:0] = reg_a; q_b[7:0] = reg_b;
  //   rhs[7:0] = xfer[7:0]; xfer_00[3:0] = xfer[3:0]; xfer_01[3:0] = xfer[7:4]

  // Notes on the sheet:
  //   addr_assert: default 1
  //   xfer_load: default 1
  //   a_dbus_load: default 1
  //   b_dbus_load: default 1
  //   a_dbus_assert: default 1
  //   b_dbus_assert: default 1
  //   a_lhs_assert: default 1
  //   b_lhs_assert: default 1
  //   a_rhs_assert: default 1
  //   b_rhs_assert: default 1
endmodule
