// Digital circuit addr_decoding.dig as structural Verilog
module addr_decoding (
  input  A15,
  input  R_nW,
  input  nCLK,
  output ROM_CS,
  output RAM_CS,
  output WE,
  output OE
);

  wire and_2_out, not_1_out, not_2_out, or_1_out;

  not not_1 (not_1_out, R_nW);
  not not_2 (not_2_out, A15);
  and and_1 (ROM_CS, not_2_out, R_nW);
  and and_2 (and_2_out, A15, not_1_out);
  and and_3 (OE, A15, R_nW);
  or or_1 (or_1_out, R_nW, nCLK);
  and and_4 (WE, and_2_out, or_1_out);

  assign RAM_CS = A15;
endmodule
