// Digital circuit address_adder.dig as structural Verilog
module address_adder (
  input  [15:0] Address_In,
  input  [7:0] Offset,
  input  Cin
);

  wire _74ls283_2_c_out, _74ls283_3_c_out, _74ls283_4_c_out, multiplexer_1_out;
  wire [3:0] bitextender_1_out;

  Multiplexer multiplexer_1 (.in_0(1'b0), .in_1(Offset[7]), .out(multiplexer_1_out));  // open: sel
  BitExtender #(.inputBits(1), .outputBits(4)) bitextender_1 (.in(multiplexer_1_out), .out(bitextender_1_out));
  _74ls283 _74ls283_1 (
    .A(Address_In[15:12]), .B(bitextender_1_out), .C_in(_74ls283_2_c_out), .VCC(1'b1), .GND(1'b0));  // open: S, C_out
  _74ls283 _74ls283_2 (
    .A(Address_In[11:8]), .B(bitextender_1_out), .C_in(_74ls283_3_c_out), .VCC(1'b1), .GND(1'b0),
    .C_out(_74ls283_2_c_out));  // open: S
  _74ls283 _74ls283_3 (
    .A(Address_In[7:4]), .B(Offset[7:4]), .C_in(_74ls283_4_c_out), .VCC(1'b1), .GND(1'b0),
    .C_out(_74ls283_3_c_out));  // open: S
  _74ls283 _74ls283_4 (
    .A(Address_In[3:0]), .B(Offset[3:0]), .C_in(Cin), .VCC(1'b1), .GND(1'b0), .C_out(_74ls283_4_c_out));  // open: S
endmodule
