// Digital circuit address_decoding_experiment.dig as structural Verilog
module address_decoding_experiment (
  input  [15:0] AddrBus,
  input  CLK,
  input  [7:0] MemBus,
  input  [7:0] R_nW,
  output [20:0] Physical_Address,
  output MMIO_Region
);

  wire and_1_out, decoder_1_out_0, decoder_1_out_1, decoder_1_out_2, decoder_1_out_3, decoder_1_out_4,
       decoder_1_out_5, decoder_1_out_6, decoder_1_out_7, nand_1_out, sel_dev0, sel_dev1, sel_dev2, sel_dev3,
       sel_dev4, sel_dev5, sel_dev6, sel_dev7, sel_dev8, sel_dev9, sel_dev10, sel_dev11, sel_dev12,
       sel_dev13, sel_dev14, sel_dev15;
  wire [2:0] VRAM_Bank_Select_q;
  wire [3:0] decoder_3_out_0, multiplexer_1_out;
  wire [7:0] Bank_0_Select_q, Bank_1_Select_q;
  wire [7:3] VRAM_Bank_Select_q_2;

  Register #(.Bits(8)) Bank_0_Select (.D(MemBus), .C(CLK), .en(1'b0), .Q(Bank_0_Select_q));
  Register #(.Bits(8)) Bank_1_Select (.D(MemBus), .C(CLK), .en(1'b0), .Q(Bank_1_Select_q));
  Register #(.Bits(8)) VRAM_Bank_Select (
    .D(MemBus), .C(CLK), .en(1'b0), .Q({VRAM_Bank_Select_q_2, VRAM_Bank_Select_q}));
  Decoder #(.Selector_Bits(3)) decoder_1 (
    .sel(AddrBus[15:13]), .out_0(decoder_1_out_0), .out_1(decoder_1_out_1), .out_2(decoder_1_out_2),
    .out_3(decoder_1_out_3), .out_4(decoder_1_out_4), .out_5(decoder_1_out_5), .out_6(decoder_1_out_6),
    .out_7(decoder_1_out_7));
  and and_1 (and_1_out, AddrBus[12], AddrBus[11], AddrBus[10], AddrBus[9], AddrBus[8]);
  nand nand_1 (nand_1_out, and_1_out, decoder_1_out_0);
  assign Physical_Address[20:13] = nand_1_out ? {8{1'b0}} : 8'bz;  // Driver driver_1
  assign Physical_Address[20:13] = decoder_1_out_1 ? 8'h1 : 8'bz;  // Driver driver_2
  assign Physical_Address[20:13] = decoder_1_out_2 ? 8'h2 : 8'bz;  // Driver driver_3
  assign Physical_Address[20:13] = decoder_1_out_3 ? 8'h3 : 8'bz;  // Driver driver_4
  assign Physical_Address[20:13] = decoder_1_out_4 ? 8'h4 : 8'bz;  // Driver driver_5
  assign Physical_Address[20:13] = decoder_1_out_5 ? Bank_0_Select_q : 8'bz;  // Driver driver_6
  assign Physical_Address[20:13] = decoder_1_out_6 ? Bank_1_Select_q : 8'bz;  // Driver driver_7
  assign Physical_Address[20:13] = decoder_1_out_7 ? {{5{1'b1}}, VRAM_Bank_Select_q} : 8'bz;  // Driver driver_8
  not not_1 (MMIO_Region, nand_1_out);
  Decoder #(.Selector_Bits(4)) decoder_2 (
    .sel(AddrBus[7:4]), .out_0(sel_dev0), .out_1(sel_dev1), .out_2(sel_dev2), .out_3(sel_dev3),
    .out_4(sel_dev4), .out_5(sel_dev5), .out_6(sel_dev6), .out_7(sel_dev7), .out_8(sel_dev8),
    .out_9(sel_dev9), .out_10(sel_dev10), .out_11(sel_dev11), .out_12(sel_dev12), .out_13(sel_dev13),
    .out_14(sel_dev14), .out_15(sel_dev15));
  Decoder #(.Selector_Bits(2)) decoder_3 (
    .sel(Physical_Address[20:19]), .out_0(decoder_3_out_0[0]), .out_1(decoder_3_out_0[1]),
    .out_2(decoder_3_out_0[2]), .out_3(decoder_3_out_0[3]));
  Multiplexer #(.Bits(4)) multiplexer_1 (
    .sel(MMIO_Region), .in_0(decoder_3_out_0), .in_1(4'b0000), .out(multiplexer_1_out));
  RAMSinglePortSel #(.AddrBits(19), .Bits(8)) ramsingleportsel_1 (
    .A({Physical_Address[18:13], AddrBus[12:0]}), .CS(multiplexer_1_out[0]), .WE(1'b0), .OE(1'b0),
    .D({8{1'b0}}));
  RAMSinglePortSel #(.AddrBits(19), .Bits(8)) ramsingleportsel_2 (
    .A({Physical_Address[18:13], AddrBus[12:0]}), .CS(multiplexer_1_out[1]), .WE(1'b0), .OE(1'b0),
    .D({8{1'b0}}));
  RAMSinglePortSel #(.AddrBits(19), .Bits(8)) ramsingleportsel_3 (
    .A({Physical_Address[18:13], AddrBus[12:0]}), .CS(multiplexer_1_out[2]), .WE(1'b0), .OE(1'b0),
    .D({8{1'b0}}));
  RAMSinglePortSel #(.AddrBits(19), .Bits(8)) ramsingleportsel_4 (
    .A({Physical_Address[18:13], AddrBus[12:0]}), .CS(multiplexer_1_out[3]), .WE(1'b0), .OE(1'b0),
    .D({8{1'b0}}));

  assign Physical_Address[12:0] = AddrBus[12:0];

  // Other names for the same wires on the sheet: sel_io_reg[3:0] = AddrBus[3:0]; data[7:0] = MemBus
endmodule
