// Digital circuit address_offset.dig as structural Verilog
module address_offset (
  input  [7:0] dbus,
  input  [15:0] addr_in,
  input  noffset_en,
  input  carry_en,
  input  naddr_xfer_assert,
  input  nassert_addr,
  input  clr,
  input  noffset_load,
  input  nclock,
  input  R_nW,
  input  MEM_nIO,
  input  D_nC,
  input  nACK,
  input  nload_br,
  input  nassert_br,
  input  U_nS,
  input  UBR_f,
  output [19:0] addr_out,
  output [15:0] xfer,
  output [7:0] q,
  output R_nW_z,
  output MEM_nIO_z,
  output D_nC_z
);

  wire and_1_out, not_1_out;
  wire [3:0] _74ls173_1_p10, bank_sel, multiplexer_2_out;
  wire [7:0] multiplexer_1_out;
  wire [7:7] undriven;
  wire [15:0] add_1_s, bitextender_1_out;

  not not_1 (not_1_out, nACK);
  // _74ls173 _74ls173_1: pin names not known; wires that end beside it: dbus[3:0], clr, nclock, nload_br, nload_br, 1'b0, 1'b0, 1'b1, 1'b0, _74ls173_1_p10
  // _74ls173 _74ls173_2: pin names not known; wires that end beside it: dbus[3:0], clr, nclock, noffset_load, noffset_load, 1'b0, 1'b0, 1'b1, 1'b0, q[3:0]
  // _74ls173 _74ls173_3: pin names not known; wires that end beside it: dbus[7:4], clr, nclock, noffset_load, noffset_load, 1'b0, 1'b0, 1'b1, 1'b0, q[7:4]
  _74ls245 _74ls245_1 (
    .DIR(1'b1), .nOE(not_1_out), .A({1'b0, bank_sel, D_nC, MEM_nIO, R_nW}),
    .B({undriven[7], addr_out[19:16], D_nC_z, MEM_nIO_z, R_nW_z}), .VCC(1'b1), .GND(1'b0));
  Multiplexer #(.Bits(8)) multiplexer_1 (.sel(noffset_en), .in_0(q), .in_1({8{1'b0}}), .out(multiplexer_1_out));
  BitExtender bitextender_1 (.in(multiplexer_1_out), .out(bitextender_1_out));
  Multiplexer #(.Bits(4)) multiplexer_2 (.sel(U_nS), .in_0(_74ls173_1_p10), .in_1(4'b0000), .out(multiplexer_2_out));
  and and_1 (and_1_out, UBR_f, D_nC);
  Add #(.Bits(16)) add_1 (.a(addr_in), .b(bitextender_1_out), .c_i(carry_en), .s(add_1_s));  // open: c_o
  _74ls245 _74ls245_2 (
    .DIR(1'b1), .nOE(nassert_br), .A({_74ls173_1_p10, _74ls173_1_p10}), .B(dbus), .VCC(1'b1), .GND(1'b0));
  Multiplexer #(.Bits(4)) multiplexer_3 (
    .sel(and_1_out), .in_0(multiplexer_2_out), .in_1(_74ls173_1_p10), .out(bank_sel));
  _74ls245 _74ls245_3 (.DIR(1'b1), .nOE(naddr_xfer_assert), .A(add_1_s[7:0]), .B(xfer[7:0]), .VCC(1'b1), .GND(1'b0));
  _74ls245 _74ls245_4 (.DIR(1'b1), .nOE(naddr_xfer_assert), .A(add_1_s[15:8]), .B(xfer[15:8]), .VCC(1'b1), .GND(1'b0));
  _74ls245 _74ls245_5 (.DIR(1'b1), .nOE(nassert_addr), .A(add_1_s[7:0]), .B(addr_out[7:0]), .VCC(1'b1), .GND(1'b0));
  _74ls245 _74ls245_6 (.DIR(1'b1), .nOE(nassert_addr), .A(add_1_s[15:8]), .B(addr_out[15:8]), .VCC(1'b1), .GND(1'b0));

  // Other names for the same wires on the sheet: bank_sel_z[3:0] = addr_out[19:16]; offset[7:0] = q;
  //   addr_16[15:0] = addr_out[15:0]; dlo[3:0] = dbus[3:0]; nclk = nclock; nload = noffset_load
endmodule
