// Digital circuit address_register.dig as structural Verilog
module address_register (
  input  clk,
  input  clr,
  input  inc,
  input  dec,
  input  xfer_load,
  input  addr_assert,
  input  xfer_assert,
  input  dbus_load_hi,
  input  dbus_load_lo,
  input  [7:0] dbus,
  output [15:0] addr,
  output [15:0] xfer,
  output [15:0] \reg 
);

  wire _74193_1_p11, _74193_1_p12, _74193_2_p11, _74193_2_p12, _74193_3_p11, _74193_3_p12, in0, in1, in2,
       in3, in4, in5, in6, in7, in8, in9, in10, in11, in12, in13, in14, in15, load_control_p5,
       load_control_p6, load_control_p7, load_control_p8, load_hi, load_lo, xfer0, xfer1, xfer2, xfer3,
       xfer4, xfer5, xfer6, xfer7, xfer8, xfer9, xfer10, xfer11, xfer12, xfer13, xfer14, xfer15;

  BusSplitter #(.Bits(16)) bussplitter_1 (
    .D(xfer), .OE(xfer_assert), .D0(xfer0), .D1(xfer1), .D2(xfer2), .D3(xfer3), .D4(xfer4), .D5(xfer5),
    .D6(xfer6), .D7(xfer7), .D8(xfer8), .D9(xfer9), .D10(xfer10), .D11(xfer11), .D12(xfer12), .D13(xfer13),
    .D14(xfer14), .D15(xfer15));
  // _7408 load_control: pin names not known; wires that end beside it: xfer_load, dbus_load_hi, xfer_load, dbus_load_lo, load_control_p5, load_control_p6, load_control_p7, load_control_p8, 1'b1, 1'b0, load_hi, load_lo
  // NotConnected on load_control_p5
  // NotConnected on load_control_p6
  // NotConnected on load_control_p7
  // NotConnected on load_control_p8
  _74ls157 Nibble_3_MUX (
    .S(dbus_load_hi), .A(dbus[7:4]), .B({xfer15, xfer14, xfer13, xfer12}), .G(1'b0), .VCC(1'b1), .GND(1'b0),
    .Y({in15, in14, in13, in12}));
  // _74574 _74574_1: pin names not known; wires that end beside it: xfer_assert, clk, \reg [8], \reg [9], \reg [10], \reg [11], \reg [12], \reg [13], \reg [14], \reg [15], 1'b1, 1'b0, xfer8, xfer9, xfer10, xfer11, xfer12, xfer13, xfer14, xfer15
  // _74193 _74193_1: pin names not known; wires that end beside it: in0, dec, inc, in1, in2, in3, clr, load_lo, 1'b1, 1'b0, _74193_1_p11, _74193_1_p12, \reg [0], \reg [1], \reg [2], \reg [3]
  _74ls157 Nibble_2_MUX (
    .S(dbus_load_hi), .A(dbus[3:0]), .B({xfer11, xfer10, xfer9, xfer8}), .G(1'b0), .VCC(1'b1), .GND(1'b0),
    .Y({in11, in10, in9, in8}));
  // _74574 _74574_2: pin names not known; wires that end beside it: xfer_assert, clk, \reg [0], \reg [1], \reg [2], \reg [3], \reg [4], \reg [5], \reg [6], \reg [7], 1'b1, 1'b0, xfer0, xfer1, xfer2, xfer3, xfer4, xfer5, xfer6, xfer7
  // _74193 _74193_2: pin names not known; wires that end beside it: in4, _74193_1_p11, _74193_1_p12, in5, in6, in7, clr, load_lo, 1'b1, 1'b0, _74193_2_p11, _74193_2_p12, \reg [4], \reg [5], \reg [6], \reg [7]
  _74ls157 Nibble_1_MUX (
    .S(dbus_load_lo), .A(dbus[7:4]), .B({xfer7, xfer6, xfer5, xfer4}), .G(1'b0), .VCC(1'b1), .GND(1'b0),
    .Y({in7, in6, in5, in4}));
  // _74574 _74574_3: pin names not known; wires that end beside it: addr_assert, clk, \reg [8], \reg [9], \reg [10], \reg [11], \reg [12], \reg [13], \reg [14], \reg [15], 1'b1, 1'b0, addr[8], addr[9], addr[10], addr[11], addr[12], addr[13], addr[14], addr[15]
  // _74193 _74193_3: pin names not known; wires that end beside it: in8, _74193_2_p11, _74193_2_p12, in9, in10, in11, clr, load_hi, 1'b1, 1'b0, _74193_3_p11, _74193_3_p12, \reg [8], \reg [9], \reg [10], \reg [11]
  _74ls157 Nibble_0_MUX (
    .S(dbus_load_lo), .A(dbus[3:0]), .B({xfer3, xfer2, xfer1, xfer0}), .G(1'b0), .VCC(1'b1), .GND(1'b0),
    .Y({in3, in2, in1, in0}));
  // _74574 _74574_4: pin names not known; wires that end beside it: addr_assert, clk, \reg [0], \reg [1], \reg [2], \reg [3], \reg [4], \reg [5], \reg [6], \reg [7], 1'b1, 1'b0, addr[0], addr[1], addr[2], addr[3], addr[4], addr[5], addr[6], addr[7]
  // _74193 _74193_4: pin names not known; wires that end beside it: in12, _74193_3_p11, _74193_3_p12, in13, in14, in15, clr, load_hi, 1'b1, 1'b0, \reg [12], \reg [13], \reg [14], \reg [15]

  // Other names for the same wires on the sheet: d0 = dbus[0]; d1 = dbus[1]; d2 = dbus[2]; d3 = dbus[3]; d4 = dbus[4];
  //   d5 = dbus[5]; d6 = dbus[6]; d7 = dbus[7]; q0 = \reg [0]; q1 = \reg [1]; q2 = \reg [2]; q3 = \reg [3];
  //   q4 = \reg [4]; q5 = \reg [5]; q6 = \reg [6]; q7 = \reg [7]; q8 = \reg [8]; q9 = \reg [9]; q10 = \reg [10];
  //   q11 = \reg [11]; q12 = \reg [12]; q13 = \reg [13]; q14 = \reg [14]; q15 = \reg [15]

  // Notes on the sheet:
  //   clr: default 1
  //   xfer_load: default 1
  //   addr_assert: default 1
  //   xfer_assert: default 1
  //   dbus_load_hi: default 1
  //   dbus_load_lo: default 1
endmodule
