// Digital circuit alu.dig as structural Verilog
module alu (
  input  [4:0] ALU_OP,
  input  LOAD_SR_DBUS,
  input  ASSERT_SR_DBUS,
  input  CLK,
  input  CLR,
  input  [7:0] LHS,
  input  [7:0] RHS,
  input  ASSERT_ALU_DBUS,
  output [4:0] FLAGS,
  output [7:0] DBUS
);

  wire _74ls260_1__1y, _74ls260_1__2y, C_fnew, c_shift, c_sum, I_fnew, N, N_fnew, nC_f,
       Negative_Flag_Select_p8, Negative_Flag_Select_p9, Negative_Flag_Select_p10, Negative_Flag_Select_p11,
       Negative_Flag_Select_p12, notconnected_1_out, notconnected_2_out, notconnected_3_out,
       notconnected_4_out, notconnected_10_out, notconnected_11_out, notconnected_12_out,
       notconnected_13_out, notconnected_14_out, notconnected_15_out, notconnected_16_out,
       notconnected_17_out, notconnected_18_out, notconnected_19_out, Overflow_Flag_Select_p8,
       Overflow_Flag_Select_p9, Overflow_Flag_Select_p10, Overflow_Flag_Select_p11, Overflow_Flag_Select_p12,
       s0, s1, s2, s3, s4, s5, s6, sel_cf_0, sel_cf_1, sel_cf_2, sel_if_0, sel_if_1, sel_nf_0, sel_nf_1,
       sel_vf_0, sel_vf_1, sel_zf_0, sel_zf_1, V, V_fnew, Z, Z_fnew;
  wire [1:0] sel_sum;
  wire [2:0] sel_shift;
  wire [3:0] sel_logic;
  wire [7:0] A, B;
  wire [7:5] Status_Register_flags;

  LED Interrupt_Inhibit (.in(FLAGS[0]));
  LED Negative__Sign (.in(FLAGS[1]));
  LED Overflow (.in(FLAGS[2]));
  LED Zero (.in(FLAGS[3]));
  LED Carry___Borrow (.in(FLAGS[4]));
  alu_diode_matrix Diode_Matrix_Decoder (
    .A(FLAGS[4]), .B(notconnected_1_out), .C(notconnected_2_out), .D(notconnected_3_out),
    .E(notconnected_4_out), .ALU_OP(ALU_OP), .Sel_Cin_0(sel_sum[0]), .Sel_Cin_1(sel_sum[1]),
    .Sel_Shift_0(sel_shift[0]), .Sel_Shift_1(sel_shift[1]), .Sel_Shift_2(sel_shift[2]),
    .Sel_Logic_0(sel_logic[0]), .Sel_Logic_1(sel_logic[1]), .Sel_Logic_2(sel_logic[2]),
    .Sel_Logic_3(sel_logic[3]), .Sel_Cf_0(sel_cf_0), .Sel_Cf_1(sel_cf_1), .Sel_Cf_2(sel_cf_2),
    .Sel_Zf_0(sel_zf_0), .Sel_Zf_1(sel_zf_1), .Sel_Vf_0(sel_vf_0), .Sel_Vf_1(sel_vf_1), .Sel_Nf_0(sel_nf_0),
    .Sel_Nf_1(sel_nf_1), .Sel_If_0(sel_if_0), .Sel_If_1(sel_if_1), .nA(nC_f));  // open: nB, nC, nD, nE
  // NotConnected on notconnected_1_out
  // NotConnected on notconnected_2_out
  // NotConnected on notconnected_3_out
  // NotConnected on notconnected_4_out
  // _74151 Carry_Flag_Select: pin names not known; wires that end beside it: sel_cf_0, sel_cf_2, sel_cf_1, 1'b0, 1'b1, c_shift, c_sum, 1'b0, FLAGS[4], FLAGS[4], FLAGS[4], FLAGS[4], 1'b1, 1'b0, C_fnew
  // _74153 Negative_Flag_Select: pin names not known; wires that end beside it: sel_nf_0, sel_nf_1, 1'b0, 1'b1, N, 1'b0, FLAGS[1], Negative_Flag_Select_p8, Negative_Flag_Select_p9, Negative_Flag_Select_p10, Negative_Flag_Select_p11, Negative_Flag_Select_p12, 1'b1, 1'b0, N_fnew
  // NotConnected on Negative_Flag_Select_p8
  // NotConnected on Negative_Flag_Select_p9
  // NotConnected on Negative_Flag_Select_p10
  // NotConnected on Negative_Flag_Select_p11
  // NotConnected on Negative_Flag_Select_p12
  // NotConnected on notconnected_10_out
  // NotConnected on notconnected_11_out
  // NotConnected on notconnected_12_out
  // NotConnected on notconnected_13_out
  // NotConnected on notconnected_14_out
  // NotConnected on notconnected_15_out
  // NotConnected on notconnected_16_out
  // NotConnected on notconnected_17_out
  // NotConnected on notconnected_18_out
  // NotConnected on notconnected_19_out
  // _74153 Zero_Flag_Select: pin names not known; wires that end beside it: sel_zf_0, sel_zf_1, 1'b0, 1'b1, Z, 1'b0, FLAGS[3], notconnected_10_out, notconnected_11_out, notconnected_12_out, notconnected_13_out, notconnected_14_out, 1'b1, 1'b0, Z_fnew
  // _74153 Interrupt_Flag_Select: pin names not known; wires that end beside it: sel_if_0, sel_if_1, 1'b0, 1'b1, 1'b0, 1'b0, FLAGS[0], notconnected_15_out, notconnected_16_out, notconnected_17_out, notconnected_18_out, notconnected_19_out, 1'b1, 1'b0, I_fnew
  // _74153 Overflow_Flag_Select: pin names not known; wires that end beside it: sel_vf_0, sel_vf_1, 1'b0, 1'b1, V, 1'b0, FLAGS[2], Overflow_Flag_Select_p8, Overflow_Flag_Select_p9, Overflow_Flag_Select_p10, Overflow_Flag_Select_p11, Overflow_Flag_Select_p12, 1'b1, 1'b0, V_fnew
  // NotConnected on Overflow_Flag_Select_p8
  // NotConnected on Overflow_Flag_Select_p9
  // NotConnected on Overflow_Flag_Select_p10
  // NotConnected on Overflow_Flag_Select_p11
  // NotConnected on Overflow_Flag_Select_p12
  alu_arithmetic_unit alu_arithmetic_unit_1 (
    .left(A), .right(B), .sum_func_sel(sel_sum), .C_f(FLAGS[4]), .nC_f(nC_f), .C_fout(c_sum),
    .sum({N, s6, s5, s4, s3, s2, s1, s0}));
  alu_shift_unit alu_shift_unit_1 (.shift_func_sel(sel_shift), .lhs(LHS), .C_fin(FLAGS[4]), .Q(A), .C_fout(c_shift));
  alu_status_register Status_Register (
    .DBUS(DBUS), .ALU({3'b000, C_fnew, Z_fnew, V_fnew, N_fnew, I_fnew}), .CLR(CLR), .CLK(CLK),
    .ASSERT(ASSERT_SR_DBUS), .LOAD_DBUS(LOAD_SR_DBUS), .flags({Status_Register_flags, FLAGS}));
  alu_logic_unit alu_logic_unit_1 (.logic_func_sel(sel_logic), .rhs(RHS), .lhs(LHS), .Q(B));
  _74ls245 _74ls245_1 (
    .DIR(1'b1), .nOE(ASSERT_ALU_DBUS), .A({N, s6, s5, s4, s3, s2, s1, s0}), .B(DBUS), .VCC(1'b1), .GND(1'b0));
  _74ls260 _74ls260_1 (
    ._1A(s0), ._2A(s1), ._3A(s2), ._4A(s3), ._5A(1'b0), ._1B(s4), ._2B(s5), ._3B(s6), ._4B(N), ._5B(1'b0),
    .VCC(1'b1), .GND(1'b0), ._1Y(_74ls260_1__1y), ._2Y(_74ls260_1__2y));
  // _74151 _74151_1: pin names not known; wires that end beside it: 1'b0, 1'b1, RHS[7], N, LHS[7], 1'b0, 1'b0, 1'b0, 1'b0, 1'b1, 1'b1, 1'b0, 1'b0, 1'b0, 1'b1, 1'b0, V
  // _7408 _7408_1: pin names not known; wires that end beside it: _74ls260_1__1y, _74ls260_1__2y, 1'b0, 1'b0, 1'b0, 1'b0, 1'b0, 1'b0, 1'b1, 1'b0, Z, 1'b0, 1'b0, 1'b0

  // Other names for the same wires on the sheet: s7 = N; I_f = FLAGS[0]; N_f = FLAGS[1]; V_f = FLAGS[2];
  //   Z_f = FLAGS[3]; C_f = FLAGS[4]; assert_alu = ASSERT_ALU_DBUS; assert_sr = ASSERT_SR_DBUS; load = LOAD_SR_DBUS

  // Notes on the sheet:
  //   LOAD_SR_DBUS: default 1
  //   ASSERT_SR_DBUS: default 1
  //   ASSERT_ALU_DBUS: default 1
  //   Determine what ALU Contributes to SR
  //   Status Register (Dual Source Register)
  //   ALU Core with DBUS Output
  //   Zero Flag Determination
  //   Sign (Negative) Flag Determination
  //   Overflow Flag Determination
endmodule

/* Test case ADD:
CLK ALU-OP LHS RHS  DBUS FLAGS   LOAD-SR-DBUS ASSERT-SR-DBUS ASSERT-ALU-DBUS CLR
C    4       0   0    0  0b01000            1              1               0   0
C    4       0   1    1  0b00000            1              1               0   0
C    4       1   0    1  0b00000            1              1               0   0
C    4       3   4    7  0b00000            1              1               0   0
C    4       4   3    7  0b00000            1              1               0   0
C    4     255   0  255  0b00010            1              1               0   0
C    4     255   1    0  0b11000            1              1               0   0
C    4     128 128    0  0b11100            1              1               0   0
*/

/* Test case ADC:
CLK ALU-OP LHS RHS  DBUS FLAGS   LOAD-SR-DBUS ASSERT-SR-DBUS ASSERT-ALU-DBUS CLR
C    5       0   0    0  0b01000            1              1               0   0
C    5       0   1    1  0b00000            1              1               0   0
C    5       1   0    1  0b00000            1              1               0   0
C    5       3   4    7  0b00000            1              1               0   0
C    5       4   3    7  0b00000            1              1               0   0
C    5     255   0  255  0b00010            1              1               0   0
C    5     255   1    0  0b11000            1              1               0   0
C    5     128 128    1  0b00000            1              1               0   0
*/
