// Digital circuit alu_decoder_unit.dig as structural Verilog
module alu_decoder_unit (
  input  [4:0] encoded,
  output out_1,
  output out_2,
  output out_3,
  output out_4,
  output out_5,
  output out_6,
  output out_7,
  output out_8,
  output out_9,
  output out_10,
  output out_11,
  output out_12,
  output out_13,
  output out_14,
  output out_15,
  output out_16,
  output out_17,
  output out_18,
  output out_19,
  output out_20,
  output out_21,
  output out_22,
  output out_23,
  output out_24,
  output out_25,
  output out_26,
  output out_27,
  output out_28,
  output out_29,
  output out_30,
  output out_31,
  output out_32
);

  wire not_1_out;

  not not_1 (not_1_out, encoded[4]);
  // _74154 _74154_1: pin names not known; wires that end beside it: encoded[0], encoded[2], encoded[1], encoded[3], 1'b0, encoded[4], 1'b1, 1'b0, out_1, out_2, out_3, out_4, out_5, out_6, out_7, out_8, out_9, out_10, out_11, out_12, out_13, out_14, out_15
  // _74154 _74154_2: pin names not known; wires that end beside it: encoded[0], encoded[2], encoded[1], encoded[3], 1'b0, not_1_out, 1'b1, 1'b0, out_16, out_17, out_18, out_19, out_20, out_21, out_22, out_23, out_24, out_25, out_26, out_27, out_28, out_29, out_30, out_31, out_32
endmodule
