// Digital circuit alu_diode_matrix.dig as structural Verilog
module alu_diode_matrix (
  input  A,
  input  B,
  input  C,
  input  D,
  input  E,
  input  [4:0] ALU_OP,
  output Sel_Cin_0,
  output Sel_Cin_1,
  output Sel_Shift_0,
  output Sel_Shift_1,
  output Sel_Shift_2,
  output Sel_Logic_0,
  output Sel_Logic_1,
  output Sel_Logic_2,
  output Sel_Logic_3,
  output Sel_Cf_0,
  output Sel_Cf_1,
  output Sel_Cf_2,
  output Sel_Zf_0,
  output Sel_Zf_1,
  output Sel_Vf_0,
  output Sel_Vf_1,
  output Sel_Nf_0,
  output Sel_Nf_1,
  output Sel_If_0,
  output Sel_If_1,
  output nA,
  output nB,
  output nC,
  output nD,
  output nE
);

  wire _7404_1_p9, _74154_1_p1, _74154_1_p2, _74154_1_p3, _74154_1_p4, _74154_1_p5, _74154_1_p6, _74154_1_p7,
       _74154_1_p8, _74154_1_p10, _74154_1_p12, _74154_1_p14, _74154_1_p16, _74154_1_p18, _74154_1_p20,
       _74154_1_p22, _74154_1_p24, _74154_1_p25, _74154_1_p26, _74154_1_p27, _74154_1_p28, _74154_1_p29,
       _74154_1_p30, _74154_1_p31, _74154_2_p1, _74154_2_p3, _74154_2_p5, _74154_2_p7, _74154_2_p9,
       _74154_2_p11, _74154_2_p13, _74154_2_p16, _74154_2_p18;

  PullUp pullup_1 (.out(Sel_Cin_0));
  PullUp pullup_2 (.out(Sel_Cin_1));
  PullUp pullup_3 (.out(Sel_Shift_0));
  PullUp pullup_4 (.out(Sel_Shift_1));
  PullUp pullup_5 (.out(Sel_Shift_2));
  PullUp pullup_6 (.out(Sel_Logic_0));
  PullUp pullup_7 (.out(Sel_Logic_1));
  PullUp pullup_8 (.out(Sel_Logic_2));
  PullUp pullup_9 (.out(Sel_Logic_3));
  PullUp pullup_10 (.out(Sel_Cf_0));
  PullUp pullup_11 (.out(Sel_Cf_1));
  PullUp pullup_12 (.out(Sel_Cf_2));
  PullUp pullup_13 (.out(Sel_Zf_0));
  PullUp pullup_14 (.out(Sel_Zf_1));
  PullUp pullup_15 (.out(Sel_Vf_0));
  PullUp pullup_16 (.out(Sel_Vf_1));
  PullUp pullup_17 (.out(Sel_Nf_0));
  PullUp pullup_18 (.out(Sel_Nf_1));
  PullUp pullup_19 (.out(Sel_If_0));
  PullUp pullup_20 (.out(Sel_If_1));
  // _7404 _7404_1: pin names not known; wires that end beside it: ALU_OP[4], A, B, C, D, E, 1'b1, 1'b0, _7404_1_p9, nA, nB, nC, nD, nE
  DiodeBackward diodebackward_1 (.in(_74154_1_p5), .out(Sel_Nf_0));
  DiodeBackward diodebackward_2 (.in(_74154_1_p7), .out(Sel_Zf_0));
  DiodeBackward diodebackward_3 (.in(_74154_1_p6), .out(Sel_Nf_0));
  DiodeBackward diodebackward_4 (.in(_74154_1_p6), .out(Sel_Nf_1));
  DiodeBackward diodebackward_5 (.in(_74154_1_p8), .out(Sel_Zf_0));
  DiodeBackward diodebackward_6 (.in(_74154_1_p8), .out(Sel_Zf_1));
  DiodeBackward diodebackward_7 (.in(_74154_1_p10), .out(Sel_Vf_0));
  DiodeBackward diodebackward_8 (.in(_74154_1_p14), .out(Sel_Cf_2));
  DiodeBackward diodebackward_9 (.in(_74154_1_p12), .out(Sel_Vf_0));
  DiodeBackward diodebackward_10 (.in(_74154_1_p12), .out(Sel_Vf_1));
  DiodeBackward diodebackward_11 (.in(_74154_1_p16), .out(Sel_Cf_0));
  DiodeBackward diodebackward_12 (.in(_74154_1_p16), .out(Sel_Cf_1));
  DiodeBackward diodebackward_13 (.in(_74154_1_p16), .out(Sel_Cf_2));
  DiodeBackward diodebackward_14 (.in(_74154_1_p18), .out(Sel_If_0));
  // _74154 _74154_1: pin names not known; wires that end beside it: _74154_1_p1, _74154_1_p2, _74154_1_p3, _74154_1_p4, _74154_1_p5, _74154_1_p6, _74154_1_p7, _74154_1_p8, 1'b0, _74154_1_p10, 1'b1, _74154_1_p12, 1'b0, _74154_1_p14, _7404_1_p9, _74154_1_p16, ALU_OP[3], _74154_1_p18, ALU_OP[1], _74154_1_p20, ALU_OP[2], _74154_1_p22, ALU_OP[0], _74154_1_p24, _74154_1_p25, _74154_1_p26, _74154_1_p27, _74154_1_p28, _74154_1_p29, _74154_1_p30, _74154_1_p31
  DiodeBackward diodebackward_15 (.in(_74154_1_p22), .out(Sel_Shift_1));
  DiodeBackward diodebackward_16 (.in(_74154_1_p22), .out(Sel_Logic_0));
  DiodeBackward diodebackward_17 (.in(_74154_1_p22), .out(Sel_Logic_1));
  DiodeBackward diodebackward_18 (.in(_74154_1_p22), .out(Sel_Logic_2));
  DiodeBackward diodebackward_19 (.in(_74154_1_p22), .out(Sel_Logic_3));
  DiodeBackward diodebackward_20 (.in(_74154_1_p22), .out(Sel_Cf_1));
  DiodeBackward diodebackward_21 (.in(_74154_1_p22), .out(Sel_Cf_2));
  DiodeBackward diodebackward_22 (.in(_74154_1_p22), .out(Sel_Zf_1));
  DiodeBackward diodebackward_23 (.in(_74154_1_p22), .out(Sel_Nf_1));
  DiodeBackward diodebackward_24 (.in(_74154_1_p20), .out(Sel_If_0));
  DiodeBackward diodebackward_25 (.in(_74154_1_p20), .out(Sel_If_1));
  DiodeBackward diodebackward_26 (.in(_74154_1_p24), .out(Sel_Shift_0));
  DiodeBackward diodebackward_27 (.in(_74154_1_p25), .out(Sel_Shift_2));
  DiodeBackward diodebackward_28 (.in(_74154_1_p24), .out(Sel_Shift_2));
  DiodeBackward diodebackward_29 (.in(_74154_1_p25), .out(Sel_Logic_0));
  DiodeBackward diodebackward_30 (.in(_74154_1_p24), .out(Sel_Logic_0));
  DiodeBackward diodebackward_31 (.in(_74154_1_p25), .out(Sel_Logic_1));
  DiodeBackward diodebackward_32 (.in(_74154_1_p24), .out(Sel_Logic_1));
  DiodeBackward diodebackward_33 (.in(_74154_1_p25), .out(Sel_Logic_2));
  DiodeBackward diodebackward_34 (.in(_74154_1_p24), .out(Sel_Logic_2));
  DiodeBackward diodebackward_35 (.in(_74154_1_p25), .out(Sel_Logic_3));
  DiodeBackward diodebackward_36 (.in(_74154_1_p24), .out(Sel_Logic_3));
  DiodeBackward diodebackward_37 (.in(_74154_1_p25), .out(Sel_Cf_1));
  DiodeBackward diodebackward_38 (.in(_74154_1_p24), .out(Sel_Cf_1));
  DiodeBackward diodebackward_39 (.in(_74154_1_p25), .out(Sel_Cf_2));
  DiodeBackward diodebackward_40 (.in(_74154_1_p24), .out(Sel_Cf_2));
  DiodeBackward diodebackward_41 (.in(_74154_1_p25), .out(Sel_Zf_1));
  DiodeBackward diodebackward_42 (.in(_74154_1_p24), .out(Sel_Zf_1));
  DiodeBackward diodebackward_43 (.in(_74154_1_p25), .out(Sel_Nf_1));
  DiodeBackward diodebackward_44 (.in(_74154_1_p24), .out(Sel_Nf_1));
  DiodeBackward diodebackward_45 (.in(_74154_1_p27), .out(Sel_Logic_0));
  DiodeBackward diodebackward_46 (.in(_74154_1_p26), .out(Sel_Logic_2));
  DiodeBackward diodebackward_47 (.in(_74154_1_p27), .out(Sel_Logic_3));
  DiodeBackward diodebackward_48 (.in(_74154_1_p26), .out(Sel_Logic_3));
  DiodeBackward diodebackward_49 (.in(_74154_1_p27), .out(Sel_Zf_1));
  DiodeBackward diodebackward_50 (.in(_74154_1_p26), .out(Sel_Zf_1));
  DiodeBackward diodebackward_51 (.in(_74154_1_p27), .out(Sel_Nf_1));
  DiodeBackward diodebackward_52 (.in(_74154_1_p26), .out(Sel_Nf_1));
  DiodeBackward diodebackward_53 (.in(_74154_1_p29), .out(Sel_Logic_0));
  DiodeBackward diodebackward_54 (.in(_74154_1_p28), .out(Sel_Logic_0));
  DiodeBackward diodebackward_55 (.in(_74154_1_p29), .out(Sel_Logic_1));
  DiodeBackward diodebackward_56 (.in(_74154_1_p29), .out(Sel_Logic_2));
  DiodeBackward diodebackward_57 (.in(_74154_1_p29), .out(Sel_Zf_1));
  DiodeBackward diodebackward_58 (.in(_74154_1_p28), .out(Sel_Zf_1));
  DiodeBackward diodebackward_59 (.in(_74154_1_p29), .out(Sel_Nf_1));
  DiodeBackward diodebackward_60 (.in(_74154_1_p28), .out(Sel_Nf_1));
  DiodeBackward diodebackward_61 (.in(_74154_1_p31), .out(Sel_Cin_0));
  DiodeBackward diodebackward_62 (.in(_74154_1_p30), .out(Sel_Shift_0));
  DiodeBackward diodebackward_63 (.in(_74154_1_p30), .out(Sel_Shift_1));
  DiodeBackward diodebackward_64 (.in(_74154_1_p30), .out(Sel_Shift_2));
  DiodeBackward diodebackward_65 (.in(_74154_1_p31), .out(Sel_Logic_0));
  DiodeBackward diodebackward_66 (.in(_74154_1_p31), .out(Sel_Logic_1));
  DiodeBackward diodebackward_67 (.in(_74154_1_p31), .out(Sel_Cf_0));
  DiodeBackward diodebackward_68 (.in(_74154_1_p30), .out(Sel_Cf_0));
  DiodeBackward diodebackward_69 (.in(_74154_1_p31), .out(Sel_Cf_2));
  DiodeBackward diodebackward_70 (.in(_74154_1_p30), .out(Sel_Cf_2));
  DiodeBackward diodebackward_71 (.in(_74154_1_p31), .out(Sel_Zf_1));
  DiodeBackward diodebackward_72 (.in(_74154_1_p30), .out(Sel_Zf_1));
  DiodeBackward diodebackward_73 (.in(_74154_1_p31), .out(Sel_Nf_1));
  DiodeBackward diodebackward_74 (.in(_74154_1_p30), .out(Sel_Nf_1));
  // _74154 _74154_2: pin names not known; wires that end beside it: _74154_2_p1, 1'b0, _74154_2_p3, 1'b1, _74154_2_p5, 1'b0, _74154_2_p7, ALU_OP[4], _74154_2_p9, ALU_OP[3], _74154_2_p11, ALU_OP[1], _74154_2_p13, ALU_OP[1], ALU_OP[2], _74154_2_p16, ALU_OP[0], _74154_2_p18
  DiodeBackward diodebackward_75 (.in(_74154_2_p3), .out(Sel_Cin_0));
  DiodeBackward diodebackward_76 (.in(_74154_2_p1), .out(Sel_Cin_0));
  DiodeBackward diodebackward_77 (.in(_74154_2_p3), .out(Sel_Cin_1));
  DiodeBackward diodebackward_78 (.in(_74154_2_p3), .out(Sel_Shift_0));
  DiodeBackward diodebackward_79 (.in(_74154_2_p3), .out(Sel_Shift_1));
  DiodeBackward diodebackward_80 (.in(_74154_2_p3), .out(Sel_Shift_2));
  DiodeBackward diodebackward_81 (.in(_74154_2_p3), .out(Sel_Logic_2));
  DiodeBackward diodebackward_82 (.in(_74154_2_p1), .out(Sel_Logic_2));
  DiodeBackward diodebackward_83 (.in(_74154_2_p3), .out(Sel_Logic_3));
  DiodeBackward diodebackward_84 (.in(_74154_2_p1), .out(Sel_Logic_3));
  DiodeBackward diodebackward_85 (.in(_74154_2_p3), .out(Sel_Cf_0));
  DiodeBackward diodebackward_86 (.in(_74154_2_p3), .out(Sel_Cf_2));
  DiodeBackward diodebackward_87 (.in(_74154_2_p3), .out(Sel_Zf_1));
  DiodeBackward diodebackward_88 (.in(_74154_2_p3), .out(Sel_Vf_1));
  DiodeBackward diodebackward_89 (.in(_74154_2_p3), .out(Sel_Nf_1));
  DiodeBackward diodebackward_90 (.in(_74154_2_p5), .out(Sel_Cin_0));
  DiodeBackward diodebackward_91 (.in(_74154_2_p7), .out(Sel_Cin_1));
  DiodeBackward diodebackward_92 (.in(_74154_2_p7), .out(Sel_Shift_0));
  DiodeBackward diodebackward_93 (.in(_74154_2_p5), .out(Sel_Shift_0));
  DiodeBackward diodebackward_94 (.in(_74154_2_p7), .out(Sel_Shift_1));
  DiodeBackward diodebackward_95 (.in(_74154_2_p5), .out(Sel_Shift_1));
  DiodeBackward diodebackward_96 (.in(_74154_2_p7), .out(Sel_Shift_2));
  DiodeBackward diodebackward_97 (.in(_74154_2_p5), .out(Sel_Shift_2));
  DiodeBackward diodebackward_98 (.in(_74154_2_p7), .out(Sel_Logic_0));
  DiodeBackward diodebackward_99 (.in(_74154_2_p7), .out(Sel_Logic_1));
  DiodeBackward diodebackward_100 (.in(_74154_2_p5), .out(Sel_Logic_2));
  DiodeBackward diodebackward_101 (.in(_74154_2_p5), .out(Sel_Logic_3));
  DiodeBackward diodebackward_102 (.in(_74154_2_p7), .out(Sel_Cf_0));
  DiodeBackward diodebackward_103 (.in(_74154_2_p5), .out(Sel_Cf_0));
  DiodeBackward diodebackward_104 (.in(_74154_2_p7), .out(Sel_Cf_2));
  DiodeBackward diodebackward_105 (.in(_74154_2_p5), .out(Sel_Cf_2));
  DiodeBackward diodebackward_106 (.in(_74154_2_p7), .out(Sel_Zf_1));
  DiodeBackward diodebackward_107 (.in(_74154_2_p5), .out(Sel_Zf_1));
  DiodeBackward diodebackward_108 (.in(_74154_2_p7), .out(Sel_Vf_1));
  DiodeBackward diodebackward_109 (.in(_74154_2_p5), .out(Sel_Vf_1));
  DiodeBackward diodebackward_110 (.in(_74154_2_p7), .out(Sel_Nf_1));
  DiodeBackward diodebackward_111 (.in(_74154_2_p5), .out(Sel_Nf_1));
  DiodeBackward diodebackward_112 (.in(_74154_2_p11), .out(Sel_Cin_1));
  DiodeBackward diodebackward_113 (.in(_74154_2_p11), .out(Sel_Shift_0));
  DiodeBackward diodebackward_114 (.in(_74154_2_p9), .out(Sel_Shift_0));
  DiodeBackward diodebackward_115 (.in(_74154_2_p11), .out(Sel_Shift_1));
  DiodeBackward diodebackward_116 (.in(_74154_2_p9), .out(Sel_Shift_1));
  DiodeBackward diodebackward_117 (.in(_74154_2_p11), .out(Sel_Shift_2));
  DiodeBackward diodebackward_118 (.in(_74154_2_p9), .out(Sel_Shift_2));
  DiodeBackward diodebackward_119 (.in(_74154_2_p11), .out(Sel_Logic_0));
  DiodeBackward diodebackward_120 (.in(_74154_2_p9), .out(Sel_Logic_0));
  DiodeBackward diodebackward_121 (.in(_74154_2_p11), .out(Sel_Logic_1));
  DiodeBackward diodebackward_122 (.in(_74154_2_p9), .out(Sel_Logic_1));
  DiodeBackward diodebackward_123 (.in(_74154_2_p11), .out(Sel_Logic_2));
  DiodeBackward diodebackward_124 (.in(_74154_2_p11), .out(Sel_Logic_3));
  DiodeBackward diodebackward_125 (.in(_74154_2_p9), .out(Sel_Cf_0));
  DiodeBackward diodebackward_126 (.in(_74154_2_p9), .out(Sel_Cf_2));
  DiodeBackward diodebackward_127 (.in(_74154_2_p9), .out(Sel_Zf_1));
  DiodeBackward diodebackward_128 (.in(_74154_2_p9), .out(Sel_Vf_1));
  DiodeBackward diodebackward_129 (.in(_74154_2_p9), .out(Sel_Nf_1));
  DiodeBackward diodebackward_130 (.in(_74154_2_p16), .out(Sel_Shift_0));
  DiodeBackward diodebackward_131 (.in(_74154_2_p16), .out(Sel_Shift_1));
  DiodeBackward diodebackward_132 (.in(_74154_2_p16), .out(Sel_Shift_2));
  DiodeBackward diodebackward_133 (.in(_74154_2_p16), .out(Sel_Logic_0));
  DiodeBackward diodebackward_134 (.in(_74154_2_p13), .out(Sel_Logic_0));
  DiodeBackward diodebackward_135 (.in(_74154_2_p16), .out(Sel_Logic_1));
  DiodeBackward diodebackward_136 (.in(_74154_2_p13), .out(Sel_Logic_1));
  DiodeBackward diodebackward_137 (.in(_74154_2_p16), .out(Sel_Logic_2));
  DiodeBackward diodebackward_138 (.in(_74154_2_p16), .out(Sel_Logic_3));
  DiodeBackward diodebackward_139 (.in(_74154_2_p18), .out(Sel_Logic_0));
  DiodeBackward diodebackward_140 (.in(_74154_2_p18), .out(Sel_Logic_1));
  DiodeBackward diodebackward_141 (.in(_74154_2_p18), .out(Sel_Logic_2));
  DiodeBackward diodebackward_142 (.in(_74154_2_p18), .out(Sel_Logic_3));

  // Notes on the sheet:
  //   SEN
  //   CLN
  //   SEZ
  //   CLZ
  //   SEV
  //   CLV
  //   SEC
  //   CLC
  //   SEI
  //   CLI
  //   LRC
  //   ASR
  //   LSR
  //   XOR
  //   NOT
  //   AND
  //   OR
  //   INC
  //   DEC
  //   SBB
  //   NEG
  //   ADC
  //   SUB
  //   LHS-C
  //   ADD
  //   LHS
  //   RHS
  //   NOP
endmodule
