// Digital circuit alu_logic_unit.dig as structural Verilog
module alu_logic_unit (
  input  [3:0] logic_func_sel,
  input  [7:0] rhs,
  input  [7:0] lhs,
  output [7:0] Q
);

  wire _74153_2_p4, _74153_2_p5, _74153_2_p6, _74153_2_p7, _74153_3_p4, _74153_3_p5, _74153_3_p6,
       _74153_3_p7, _74153_4_p4, _74153_4_p5, _74153_4_p6, _74153_4_p7, _74153_6_p4, _74153_6_p5,
       _74153_6_p6, _74153_6_p7, _74153_7_p4, _74153_7_p5, _74153_7_p6, _74153_7_p7, _74153_8_p4,
       _74153_8_p5, _74153_8_p6, _74153_8_p7, notconnected_1_out, notconnected_2_out, notconnected_3_out,
       notconnected_4_out, notconnected_17_out, notconnected_18_out, notconnected_19_out, notconnected_20_out;

  // NotConnected on notconnected_1_out
  // NotConnected on notconnected_2_out
  // NotConnected on notconnected_3_out
  // NotConnected on notconnected_4_out
  // _74153 _74153_1: pin names not known; wires that end beside it: lhs[7], rhs[7], 1'b1, notconnected_1_out, notconnected_2_out, notconnected_3_out, notconnected_4_out, 1'b0, logic_func_sel[0], logic_func_sel[1], logic_func_sel[2], logic_func_sel[3], 1'b1, 1'b0, 1'b0, Q[7]
  // _74153 _74153_2: pin names not known; wires that end beside it: lhs[6], rhs[6], 1'b1, _74153_2_p4, _74153_2_p5, _74153_2_p6, _74153_2_p7, 1'b0, logic_func_sel[0], logic_func_sel[1], logic_func_sel[2], logic_func_sel[3], 1'b1, 1'b0, 1'b0, Q[6]
  // NotConnected on _74153_2_p4
  // NotConnected on _74153_2_p5
  // NotConnected on _74153_2_p6
  // NotConnected on _74153_2_p7
  // _74153 _74153_3: pin names not known; wires that end beside it: lhs[5], rhs[5], 1'b1, _74153_3_p4, _74153_3_p5, _74153_3_p6, _74153_3_p7, 1'b0, logic_func_sel[0], logic_func_sel[1], logic_func_sel[2], logic_func_sel[3], 1'b1, 1'b0, 1'b0, Q[5]
  // NotConnected on _74153_3_p4
  // NotConnected on _74153_3_p5
  // NotConnected on _74153_3_p6
  // NotConnected on _74153_3_p7
  // _74153 _74153_4: pin names not known; wires that end beside it: lhs[4], rhs[4], 1'b1, _74153_4_p4, _74153_4_p5, _74153_4_p6, _74153_4_p7, 1'b0, logic_func_sel[0], logic_func_sel[1], logic_func_sel[2], logic_func_sel[3], 1'b1, 1'b0, 1'b0, Q[4]
  // NotConnected on _74153_4_p4
  // NotConnected on _74153_4_p5
  // NotConnected on _74153_4_p6
  // NotConnected on _74153_4_p7
  // NotConnected on notconnected_17_out
  // NotConnected on notconnected_18_out
  // NotConnected on notconnected_19_out
  // NotConnected on notconnected_20_out
  // _74153 _74153_5: pin names not known; wires that end beside it: lhs[3], rhs[3], 1'b1, notconnected_17_out, notconnected_18_out, notconnected_19_out, notconnected_20_out, 1'b0, logic_func_sel[0], logic_func_sel[1], logic_func_sel[2], logic_func_sel[3], 1'b1, 1'b0, 1'b0, Q[3]
  // _74153 _74153_6: pin names not known; wires that end beside it: lhs[2], rhs[2], 1'b1, _74153_6_p4, _74153_6_p5, _74153_6_p6, _74153_6_p7, 1'b0, logic_func_sel[0], logic_func_sel[1], logic_func_sel[2], logic_func_sel[3], 1'b1, 1'b0, 1'b0, Q[2]
  // NotConnected on _74153_6_p4
  // NotConnected on _74153_6_p5
  // NotConnected on _74153_6_p6
  // NotConnected on _74153_6_p7
  // _74153 _74153_7: pin names not known; wires that end beside it: lhs[1], rhs[1], 1'b1, _74153_7_p4, _74153_7_p5, _74153_7_p6, _74153_7_p7, 1'b0, logic_func_sel[0], logic_func_sel[1], logic_func_sel[2], logic_func_sel[3], 1'b1, 1'b0, 1'b0, Q[1]
  // NotConnected on _74153_7_p4
  // NotConnected on _74153_7_p5
  // NotConnected on _74153_7_p6
  // NotConnected on _74153_7_p7
  // _74153 _74153_8: pin names not known; wires that end beside it: lhs[0], rhs[0], 1'b1, _74153_8_p4, _74153_8_p5, _74153_8_p6, _74153_8_p7, 1'b0, logic_func_sel[0], logic_func_sel[1], logic_func_sel[2], logic_func_sel[3], 1'b1, 1'b0, 1'b0, Q[0]
  // NotConnected on _74153_8_p4
  // NotConnected on _74153_8_p5
  // NotConnected on _74153_8_p6
  // NotConnected on _74153_8_p7

  // Other names for the same wires on the sheet: lhs_0 = lhs[0]; lhs_1 = lhs[1]; lhs_2 = lhs[2]; lhs_3 = lhs[3];
  //   lhs_4 = lhs[4]; lhs_5 = lhs[5]; lhs_6 = lhs[6]; lhs_7 = lhs[7]; func_0 = logic_func_sel[0];
  //   func_1 = logic_func_sel[1]; func_2 = logic_func_sel[2]; func_3 = logic_func_sel[3]; rhs_0 = rhs[0];
  //   rhs_1 = rhs[1]; rhs_2 = rhs[2]; rhs_3 = rhs[3]; rhs_4 = rhs[4]; rhs_5 = rhs[5]; rhs_6 = rhs[6]; rhs_7 = rhs[7]
endmodule
