// Digital circuit alu_shift_unit.dig as structural Verilog
module alu_shift_unit (
  input  [2:0] shift_func_sel,
  input  [7:0] lhs,
  input  C_fin,
  output [7:0] Q,
  output C_fout
);

  wire _74153_5_p4, _74153_5_p5, _74153_5_p6, _74153_5_p7, LSR_Carry_in_Sel_p3, LSR_Carry_in_Sel_p4,
       LSR_Carry_in_Sel_p5, LSR_Carry_in_Sel_p7, LSR_Carry_in_Sel_p8, LSR_Carry_in_Sel_p9,
       LSR_Carry_in_Sel_p13;

  // _74157 LSR_Carry_in_Sel: pin names not known; wires that end beside it: shift_func_sel[0], C_fin, LSR_Carry_in_Sel_p3, LSR_Carry_in_Sel_p4, LSR_Carry_in_Sel_p5, 1'b0, LSR_Carry_in_Sel_p7, LSR_Carry_in_Sel_p8, LSR_Carry_in_Sel_p9, 1'b0, 1'b1, 1'b0, LSR_Carry_in_Sel_p13
  // NotConnected on LSR_Carry_in_Sel_p3
  // NotConnected on LSR_Carry_in_Sel_p4
  // NotConnected on LSR_Carry_in_Sel_p5
  // NotConnected on LSR_Carry_in_Sel_p7
  // NotConnected on LSR_Carry_in_Sel_p8
  // NotConnected on LSR_Carry_in_Sel_p9
  // _74153 _74153_1: pin names not known; wires that end beside it: shift_func_sel[1], shift_func_sel[2], 1'b0, lhs[7], LSR_Carry_in_Sel_p13, lhs[7], 1'b0, 1'b0, lhs[6], lhs[7], lhs[7], 1'b0, 1'b1, 1'b0, Q[7], Q[6]
  // _74153 _74153_2: pin names not known; wires that end beside it: shift_func_sel[1], shift_func_sel[2], 1'b0, lhs[5], lhs[6], lhs[6], 1'b0, 1'b0, lhs[4], lhs[5], lhs[5], 1'b0, 1'b1, 1'b0, Q[5], Q[4]
  // _74153 _74153_3: pin names not known; wires that end beside it: shift_func_sel[1], shift_func_sel[2], 1'b0, lhs[3], lhs[4], lhs[4], 1'b0, 1'b0, lhs[2], lhs[3], lhs[3], 1'b0, 1'b1, 1'b0, Q[3], Q[2]
  // _74153 _74153_4: pin names not known; wires that end beside it: shift_func_sel[1], shift_func_sel[2], 1'b0, lhs[1], lhs[2], lhs[2], 1'b0, 1'b0, lhs[0], lhs[1], lhs[1], 1'b0, 1'b1, 1'b0, Q[1], Q[0]
  // _74153 _74153_5: pin names not known; wires that end beside it: shift_func_sel[1], shift_func_sel[2], 1'b1, _74153_5_p4, _74153_5_p5, _74153_5_p6, _74153_5_p7, 1'b0, C_fin, lhs[0], lhs[0], 1'b0, 1'b1, 1'b0, 1'b0, C_fout
  // NotConnected on _74153_5_p4
  // NotConnected on _74153_5_p5
  // NotConnected on _74153_5_p6
  // NotConnected on _74153_5_p7

  // Other names for the same wires on the sheet: lhs_0 = lhs[0]; lhs_1 = lhs[1]; lhs_2 = lhs[2]; lhs_3 = lhs[3];
  //   lhs_4 = lhs[4]; lhs_5 = lhs[5]; lhs_6 = lhs[6]; lhs_7 = lhs[7]; q_0 = Q[0]; q_1 = Q[1]; q_2 = Q[2]; q_3 = Q[3];
  //   q_4 = Q[4]; q_5 = Q[5]; q_6 = Q[6]; q_7 = Q[7]; f_0 = shift_func_sel[0]; f_1 = shift_func_sel[1];
  //   f_2 = shift_func_sel[2]
endmodule
