// Digital circuit alu_status_register.dig as structural Verilog
module alu_status_register (
  input  [7:0] DBUS,
  input  [4:0] ALU,
  input  CLR,
  input  CLK,
  input  ASSERT,
  input  LOAD_DBUS,
  input  nSet_nSUP,
  input  nSet_nUBR,
  input  nClear_nUBR,
  input  nSet_nNMI_nInhibit,
  output [7:0] flags
);

  wire load;
  wire [3:0] Source_Select_Hi_y, Source_Select_Lo_y;
  wire [3:1] flags_in_hi;

  Multiplexer multiplexer_1 (.sel(nSet_nSUP), .in_0(1'b0), .in_1(flags[5]), .out(flags_in_hi[1]));
  Multiplexer #(.Selector_Bits(2)) multiplexer_2 (
    .sel({nSet_nUBR, nClear_nUBR}), .in_0(flags[6]), .in_1(1'b1), .in_2(1'b0), .in_3(flags[6]),
    .out(flags_in_hi[2]));
  Multiplexer multiplexer_3 (.sel(nSet_nNMI_nInhibit), .in_0(1'b1), .in_1(flags[7]), .out(flags_in_hi[3]));
  or or_1 (load, LOAD_DBUS, flags[5]);
  _74ls157 Source_Select_Hi (
    .S(load), .A(DBUS[7:4]), .B({flags_in_hi, ALU[4]}), .G(1'b0), .VCC(1'b1), .GND(1'b0),
    .Y(Source_Select_Hi_y));
  _74ls157 Source_Select_Lo (
    .S(load), .A(DBUS[3:0]), .B(ALU[3:0]), .G(1'b0), .VCC(1'b1), .GND(1'b0), .Y(Source_Select_Lo_y));
  // _74ls173 Status_Hi: pin names not known; wires that end beside it: Source_Select_Hi_y, CLR, CLK, 1'b0, 1'b0, 1'b0, 1'b0, 1'b1, 1'b0, flags[7:4]
  // _74ls173 Status_Lo: pin names not known; wires that end beside it: Source_Select_Lo_y, CLR, CLK, 1'b0, 1'b0, 1'b0, 1'b0, 1'b1, 1'b0, flags[3:0]
  _74ls245 to_DBUS (.DIR(1'b1), .nOE(ASSERT), .A(flags), .B(DBUS), .VCC(1'b1), .GND(1'b0));

  // Other names for the same wires on the sheet: alu_flags_in[4:0] = ALU; flags_in_lo[3:0] = ALU[3:0];
  //   flags_in_hi[0] = ALU[4]; clr_ubr = nClear_nUBR; dbus_lo[3:0] = DBUS[3:0]; dbus_hi[3:0] = DBUS[7:4];
  //   dbus_load = LOAD_DBUS; alu_flags[4:0] = flags[4:0]; q[7:0] = flags; q_hi[3:0] = flags[7:4]; sup = flags[5];
  //   ubr = flags[6]; nmi = flags[7]; q_lo[3:0] = flags[3:0]; set_nmi = nSet_nNMI_nInhibit; set_sup = nSet_nSUP;
  //   set_ubr = nSet_nUBR

  // Notes on the sheet:
  //   ASSERT: default 1
  //   nSet_nSUP: default 1
  //   nSet_nUBR: default 1
  //   nClear_nUBR: default 1
  //   nSet_nNMI_nInhibit: default 1
  //   Zero because SUP active low
endmodule
