// Digital circuit bank_register.dig as structural Verilog
module bank_register (
  input  clk,
  input  [7:0] dbus,
  input  ncode,
  output [3:0] addr_space,
  output [3:0] bank_select
);

  wire and_1_out, clr_ubr_out, int_out, k_f_q, rti_out, set_ubr_out, ubr_f_q;
  wire [3:0] br_q;

  Button \int  (.out(int_out));
  Button rti (.out(rti_out));
  Button set_ubr (.out(set_ubr_out));
  Button clr_ubr (.out(clr_ubr_out));
  D_FF #(.Bits(4)) br (.D(dbus[3:0]), .C(clk), .Q(br_q));  // open: nQ
  RS_FF_AS k_f (.S(int_out), .R(rti_out), .Q(k_f_q));  // open: nQ
  RS_FF_AS ubr_f (.S(set_ubr_out), .R(clr_ubr_out), .Q(ubr_f_q));  // open: nQ
  Multiplexer #(.Bits(4)) multiplexer_1 (.sel(k_f_q), .in_0(br_q), .in_1(4'b0000), .out(addr_space));
  and and_1 (and_1_out, ubr_f_q, ncode);
  Multiplexer #(.Bits(4)) multiplexer_2 (.sel(and_1_out), .in_0(addr_space), .in_1(br_q), .out(bank_select));
endmodule
