// Digital circuit bus_controller.dig as structural Verilog
module bus_controller (
  input  [3:0] dbus_assert,
  input  [2:0] xfer_load,
  input  [2:0] addr_assert,
  input  clk,
  input  [2:0] count,
  input  dec_sp,
  input  nclk,
  input  [4:0] dbus_load,
  input  [4:0] xfer_assert,
  output ALU_dbus_assert,
  output A_dbus_assert,
  output B_dbus_assert,
  output C_dbus_assert,
  output D_dbus_assert,
  output DP_dbus_assert,
  output DA_dbus_assert,
  output TH_dbus_assert,
  output TL_dbus_assert,
  output SR_dbus_assert,
  output MEM_dbus_assert,
  output MSB_dbus_assert,
  output LSB_dbus_assert,
  output A_dbus_load,
  output B_dbus_load,
  output C_dbus_load,
  output D_dbus_load,
  output DP_dbus_load,
  output DA_dbus_load,
  output TH_dbus_load,
  output TL_dbus_load,
  output SR_dbus_load,
  output MEM_dbus_load,
  output IR_dbus_load,
  output OFF_dbus_load,
  output PCH_dbus_load,
  output PCL_dbus_load,
  output SPH_dbus_load,
  output SPL_dbus_load,
  output XH_dbus_load,
  output XL_dbus_load,
  output YH_dbus_load,
  output YL_dbus_load,
  output PC_xfer_assert,
  output SP_xfer_assert,
  output X_xfer_assert,
  output Y_xfer_assert,
  output ISR_xfer_assert,
  output addr_xfer_assert,
  output A_lhs_assert,
  output B_lhs_assert,
  output C_lhs_assert,
  output D_lhs_assert,
  output TH_lhs_assert,
  output A_rhs_assert,
  output B_rhs_assert,
  output C_rhs_assert,
  output D_rhs_assert,
  output TL_rhs_assert,
  output PC_xfer_load,
  output SP_xfer_load,
  output X_xfer_load,
  output Y_xfer_load,
  output AB_xfer_load,
  output CD_xfer_load,
  output ACK_addr_assert,
  output PC_addr_assert,
  output SP_addr_assert,
  output X_addr_assert,
  output Y_addr_assert,
  output DP_addr_assert,
  output T_addr_assert,
  output IO_addr_assert,
  output PC_inc,
  output SP_inc,
  output X_inc,
  output Y_inc,
  output ADDR_inc,
  output X_dec,
  output Y_dec,
  output SP_dec,
  output musteq_load
);

  wire _7400_1_p5, _7400_1_p6, _7400_1_p7, _7400_1_p8, _7421_1_p11, _7421_1_p12, _7421_2_p11, _7421_2_p12,
       _7421_3_p11, _7421_3_p12, naddr_a0, naddr_a6, ndbus_a13, ndbus_a14, ndbus_a15, ndbus_l21, ndbus_l22,
       ndbus_l23, ndbus_l24, ndbus_l25, ndbus_l26, ndbus_l27, ndbus_l29, ndbus_l30, ndbus_l31, ndl4,
       not_1_out, notconnected_1_out, notconnected_2_out, nxa4, nxfer_a6, nxfer_a7, nxfer_a8, nxfer_a9,
       nxfer_a10, nxfer_a11, nxfer_a12, nxfer_a13, nxfer_a14, nxfer_a15, nxfer_a16, nxfer_a17, nxfer_a18,
       nxfer_a19, nxfer_a20, nxfer_a21, nxfer_a22, nxfer_a23, nxfer_a24, nxfer_a25, nxfer_a26, nxfer_a27,
       nxfer_a28, nxfer_a29, nxfer_a30, nxfer_a31, nxfer_l7, select_lhs_assert_p11, select_lhs_assert_p12,
       select_rhs_assert_p11, select_rhs_assert_p12;

  not not_1 (not_1_out, dbus_load[3]);
  // _74138 DBUS_assert: pin names not known; wires that end beside it: dbus_assert[0], dbus_assert[2], dbus_assert[1], 1'b1, 1'b0, dbus_assert[3], 1'b1, 1'b0, ALU_dbus_assert, A_dbus_assert, B_dbus_assert, C_dbus_assert, D_dbus_assert, DP_dbus_assert, DA_dbus_assert, TH_dbus_assert
  // _74138 _74138_1: pin names not known; wires that end beside it: dbus_assert[0], dbus_assert[2], dbus_assert[1], dbus_assert[3], 1'b0, 1'b0, 1'b1, 1'b0, TL_dbus_assert, SR_dbus_assert, MEM_dbus_assert, MSB_dbus_assert, LSB_dbus_assert, ndbus_a13, ndbus_a14, ndbus_a15
  // _74138 DBUS_load: pin names not known; wires that end beside it: dbus_load[0], dbus_load[2], dbus_load[1], ndl4, 1'b0, dbus_load[3], 1'b1, 1'b0, A_dbus_load, B_dbus_load, C_dbus_load, D_dbus_load, DP_dbus_load, DA_dbus_load, TH_dbus_load
  // _74138 _74138_2: pin names not known; wires that end beside it: dbus_load[0], dbus_load[2], dbus_load[1], dbus_load[3], 1'b0, dbus_load[4], 1'b1, 1'b0, TL_dbus_load, SR_dbus_load, MEM_dbus_load, IR_dbus_load, OFF_dbus_load, PCH_dbus_load, PCL_dbus_load, SPH_dbus_load
  // _74138 _74138_3: pin names not known; wires that end beside it: dbus_load[0], dbus_load[2], dbus_load[1], dbus_load[4], 1'b0, dbus_load[3], 1'b1, 1'b0, SPL_dbus_load, XH_dbus_load, XL_dbus_load, YH_dbus_load, YL_dbus_load, ndbus_l21, ndbus_l22, ndbus_l23
  // _74138 _74138_4: pin names not known; wires that end beside it: dbus_load[0], dbus_load[2], dbus_load[1], dbus_load[4], 1'b0, not_1_out, 1'b1, 1'b0, ndbus_l24, ndbus_l25, ndbus_l26, ndbus_l27, musteq_load, ndbus_l29, ndbus_l30, ndbus_l31
  // _7404 _7404_1: pin names not known; wires that end beside it: dbus_load[4], xfer_assert[4], 1'b1, 1'b1, 1'b1, 1'b1, 1'b1, 1'b0, ndl4, nxa4
  // _74138 XFER_assert: pin names not known; wires that end beside it: xfer_assert[0], xfer_assert[2], xfer_assert[1], 1'b1, xfer_assert[3], xfer_assert[4], 1'b1, 1'b0, PC_xfer_assert, SP_xfer_assert, X_xfer_assert, Y_xfer_assert, ISR_xfer_assert, addr_xfer_assert, nxfer_a6, nxfer_a7
  // _74138 _74138_5: pin names not known; wires that end beside it: xfer_assert[0], xfer_assert[2], xfer_assert[1], xfer_assert[3], xfer_assert[4], 1'b0, 1'b1, 1'b0, nxfer_a8, nxfer_a9, nxfer_a10, nxfer_a11, nxfer_a12, nxfer_a13, nxfer_a14, nxfer_a15
  // _74138 _74138_6: pin names not known; wires that end beside it: xfer_assert[0], xfer_assert[2], xfer_assert[1], xfer_assert[4], xfer_assert[3], 1'b0, 1'b1, 1'b0, nxfer_a16, nxfer_a17, nxfer_a18, nxfer_a19, nxfer_a20, nxfer_a21, nxfer_a22, nxfer_a23
  // _74138 _74138_7: pin names not known; wires that end beside it: xfer_assert[0], xfer_assert[2], xfer_assert[1], xfer_assert[3], nxa4, 1'b0, 1'b1, 1'b0, nxfer_a24, nxfer_a25, nxfer_a26, nxfer_a27, nxfer_a28, nxfer_a29, nxfer_a30, nxfer_a31
  // _74138 XFER_load: pin names not known; wires that end beside it: xfer_load[0], xfer_load[2], xfer_load[1], 1'b1, nclk, 1'b0, 1'b1, 1'b0, PC_xfer_load, SP_xfer_load, X_xfer_load, Y_xfer_load, AB_xfer_load, CD_xfer_load, nxfer_l7
  // _74138 ADDR_assert: pin names not known; wires that end beside it: addr_assert[0], addr_assert[2], addr_assert[1], 1'b1, 1'b0, 1'b0, 1'b1, 1'b0, naddr_a0, PC_addr_assert, SP_addr_assert, X_addr_assert, Y_addr_assert, DP_addr_assert, naddr_a6, IO_addr_assert
  // _74138 Counter_Inc_Dec: pin names not known; wires that end beside it: count[0], count[2], count[1], 1'b1, 1'b0, nclk, 1'b1, 1'b0, PC_inc, SP_inc, X_inc, Y_inc, ADDR_inc, X_dec, Y_dec
  // _7421 select_lhs_assert: pin names not known; wires that end beside it: nxfer_a6, nxfer_a8, nxfer_a11, nxfer_a13, nxfer_a7, nxfer_a12, nxfer_a9, nxfer_a14, 1'b1, 1'b0, select_lhs_assert_p11, select_lhs_assert_p12
  // _7421 _7421_1: pin names not known; wires that end beside it: nxfer_a16, nxfer_a18, nxfer_a21, nxfer_a23, nxfer_a17, nxfer_a22, nxfer_a19, nxfer_a24, 1'b1, 1'b0, _7421_1_p11, _7421_1_p12
  // _7421 _7421_2: pin names not known; wires that end beside it: nxfer_a26, nxfer_a28, nxfer_a6, nxfer_a16, nxfer_a27, nxfer_a11, nxfer_a29, nxfer_a21, 1'b1, 1'b0, _7421_2_p11, _7421_2_p12
  // _7421 select_rhs_assert: pin names not known; wires that end beside it: nxfer_a7, nxfer_a17, nxfer_a8, nxfer_a18, nxfer_a12, nxfer_a13, nxfer_a22, nxfer_a23, 1'b1, 1'b0, select_rhs_assert_p11, select_rhs_assert_p12
  // _7421 _7421_3: pin names not known; wires that end beside it: nxfer_a9, nxfer_a19, nxfer_a10, nxfer_a20, nxfer_a14, nxfer_a15, nxfer_a24, nxfer_a25, 1'b1, 1'b0, _7421_3_p11, _7421_3_p12
  // NotConnected on notconnected_1_out
  // NotConnected on notconnected_2_out
  // _7408 _7408_1: pin names not known; wires that end beside it: select_lhs_assert_p11, nxfer_a10, select_lhs_assert_p12, nxfer_a15, _7421_1_p11, nxfer_a20, _7421_1_p12, nxfer_a25, 1'b1, 1'b0, A_lhs_assert, B_lhs_assert, C_lhs_assert, D_lhs_assert
  // _7408 _7408_2: pin names not known; wires that end beside it: _7421_2_p11, nxfer_a30, _7421_2_p12, nxfer_a26, select_rhs_assert_p11, nxfer_a27, select_rhs_assert_p12, nxfer_a28, 1'b1, 1'b0, TH_lhs_assert, A_rhs_assert, B_rhs_assert, C_rhs_assert
  // _7408 _7408_3: pin names not known; wires that end beside it: _7421_3_p11, nxfer_a29, _7421_3_p12, nxfer_a30, naddr_a6, IO_addr_assert, notconnected_1_out, notconnected_2_out, 1'b1, 1'b0, D_rhs_assert, TL_rhs_assert, T_addr_assert
  // _7400 _7400_1: pin names not known; wires that end beside it: clk, dec_sp, naddr_a0, addr_xfer_assert, _7400_1_p5, _7400_1_p6, _7400_1_p7, _7400_1_p8, 1'b1, 1'b0, SP_dec, ACK_addr_assert
  // NotConnected on _7400_1_p5
  // NotConnected on _7400_1_p6
  // NotConnected on _7400_1_p7
  // NotConnected on _7400_1_p8

  // Other names for the same wires on the sheet: aa0 = addr_assert[0]; aa1 = addr_assert[1]; aa2 = addr_assert[2];
  //   ci0 = count[0]; ci1 = count[1]; ci2 = count[2]; da0 = dbus_assert[0]; da1 = dbus_assert[1];
  //   da2 = dbus_assert[2]; da3 = dbus_assert[3]; dl0 = dbus_load[0]; dl1 = dbus_load[1]; dl2 = dbus_load[2];
  //   dl3 = dbus_load[3]; dl4 = dbus_load[4]; naddr_a1 = PC_addr_assert; naddr_a2 = SP_addr_assert;
  //   naddr_a3 = X_addr_assert; naddr_a4 = Y_addr_assert; naddr_a5 = DP_addr_assert; naddr_a7 = IO_addr_assert;
  //   ncount_1 = PC_inc; ncount_2 = SP_inc; ncount_3 = X_inc; ncount_4 = Y_inc; ncount_5 = ADDR_inc; ncount_6 = X_dec;
  //   ncount_7 = Y_dec; ndbus_a0 = ALU_dbus_assert; ndbus_a1 = A_dbus_assert; ndbus_a2 = B_dbus_assert;
  //   ndbus_a3 = C_dbus_assert; ndbus_a4 = D_dbus_assert; ndbus_a5 = DP_dbus_assert; ndbus_a6 = DA_dbus_assert;
  //   ndbus_a7 = TH_dbus_assert; ndbus_a8 = TL_dbus_assert; ndbus_a9 = SR_dbus_assert; ndbus_a10 = MEM_dbus_assert;
  //   ndbus_a11 = MSB_dbus_assert; ndbus_a12 = LSB_dbus_assert; ndbus_l1 = A_dbus_load; ndbus_l2 = B_dbus_load;
  //   ndbus_l3 = C_dbus_load; ndbus_l4 = D_dbus_load; ndbus_l5 = DP_dbus_load; ndbus_l6 = DA_dbus_load;
  //   ndbus_l7 = TH_dbus_load; ndbus_l8 = TL_dbus_load; ndbus_l9 = SR_dbus_load; ndbus_l10 = MEM_dbus_load;
  //   ndbus_l11 = IR_dbus_load; ndbus_l12 = OFF_dbus_load; ndbus_l13 = PCH_dbus_load; ndbus_l14 = PCL_dbus_load;
  //   ndbus_l15 = SPH_dbus_load; ndbus_l16 = SPL_dbus_load; ndbus_l17 = XH_dbus_load; ndbus_l18 = XL_dbus_load;
  //   ndbus_l19 = YH_dbus_load; ndbus_l20 = YL_dbus_load; ndbus_l28 = musteq_load; nxfer_a0 = PC_xfer_assert;
  //   nxfer_a1 = SP_xfer_assert; nxfer_a2 = X_xfer_assert; nxfer_a3 = Y_xfer_assert; nxfer_a4 = ISR_xfer_assert;
  //   nxfer_a5 = addr_xfer_assert; nxfer_l1 = PC_xfer_load; nxfer_l2 = SP_xfer_load; nxfer_l3 = X_xfer_load;
  //   nxfer_l4 = Y_xfer_load; nxfer_l5 = AB_xfer_load; nxfer_l6 = CD_xfer_load; xa0 = xfer_assert[0];
  //   xa1 = xfer_assert[1]; xa2 = xfer_assert[2]; xa3 = xfer_assert[3]; xa4 = xfer_assert[4]; xl0 = xfer_load[0];
  //   xl1 = xfer_load[1]; xl2 = xfer_load[2]
endmodule
