// Digital circuit constant_generator_16bit.dig as structural Verilog
module constant_generator_16bit (
  input  [15:0] RSTv_Lo,
  input  [15:0] ISRv_Lo,
  input  [15:0] SPi,
  input  SPi_xfer_assert,
  input  RST_xfer_assert,
  input  ISR_xfer_assert,
  output [15:0] xfer
);

  _74ls245 RSTv_Lo_to_XFER (.DIR(1'b1), .nOE(RST_xfer_assert), .A(RSTv_Lo[7:0]), .B(xfer[7:0]), .VCC(1'b1), .GND(1'b0));
  _74ls245 _74ls245_1 (.DIR(1'b1), .nOE(RST_xfer_assert), .A(RSTv_Lo[15:8]), .B(xfer[15:8]), .VCC(1'b1), .GND(1'b0));
  _74ls245 ISRv_Lo_to_XFER (.DIR(1'b1), .nOE(ISR_xfer_assert), .A(ISRv_Lo[7:0]), .B(xfer[7:0]), .VCC(1'b1), .GND(1'b0));
  _74ls245 _74ls245_2 (.DIR(1'b1), .nOE(ISR_xfer_assert), .A(ISRv_Lo[15:8]), .B(xfer[15:8]), .VCC(1'b1), .GND(1'b0));
  _74ls245 SPi_to_XFER (.DIR(1'b1), .nOE(SPi_xfer_assert), .A(SPi[7:0]), .B(xfer[7:0]), .VCC(1'b1), .GND(1'b0));
  _74ls245 _74ls245_3 (.DIR(1'b1), .nOE(SPi_xfer_assert), .A(SPi[15:8]), .B(xfer[15:8]), .VCC(1'b1), .GND(1'b0));

  // Other names for the same wires on the sheet: xfer_hi[7:0] = xfer[15:8]; xfer_lo[7:0] = xfer[7:0]
endmodule
