// Digital circuit constant_generator_8bit.dig as structural Verilog
module constant_generator_8bit (
  input  dpi_dbus_assert,
  input  [7:0] DPi,
  input  zero_dbus_assert,
  output [7:0] dbus
);

  _74ls245 DPi_to_dbus (.DIR(1'b1), .nOE(dpi_dbus_assert), .A(DPi), .B(dbus), .VCC(1'b1), .GND(1'b0));
  _74ls245 zero_to_dbus (.DIR(1'b1), .nOE(zero_dbus_assert), .A({8{1'b0}}), .B(dbus), .VCC(1'b1), .GND(1'b0));
endmodule
