// Digital circuit control_unit.dig as structural Verilog
module control_unit (
  input  nirq,
  input  [7:0] opcode,
  input  [4:0] flags,
  input  nreq,
  input  nrst,
  input  nnmi,
  input  NMI_Inhib,
  input  clk,
  output [3:0] dbus_assert,
  output [4:0] dbus_load,
  output [3:0] alu_op,
  output [4:0] xfer_assert,
  output [2:0] xfer_load,
  output [2:0] addr_assert,
  output [2:0] count,
  output dec_sp,
  output nclk,
  output noffset,
  output rst,
  output [17:0] dbg
);

  wire _3_input_AND_p3, _3_input_AND_p4, _3_input_AND_p5, _3_input_AND_p6, _3_input_AND_p8, _3_input_AND_p9,
       _7402_1_p2, AND_p7, AND_p8, AND_p12, button_1_out, clk_t, clr_ext, clr_ubr, ctrl_inverter_p6, irq,
       irq_and, nirq_latch, nmi, nmi_and, nmi_nand, nnmi_inhib, nnmi_latch, notconnected_1_out,
       notconnected_15_out, notconnected_16_out, notconnected_17_out, notconnected_18_out, nreq_latch,
       nrst_useq, nset_ext, offset, req, rst_useq, seq_rst, sequencer_p1, sequencer_p4, sequencer_p5,
       sequencer_p6, set_ext, set_nmi, set_sup, set_ubr, t0;
  wire [1:0] OR_2_p12;
  wire [7:0] ucode0_d, ucode1_d, ucode2_d, ucode3_d;
  wire [7:2] State_Latch_q;
  wire [7:3] Interrupt_Latch_q;
  wire [7:5] _74ls273_4_q;

  Button button_1 (.out(button_1_out));
  or or_1 (clk_t, button_1_out, clk);
  // NotConnected on notconnected_1_out
  // _7404 NOT: pin names not known; wires that end beside it: nreq_latch, NMI_Inhib, nnmi_latch, nmi_and, nirq_latch, notconnected_1_out, 1'b1, 1'b0, req, nnmi_inhib, nmi, nmi_nand, irq
  // _7404 ctrl_inverter: pin names not known; wires that end beside it: clk_t, nrst, offset, nrst_useq, nset_ext, ctrl_inverter_p6, 1'b1, 1'b0, nclk, rst, noffset, rst_useq, set_ext
  // NotConnected on ctrl_inverter_p6
  _74ls273 Interrupt_Latch (
    .CP(clk_t), .nMR(nrst), .D({{5{1'b0}}, nreq, nnmi, nirq}), .VCC(1'b1), .GND(1'b0),
    .Q({Interrupt_Latch_q, nreq_latch, nnmi_latch, nirq_latch}));
  // _7408 AND: pin names not known; wires that end beside it: nmi, nnmi_inhib, nmi_nand, irq_and, flags[4], irq, AND_p7, AND_p8, 1'b1, 1'b0, nmi_and, AND_p12, irq_and
  // NotConnected on AND_p7
  // NotConnected on AND_p8
  // _7411 _3_input_AND: pin names not known; wires that end beside it: dbg[0], dbg[1], _3_input_AND_p3, _3_input_AND_p4, _3_input_AND_p5, _3_input_AND_p6, dbg[2], _3_input_AND_p8, _3_input_AND_p9, 1'b1, 1'b0, t0
  // NotConnected on _3_input_AND_p3
  // NotConnected on _3_input_AND_p4
  // NotConnected on _3_input_AND_p5
  // NotConnected on _3_input_AND_p6
  // NotConnected on _3_input_AND_p8
  // NotConnected on _3_input_AND_p9
  // _7432 OR_2: pin names not known; wires that end beside it: req, nmi_and, req, AND_p12, rst_useq, rst, seq_rst, t0, 1'b1, 1'b0, OR_2_p12[0], OR_2_p12[1], seq_rst, clr_ext
  // _74193 sequencer: pin names not known; wires that end beside it: sequencer_p1, 1'b1, nclk, sequencer_p4, sequencer_p5, sequencer_p6, seq_rst, 1'b1, 1'b1, 1'b0, dbg[0], dbg[1], dbg[2]
  // NotConnected on sequencer_p1
  // NotConnected on sequencer_p4
  // NotConnected on sequencer_p5
  // NotConnected on sequencer_p6
  _74ls273 State_Latch (
    .CP(nclk), .nMR(nrst), .D({{6{1'b0}}, OR_2_p12}), .VCC(1'b1), .GND(1'b0), .Q({State_Latch_q, dbg[17:16]}));
  // NotConnected on notconnected_15_out
  // NotConnected on notconnected_16_out
  // NotConnected on notconnected_17_out
  // NotConnected on notconnected_18_out
  // _7402 _7402_1: pin names not known; wires that end beside it: clr_ext, _7402_1_p2, dbg[15], set_ext, notconnected_15_out, notconnected_16_out, notconnected_17_out, notconnected_18_out, 1'b1, 1'b0, dbg[15], _7402_1_p2
  ROM #(.AddrBits(18), .Bits(8)) ucode0 (.A({dbg[17:15], opcode, flags[3:0], dbg[2:0]}), .sel(1'b1), .D(ucode0_d));
  ROM #(.AddrBits(18), .Bits(8)) ucode1 (.A({dbg[17:15], opcode, flags[3:0], dbg[2:0]}), .sel(1'b1), .D(ucode1_d));
  ROM #(.AddrBits(18), .Bits(8)) ucode2 (.A({dbg[17:15], opcode, flags[3:0], dbg[2:0]}), .sel(1'b1), .D(ucode2_d));
  ROM #(.AddrBits(18), .Bits(8)) ucode3 (.A({dbg[17:15], opcode, flags[3:0], dbg[2:0]}), .sel(1'b1), .D(ucode3_d));
  _74ls273 _74ls273_1 (.CP(clk_t), .nMR(nrst), .D(ucode0_d), .VCC(1'b1), .GND(1'b0), .Q({alu_op, dbus_assert}));
  _74ls273 _74ls273_2 (.CP(clk_t), .nMR(nrst), .D(ucode1_d), .VCC(1'b1), .GND(1'b0), .Q({addr_assert, dbus_load}));
  _74ls273 _74ls273_3 (.CP(clk_t), .nMR(nrst), .D(ucode2_d), .VCC(1'b1), .GND(1'b0), .Q({xfer_load, xfer_assert}));
  _74ls273 _74ls273_4 (
    .CP(clk_t), .nMR(nrst), .D(ucode3_d), .VCC(1'b1), .GND(1'b0), .Q({_74ls273_4_q, offset, dec_sp, count}));
  // _74138 _74138_1: pin names not known; wires that end beside it: _74ls273_4_q[5], _74ls273_4_q[7], _74ls273_4_q[6], 1'b1, 1'b0, 1'b0, 1'b1, 1'b0, nrst_useq, nset_ext, set_ubr, clr_ubr, set_sup, set_nmi

  assign dbg[14:3] = {opcode, flags[3:0]};

  // Other names for the same wires on the sheet: ucode_addr[17:0] = {dbg[17:15], opcode, flags[3:0], dbg[2:0]};
  //   t_state[2:0] = dbg[2:0]; ext = dbg[15]; C_f = flags[0]; Z_f = flags[1]; V_f = flags[2]; N_f = flags[3];
  //   I_f = flags[4]

  // Notes on the sheet:
  //   nirq: default 1
  //   nreq: default 1
  //   nnmi: default 1
  //   NMI_Inhib: default 1
  //   ucode0 loads microcode0.bin
  //   ucode1 loads microcode1.bin
  //   ucode2 loads microcode2.bin
  //   ucode3 loads microcode3.bin
endmodule
