// Digital circuit dual_reg8.dig as structural Verilog
module dual_reg8 (
  input  rst,
  input  nclk,
  input  [7:0] dbus,
  input  nload_lhs,
  input  nassert_outa_lhs,
  input  nassert_outb_lhs,
  input  nassert_outc_lhs,
  input  nload_rhs,
  input  nassert_outa_rhs,
  input  nassert_outb_rhs,
  input  nassert_outc_rhs,
  output [7:0] Q_lhs,
  output [7:0] out_a_lhs,
  output [7:0] out_b_lhs,
  output [7:0] out_c_lhs,
  output [7:0] Q_rhs,
  output [7:0] out_a_rhs,
  output [7:0] out_b_rhs,
  output [7:0] out_c_rhs
);

  _74ls245 _74ls245_1 (.DIR(1'b1), .nOE(nassert_outa_lhs), .A(Q_lhs), .B(out_a_lhs), .VCC(1'b1), .GND(1'b0));
  // _74ls173 _74ls173_1: pin names not known; wires that end beside it: dbus[7:4], rst, nclk, nload_lhs, nload_lhs, 1'b0, 1'b0, 1'b1, 1'b0, Q_lhs[7:4]
  // _74ls173 _74ls173_2: pin names not known; wires that end beside it: dbus[3:0], rst, nclk, nload_lhs, nload_lhs, 1'b0, 1'b0, 1'b1, 1'b0, Q_lhs[3:0]
  _74ls245 _74ls245_2 (.DIR(1'b1), .nOE(nassert_outb_lhs), .A(Q_lhs), .B(out_b_lhs), .VCC(1'b1), .GND(1'b0));
  _74ls245 _74ls245_3 (.DIR(1'b1), .nOE(nassert_outc_lhs), .A(Q_lhs), .B(out_c_lhs), .VCC(1'b1), .GND(1'b0));
  _74ls245 _74ls245_4 (.DIR(1'b1), .nOE(nassert_outa_rhs), .A(Q_rhs), .B(out_a_rhs), .VCC(1'b1), .GND(1'b0));
  // _74ls173 _74ls173_3: pin names not known; wires that end beside it: dbus[7:4], rst, nclk, nload_rhs, nload_rhs, 1'b0, 1'b0, 1'b1, 1'b0, Q_rhs[7:4]
  // _74ls173 _74ls173_4: pin names not known; wires that end beside it: dbus[3:0], rst, nclk, nload_rhs, nload_rhs, 1'b0, 1'b0, 1'b1, 1'b0, Q_rhs[3:0]
  _74ls245 _74ls245_5 (.DIR(1'b1), .nOE(nassert_outb_rhs), .A(Q_rhs), .B(out_b_rhs), .VCC(1'b1), .GND(1'b0));
  _74ls245 _74ls245_6 (.DIR(1'b1), .nOE(nassert_outc_rhs), .A(Q_rhs), .B(out_c_rhs), .VCC(1'b1), .GND(1'b0));

  // Other names for the same wires on the sheet: dbus_lo[3:0] = dbus[3:0]; dbus_hi[3:0] = dbus[7:4]

  // Notes on the sheet:
  //   nload_lhs: default 1
  //   nassert_outa_lhs: default 1
  //   nassert_outb_lhs: default 1
  //   nassert_outc_lhs: default 1
  //   nload_rhs: default 1
  //   nassert_outa_rhs: default 1
  //   nassert_outb_rhs: default 1
  //   nassert_outc_rhs: default 1
endmodule
