// Digital circuit general_purpose_register.dig as structural Verilog
module general_purpose_register (
  input  [7:0] DBUS_IN,
  input  CLK,
  input  DBUS_LOAD,
  input  DBUS_ASSERT,
  input  LHS_ASSERT,
  input  RHS_ASSERT,
  input  CLR,
  output [7:0] LHS,
  output [7:0] RHS,
  output [7:0] DBUS_OUT
);

  wire q0, q1, q2, q3, q4, q5, q6, q7;

  // _74173 Low_Byte: pin names not known; wires that end beside it: DBUS_IN[0], 1'b1, 1'b0, CLR, DBUS_IN[1], DBUS_IN[2], DBUS_IN[3], CLK, DBUS_LOAD, DBUS_LOAD, 1'b0, 1'b0, q0, q1, q2, q3
  // _74173 High_Byte: pin names not known; wires that end beside it: DBUS_IN[4], 1'b1, 1'b0, CLR, DBUS_IN[5], DBUS_IN[6], DBUS_IN[7], CLK, DBUS_LOAD, DBUS_LOAD, 1'b0, 1'b0, q4, q5, q6, q7
  // _74245 to_DBUS: pin names not known; wires that end beside it: 1'b1, DBUS_ASSERT, q0, DBUS_IN[0], q1, DBUS_IN[1], q2, DBUS_IN[2], q3, DBUS_IN[3], q4, DBUS_IN[4], q5, DBUS_IN[5], q6, DBUS_IN[6], q7, DBUS_IN[7], 1'b1, 1'b0
  // _74245 to_LHS: pin names not known; wires that end beside it: 1'b1, LHS_ASSERT, q0, LHS[0], q1, LHS[1], q2, LHS[2], q3, LHS[3], q4, LHS[4], q5, LHS[5], q6, LHS[6], q7, LHS[7], 1'b1, 1'b0
  // _74245 to_RHS: pin names not known; wires that end beside it: 1'b1, RHS_ASSERT, q0, RHS[0], q1, RHS[1], q2, RHS[2], q3, RHS[3], q4, RHS[4], q5, RHS[5], q6, RHS[6], q7, RHS[7], 1'b1, 1'b0

  assign DBUS_OUT = DBUS_IN;

  // Other names for the same wires on the sheet: dbus[7:0] = DBUS_IN; dbus0 = DBUS_IN[0]; dbus1 = DBUS_IN[1];
  //   dbus2 = DBUS_IN[2]; dbus3 = DBUS_IN[3]; dbus4 = DBUS_IN[4]; dbus5 = DBUS_IN[5]; dbus6 = DBUS_IN[6];
  //   dbus7 = DBUS_IN[7]

  // Notes on the sheet:
  //   DBUS_LOAD: default 1
  //   DBUS_ASSERT: default 1
  //   LHS_ASSERT: default 1
  //   RHS_ASSERT: default 1
endmodule
