// Digital circuit gpr_pair.dig as structural Verilog
module gpr_pair (
  input  naddr_assert,
  input  nxfer_load,
  input  nhi_dbus_load,
  input  nlo_dbus_load,
  input  nhi_dbus_assert,
  input  nlo_dbus_assert,
  input  nhi_lhs_assert,
  input  nlo_lhs_assert,
  input  nhi_rhs_assert,
  input  nlo_rhs_assert,
  input  [7:0] dbus,
  input  [15:0] xfer,
  input  nclr,
  output [15:0] addr,
  output [7:0] reg_hi,
  output [7:0] reg_lo
);

  wire load_control_p5, load_control_p6, load_control_p7, load_control_p8, load_hi, load_lo;
  wire [3:0] d_00, d_01, d_10, d_11;

  // _7408 load_control: pin names not known; wires that end beside it: nxfer_load, nhi_dbus_load, nxfer_load, nlo_dbus_load, load_control_p5, load_control_p6, load_control_p7, load_control_p8, 1'b1, 1'b0, load_hi, load_lo
  // NotConnected on load_control_p5
  // NotConnected on load_control_p6
  // NotConnected on load_control_p7
  // NotConnected on load_control_p8
  _74ls157 Hi_Reg_Hi_mux_in (
    .S(nhi_dbus_load), .A(dbus[7:4]), .B(xfer[15:12]), .G(1'b0), .VCC(1'b1), .GND(1'b0), .Y(d_11));
  _74ls273 Hi_Reg (.CP(load_hi), .nMR(nclr), .D({d_11, d_10}), .VCC(1'b1), .GND(1'b0), .Q(reg_hi));
  _74ls245 Hi_Reg_to_dbus (.DIR(1'b1), .nOE(nhi_dbus_assert), .A(reg_hi), .B(dbus), .VCC(1'b1), .GND(1'b0));
  _74ls245 Hi_Reg_to_rhs (.DIR(1'b1), .nOE(nhi_rhs_assert), .A(reg_hi), .B(xfer[7:0]), .VCC(1'b1), .GND(1'b0));
  _74ls245 Hi_Reg_to_addr (.DIR(1'b1), .nOE(naddr_assert), .A(reg_hi), .B(addr[15:8]), .VCC(1'b1), .GND(1'b0));
  _74ls245 Hi_Reg_to_lhs (.DIR(1'b1), .nOE(nhi_lhs_assert), .A(reg_hi), .B(xfer[15:8]), .VCC(1'b1), .GND(1'b0));
  _74ls157 Hi_Reg_Lo_mux_in (
    .S(nhi_dbus_load), .A(dbus[3:0]), .B(xfer[11:8]), .G(1'b0), .VCC(1'b1), .GND(1'b0), .Y(d_10));
  _74ls273 Lo_Reg (.CP(load_lo), .nMR(nclr), .D({d_01, d_00}), .VCC(1'b1), .GND(1'b0), .Q(reg_lo));
  _74ls245 Lo_Reg_to_dbus (.DIR(1'b1), .nOE(nlo_dbus_assert), .A(reg_lo), .B(dbus), .VCC(1'b1), .GND(1'b0));
  _74ls245 Lo_Reg_to_lhs (.DIR(1'b1), .nOE(nlo_lhs_assert), .A(reg_lo), .B(xfer[15:8]), .VCC(1'b1), .GND(1'b0));
  _74ls157 Lo_Reg_Hi_mux_in (
    .S(nlo_dbus_load), .A(dbus[7:4]), .B(xfer[7:4]), .G(1'b0), .VCC(1'b1), .GND(1'b0), .Y(d_01));
  _74ls245 Lo_Reg_to_addr (.DIR(1'b1), .nOE(naddr_assert), .A(reg_lo), .B(addr[7:0]), .VCC(1'b1), .GND(1'b0));
  _74ls245 Lo_Reg_to_rhs (.DIR(1'b1), .nOE(nlo_rhs_assert), .A(reg_lo), .B(xfer[7:0]), .VCC(1'b1), .GND(1'b0));
  _74ls157 Lo_Reg_Lo_mux_in (
    .S(nlo_dbus_load), .A(dbus[3:0]), .B(xfer[3:0]), .G(1'b0), .VCC(1'b1), .GND(1'b0), .Y(d_00));

  // Other names for the same wires on the sheet: addr_hi[7:0] = addr[15:8]; addr_lo[7:0] = addr[7:0];
  //   assert_addr = naddr_assert; assert_hi_dbus = nhi_dbus_assert; assert_hi_lhs = nhi_lhs_assert;
  //   assert_hi_rhs = nhi_rhs_assert; assert_lo_dbus = nlo_dbus_assert; assert_lo_lhs = nlo_lhs_assert;
  //   assert_lo_rhs = nlo_rhs_assert; d_lo[7:0] = {d_01, d_00}; d_hi[7:0] = {d_11, d_10}; dbus_lo[3:0] = dbus[3:0];
  //   dbus_hi[3:0] = dbus[7:4]; lhs[7:0] = xfer[15:8]; xfer_10[3:0] = xfer[11:8]; xfer_11[3:0] = xfer[15:12];
  //   load_hi_dbus = nhi_dbus_load; load_lo_dbus = nlo_dbus_load; load_xfer = nxfer_load; q_hi[7:0] = reg_hi;
  //   q_lo[7:0] = reg_lo; rhs[7:0] = xfer[7:0]; xfer_00[3:0] = xfer[3:0]; xfer_01[3:0] = xfer[7:4]

  // Notes on the sheet:
  //   naddr_assert: default 1
  //   nxfer_load: default 1
  //   nhi_dbus_load: default 1
  //   nlo_dbus_load: default 1
  //   nhi_dbus_assert: default 1
  //   nlo_dbus_assert: default 1
  //   nhi_lhs_assert: default 1
  //   nlo_lhs_assert: default 1
  //   nhi_rhs_assert: default 1
  //   nlo_rhs_assert: default 1
endmodule
