// Digital circuit instruction_register.dig as structural Verilog
module instruction_register (
  input  clk,
  input  [7:0] dbus,
  input  dbus_load,
  input  clr,
  output [7:0] opcode
);

  wire dbus_hi, dbus_load_t;

  // _74ls173 high: pin names not known; wires that end beside it: dbus_hi, 1'b1, 1'b0, clr, clk, dbus_load_t, dbus_load_t, 1'b0, 1'b0, opcode[7:4]
  // _74ls173 lo: pin names not known; wires that end beside it: dbus[7:4], 1'b1, 1'b0, clr, clk, dbus_load_t, dbus_load_t, 1'b0, 1'b0, opcode[3:0]

  assign dbus[3:0] = dbus[7:4];

  // Other names for the same wires on the sheet: dbus_lo[3:0] = dbus[7:4]; ir_load = dbus_load; q[7:0] = opcode;
  //   q_hi[3:0] = opcode[7:4]; q_lo[3:0] = opcode[3:0]
endmodule
