// Digital circuit memory_bridge.dig as structural Verilog
module memory_bridge (
  input  dbus_assert,
  input  dbus_load,
  input  [7:0] dbus,
  input  [7:0] mbus
);

  _74ls245 _74ls245_1 (.DIR(1'b1), .nOE(dbus_load), .A(dbus), .B(mbus), .VCC(1'b1), .GND(1'b0));
  _74ls245 _74ls245_2 (.DIR(1'b1), .nOE(dbus_assert), .A(mbus), .B(dbus), .VCC(1'b1), .GND(1'b0));

  // Notes on the sheet:
  //   dbus_assert: default 1
  //   dbus_load: default 1
endmodule
