// Digital circuit mode_determination.dig as structural Verilog
module mode_determination (
  input  nREQ,
  input  nNMI,
  input  nIRQ,
  input  NMI_Inhib,
  input  IRQ_Enable,
  output M0,
  output M1
);

  wire and_3_out, IRQ, NMI, not_2_out, REQ;

  not not_1 (REQ, nREQ);
  and and_1 (NMI, ~NMI_Inhib, ~nNMI);  // And
  and and_2 (IRQ, IRQ_Enable, ~nIRQ);  // And
  not not_2 (not_2_out, NMI);
  and and_3 (and_3_out, IRQ, not_2_out);
  or or_1 (M0, NMI, REQ);
  or or_2 (M1, and_3_out, REQ);
endmodule
