// Digital circuit mode_state_machine.dig as structural Verilog
module mode_state_machine (
  input  RST,
  input  M0_tog,
  input  M1_tog,
  input  RST_useq,
  input  CLK,
  input  nRDY,
  output RST_latch,
  output CLK_qual,
  output M0,
  output M1,
  output [2:0] T_state,
  output nBUS
);

  wire and_1_out, and_2_out, and_3_out, and_4_out, and_5_out, instr_end, M0_Latch_nq, M1_Latch_nq, m_rst,
       or_1_out, or_2_out, Sequencer_ovf, xor_1_out;

  nor nor_1 (nBUS, nRDY, RST);
  and and_1 (and_1_out, M1_Latch_nq, M1_tog);
  and and_2 (and_2_out, M1_tog, M1);
  and and_3 (and_3_out, M0_Latch_nq, M0_tog);
  and and_4 (and_4_out, M0_tog, M0);
  xor xor_1 (xor_1_out, CLK_qual, nBUS);
  and and_5 (and_5_out, M0, M1);
  or or_1 (or_1_out, and_1_out, m_rst);
  or or_2 (or_2_out, and_3_out, m_rst);
  D_FF CLK_Latch (.D(xor_1_out), .C(CLK), .Q(CLK_qual));  // open: nQ
  RS_FF_AS u_RST_Latch (.S(RST), .R(and_5_out), .Q(RST_latch));  // open: nQ
  RS_FF M1_Latch (.S(or_1_out), .C(CLK_qual), .R(and_2_out), .Q(M1), .nQ(M1_Latch_nq));
  RS_FF M0_Latch (.S(or_2_out), .C(CLK_qual), .R(and_4_out), .Q(M0), .nQ(M0_Latch_nq));
  Counter #(.Bits(3)) Sequencer (.en(1'b1), .C(CLK_qual), .clr(RST_useq), .out(T_state), .ovf(Sequencer_ovf));
  or or_3 (instr_end, Sequencer_ovf, RST_useq);
  and and_6 (m_rst, instr_end, RST_latch);

  // Other names for the same wires on the sheet: clk_t = CLK_qual; m_0 = M0; m_1 = M1; rst_qual = RST_latch

  // Notes on the sheet:
  //   CLK: Hz: 2
  //   RST will typically be brought high by a
  //   power-on-reset circuit and then held high
  //   until the shadow RAM copier and microcode
  //   copier circuits have completed.
  //   Can also be brought high by a hardware
  //   reset button.
  //   While the RST button is held, the CPU is
  //   effectively halted and should be disconnected
  //   from the memory buses so that other devices
  //   can drive the buses
  //   M0 Toggle and M1 Toggle
  //   are from the control bus, so
  //   should typically be active for only
  //   1 clock cycle.
  //   00 - NRM
  //   01 - EX1
  //   10 - EX2
  //   11 - RST
  //   only want to execute a mode switch
  //   on the boundary of an instruction cycle.
  //   so wait until sequencer overflows,
  //   or until control bus resets it, before
  //   allowing mode latches to force on.
endmodule

/* Test case Counter Increment:
CLK T_state RST M0_tog M1_tog RST_useq RST_latched CLK_qualified
0   0       0   0      0      0        0           0
C   1       0   0      0      0        0           1
C   1       0   0      0      0        0           0
C   2       0   0      0      0        0           1
C   2       0   0      0      0        0           0
C   3       0   0      0      0        0           1
C   3       0   0      0      0        0           0
C   4       0   0      0      0        0           1
C   4       0   0      0      0        0           0
C   5       0   0      0      0        0           1
C   5       0   0      0      0        0           0
C   6       0   0      0      0        0           1
C   6       0   0      0      0        0           0
C   7       0   0      0      0        0           1
C   7       0   0      0      0        0           0
C   0       0   0      0      0        0           1
C   0       0   0      0      0        0           0
*/

/* Test case RST Latch Set:
CLK T_state RST M0_tog M1_tog RST_useq RST_latched CLK_qualified
# Set the latch then show it stays set after RST released
0   0       0   0      0      0        0           0
0   0       1   0      0      0        1           0
0   0       0   0      0      0        1           0
*/

/* Test case RST Latch Clear (ovf):
CLK T_state RST M0_tog M1_tog RST_useq RST_latched CLK_qualified
# Set the latch then show it stays set after RST released
0   0       0   0      0      0        0           0
0   0       1   0      0      0        1           0
0   0       0   0      0      0        1           0
C   1       0   0      0      0        1           1
C   1       0   0      0      0        1           0
C   2       0   0      0      0        1           1
C   2       0   0      0      0        1           0
C   3       0   0      0      0        1           1
C   3       0   0      0      0        1           0
C   4       0   0      0      0        1           1
C   4       0   0      0      0        1           0
C   5       0   0      0      0        1           1
C   5       0   0      0      0        1           0
C   6       0   0      0      0        1           1
C   6       0   0      0      0        1           0
C   7       0   0      0      0        1           1
C   7       0   0      0      0        1           0
C   0       0   0      0      0        0           1
*/

/* Test case RST Latch Clear (RST_useq):
CLK T_state RST M0_tog M1_tog RST_useq RST_latched CLK_qualified
0   0       0   0      0      0        0           0
0   0       1   0      0      0        1           0
0   0       0   0      0      0        1           0
0   0       0   0      0      1        1           0
C   1       0   0      0      0        1           1
C   1       0   0      0      1        1           0
C   0       0   0      0      0        0           0
*/
