// Digital circuit reset_module.dig as structural Verilog
module reset_module (
  input  clk,
  input  nrst_in,
  output nrst
);

  wire and_1_out, counter_1_ovf, d_ff_1_q, reset_1_out;

  Reset reset_1 (.out(reset_1_out));
  D_FF d_ff_1 (.D(nrst_in), .C(clk), .Q(d_ff_1_q));  // open: nQ
  Counter #(.Bits(3)) counter_1 (.en(reset_1_out), .C(clk), .clr(d_ff_1_q), .ovf(counter_1_ovf));  // open: out
  and and_1 (and_1_out, reset_1_out, counter_1_ovf);
  RS_FF_AS rs_ff_as_1 (.S(and_1_out), .R(d_ff_1_q), .Q(nrst));  // open: nQ

  // Notes on the sheet:
  //   clk: Hz: 4
endmodule
