// Digital circuit status_expanded.dig as structural Verilog
module status_expanded (
  input  Reset,
  input  Clock,
  input  [4:0] ALU_Flags_In,
  input  [7:0] DBUS,
  input  nDBUS_nLoad,
  input  nSet_nSUP,
  input  nSet_nUBR,
  input  nClear_nUBR,
  input  nSet_nNMI_nInhibit,
  output [7:0] Status_Register
);

  wire or_1_out;
  wire [3:0] input_hi, input_lo;
  wire [7:5] multiplexer_1_out;

  Multiplexer multiplexer_1 (.sel(nSet_nSUP), .in_0(1'b0), .in_1(Status_Register[5]), .out(multiplexer_1_out[5]));
  Multiplexer #(.Selector_Bits(2)) multiplexer_2 (
    .sel({nSet_nUBR, nClear_nUBR}), .in_0(Status_Register[6]), .in_1(1'b1), .in_2(1'b0),
    .in_3(Status_Register[6]), .out(multiplexer_1_out[6]));
  Multiplexer multiplexer_3 (
    .sel(nSet_nNMI_nInhibit), .in_0(1'b1), .in_1(Status_Register[7]), .out(multiplexer_1_out[7]));
  or or_1 (or_1_out, nDBUS_nLoad, Status_Register[5]);
  Multiplexer #(.Bits(8)) multiplexer_4 (
    .sel(or_1_out), .in_0(DBUS), .in_1({multiplexer_1_out, ALU_Flags_In}), .out({input_hi, input_lo}));
  // _74ls173 _74ls173_1: pin names not known; wires that end beside it: input_lo, Reset, Clock, 1'b0, 1'b0, 1'b0, 1'b0, 1'b1, 1'b0, Status_Register[3:0]
  // _74ls173 _74ls173_2: pin names not known; wires that end beside it: input_hi, Reset, Clock, 1'b0, 1'b0, 1'b0, 1'b0, 1'b1, 1'b0, Status_Register[7:4]

  // Other names for the same wires on the sheet: alu_flags[4:0] = Status_Register[4:0]; sup = Status_Register[5];
  //   ubr = Status_Register[6]; nmi = Status_Register[7]; clk = Clock; clr_ubr = nClear_nUBR; dbus_load = nDBUS_nLoad;
  //   rst = Reset; set_nmi = nSet_nNMI_nInhibit; set_sup = nSet_nSUP; set_ubr = nSet_nUBR

  // Notes on the sheet:
  //   Reset: default 1
  //   nDBUS_nLoad: default 1
  //   nSet_nSUP: default 1
  //   nSet_nUBR: default 1
  //   nClear_nUBR: default 1
  //   nSet_nNMI_nInhibit: default 1
  //   Zero because SUP active low
endmodule
