// Digital circuit telnet_example.dig as structural Verilog
module telnet_example (
  input  [7:0] in_1,
  input  in_2,
  input  clk
);

  Terminal terminal_1 (.D(in_1), .C(clk), .en(in_2));

  // Notes on the sheet:
  //   clk: Hz: 10
endmodule
