// Digital circuit temp_reg_pair.dig as structural Verilog
module temp_reg_pair (
  input  nhi_dbus_load,
  input  nlo_dbus_load,
  input  nhi_dbus_assert,
  input  nlo_dbus_assert,
  input  nhi_lhs_assert,
  input  nlo_lhs_assert,
  input  nhi_rhs_assert,
  input  nlo_rhs_assert,
  input  [7:0] dbus,
  input  clr,
  input  nclk,
  input  naddr_assert,
  output [7:0] reg_hi,
  output [7:0] reg_lo,
  output [15:0] xfer,
  output [15:0] addr
);

  // _74ls173 _74ls173_1: pin names not known; wires that end beside it: dbus[7:4], clr, nclk, nhi_dbus_load, nhi_dbus_load, 1'b0, 1'b0, 1'b1, 1'b0, reg_hi[7:4]
  _74ls245 Hi_Reg_to_lhs (.DIR(1'b1), .nOE(nhi_lhs_assert), .A(reg_hi), .B(xfer[15:8]), .VCC(1'b1), .GND(1'b0));
  // _74ls173 _74ls173_2: pin names not known; wires that end beside it: dbus[3:0], clr, nclk, nhi_dbus_load, nhi_dbus_load, 1'b0, 1'b0, 1'b1, 1'b0, reg_hi[3:0]
  _74ls245 Hi_Reg_to_dbus (.DIR(1'b1), .nOE(nhi_dbus_assert), .A(reg_hi), .B(dbus), .VCC(1'b1), .GND(1'b0));
  _74ls245 Hi_Reg_to_rhs (.DIR(1'b1), .nOE(nhi_rhs_assert), .A(reg_hi), .B(xfer[7:0]), .VCC(1'b1), .GND(1'b0));
  _74ls245 Hi_Reg_to_addr (.DIR(1'b1), .nOE(naddr_assert), .A(reg_hi), .B(addr[15:8]), .VCC(1'b1), .GND(1'b0));
  // _74ls173 _74ls173_3: pin names not known; wires that end beside it: dbus[7:4], clr, nclk, nlo_dbus_load, nlo_dbus_load, 1'b0, 1'b0, 1'b1, 1'b0, reg_lo[7:4]
  _74ls245 Lo_Reg_to_addr (.DIR(1'b1), .nOE(naddr_assert), .A(reg_lo), .B(addr[7:0]), .VCC(1'b1), .GND(1'b0));
  _74ls245 Lo_Reg_to_lhs (.DIR(1'b1), .nOE(nlo_lhs_assert), .A(reg_lo), .B(xfer[15:8]), .VCC(1'b1), .GND(1'b0));
  // _74ls173 _74ls173_4: pin names not known; wires that end beside it: dbus[3:0], clr, nclk, nlo_dbus_load, nlo_dbus_load, 1'b0, 1'b0, 1'b1, 1'b0, reg_lo[3:0]
  _74ls245 Lo_Reg_to_dbus (.DIR(1'b1), .nOE(nlo_dbus_assert), .A(reg_lo), .B(dbus), .VCC(1'b1), .GND(1'b0));
  _74ls245 Lo_Reg_to_rhs (.DIR(1'b1), .nOE(nlo_rhs_assert), .A(reg_lo), .B(xfer[7:0]), .VCC(1'b1), .GND(1'b0));

  // Other names for the same wires on the sheet: q_hi[7:0] = reg_hi; q_lo[7:0] = reg_lo; addr_hi[7:0] = addr[15:8];
  //   addr_lo[7:0] = addr[7:0]; assert_addr = naddr_assert; assert_hi_dbus = nhi_dbus_assert;
  //   assert_hi_lhs = nhi_lhs_assert; assert_hi_rhs = nhi_rhs_assert; assert_lo_dbus = nlo_dbus_assert;
  //   assert_lo_lhs = nlo_lhs_assert; assert_lo_rhs = nlo_rhs_assert; dbus_lo[3:0] = dbus[3:0];
  //   dbus_hi[3:0] = dbus[7:4]; lhs[7:0] = xfer[15:8]; xfer_10[3:0] = xfer[11:8]; xfer_11[3:0] = xfer[15:12];
  //   load_hi_dbus = nhi_dbus_load; load_lo_dbus = nlo_dbus_load; rhs[7:0] = xfer[7:0]; xfer_00[3:0] = xfer[3:0];
  //   xfer_01[3:0] = xfer[7:4]

  // Notes on the sheet:
  //   nhi_dbus_load: default 1
  //   nlo_dbus_load: default 1
  //   nhi_dbus_assert: default 1
  //   nlo_dbus_assert: default 1
  //   nhi_lhs_assert: default 1
  //   nlo_lhs_assert: default 1
  //   nhi_rhs_assert: default 1
  //   nlo_rhs_assert: default 1
  //   naddr_assert: default 1
endmodule
