// Digital circuit temp_register2.dig as structural Verilog
module temp_register2 (
  input  [7:0] dbus,
  input  clk,
  input  clr,
  input  assert_dbus,
  input  assert_rhs,
  input  load_dbus,
  output [7:0] rhs,
  output [7:0] \reg 
);

  // _74ls173 T2_hi: pin names not known; wires that end beside it: dbus[7:4], 1'b1, 1'b0, clr, clk, load_dbus, load_dbus, 1'b0, 1'b0, \reg [3:0]
  // _74ls173 T2_lo: pin names not known; wires that end beside it: dbus[3:0], 1'b1, 1'b0, clr, clk, load_dbus, load_dbus, 1'b0, 1'b0, \reg [7:4]
  _74ls245 to_DBUS (.DIR(1'b1), .nOE(assert_dbus), .A(\reg ), .B(dbus), .VCC(1'b1), .GND(1'b0));
  _74ls245 to_RHS (.DIR(1'b1), .nOE(assert_rhs), .A(\reg ), .B(rhs), .VCC(1'b1), .GND(1'b0));

  // Other names for the same wires on the sheet: d_lo[3:0] = dbus[3:0]; d_hi[3:0] = dbus[7:4]; load = load_dbus;
  //   q[7:0] = \reg ; q_hi[3:0] = \reg [7:4]; q_lo[3:0] = \reg [3:0]
endmodule
