// Digital circuit triple_clock.dig as structural Verilog
module triple_clock (
  input  [2:0] tog_mode,
  input  nbrk,
  input  [2:0] rst_mode,
  input  run_clk,
  input  demo_clk,
  input  step_clk,
  output cpu_clk_out,
  output run_clk_out,
  output [2:0] mode
);

  wire _74574_1_p13, _74574_1_p14, _74574_1_p15, and_1_out, and_2_out, and_3_out, nand_1_out, nand_2_out,
       nand_3_out;

  nand nand_1 (nand_1_out, and_2_out, and_3_out);
  nand nand_2 (nand_2_out, and_1_out, and_3_out);
  nand nand_3 (nand_3_out, and_1_out, and_2_out);
  and and_1 (and_1_out, nand_1_out, rst_mode[0], tog_mode[0]);
  and and_2 (and_2_out, nand_2_out, rst_mode[1], tog_mode[1]);
  and and_3 (and_3_out, rst_mode[2], nand_3_out, tog_mode[2], nbrk);
  // _74574 _74574_1: pin names not known; wires that end beside it: 1'b0, run_clk, and_3_out, and_1_out, and_2_out, 1'b0, 1'b0, 1'b0, 1'b0, 1'b0, 1'b1, 1'b0, _74574_1_p13, _74574_1_p14, _74574_1_p15
  not not_1 (mode[2], _74574_1_p13);
  not not_2 (mode[1], _74574_1_p15);
  not not_3 (mode[0], _74574_1_p14);
  // _74151 _74151_1: pin names not known; wires that end beside it: _74574_1_p13, _74574_1_p14, _74574_1_p15, 1'b0, step_clk, step_clk, step_clk, run_clk, step_clk, demo_clk, step_clk, step_clk, 1'b1, 1'b0, cpu_clk_out

  assign run_clk_out = run_clk;

  // Other names for the same wires on the sheet: clk_crystal = run_clk; clk_demo = demo_clk; clk_step = step_clk;
  //   nrun_rst = rst_mode[0]; ndemo_rst = rst_mode[1]; nstep_rst = rst_mode[2]; nrun = tog_mode[0];
  //   ndemo = tog_mode[1]; nbreak = tog_mode[2]

  // Notes on the sheet:
  //   nbrk: default 1
  //   run_clk: Hz: 5
endmodule
