// Digital circuit vdp.dig as structural Verilog
module vdp (
  input  px_clk,
  output px_clk_hf,
  output [8:0] x_pos,
  output [9:0] y_pos,
  output inv_px_clk
);

  wire comparator_1_eq, comparator_2_eq, comparator_3_eq, comparator_4_eq, comparator_5_eq, comparator_6_eq,
       d_ff_1_nq, H, not_2_out, not_3_out, or_1_out, V;
  wire [2:0] g, r;
  wire [2:1] b;
  wire [7:0] rom_1_d;

  D_FF d_ff_1 (.D(d_ff_1_nq), .C(px_clk), .Q(px_clk_hf), .nQ(d_ff_1_nq));
  Counter #(.Bits(9)) Px_Ct (.en(1'b1), .C(px_clk_hf), .clr(comparator_3_eq), .out(x_pos));  // open: ovf
  Counter #(.Bits(10)) Ln_Ct (.en(comparator_3_eq), .C(px_clk_hf), .clr(comparator_6_eq), .out(y_pos));  // open: ovf
  Comparator #(.Bits(9)) comparator_1 (.a(x_pos), .b(9'h147), .eq(comparator_1_eq));  // open: gt, lt
  Comparator #(.Bits(9)) comparator_2 (.a(x_pos), .b(9'h177), .eq(comparator_2_eq));  // open: gt, lt
  Comparator #(.Bits(9)) comparator_3 (.a(x_pos), .b(9'h18f), .eq(comparator_3_eq));  // open: gt, lt
  Comparator #(.Bits(10)) comparator_4 (.a(y_pos), .b(10'h1e9), .eq(comparator_4_eq));  // open: gt, lt
  Comparator #(.Bits(10)) comparator_5 (.a(y_pos), .b(10'h1eb), .eq(comparator_5_eq));  // open: gt, lt
  Comparator #(.Bits(10)) comparator_6 (.a(y_pos), .b(10'h20d), .eq(comparator_6_eq));  // open: gt, lt
  RS_FF_AS H_SYNC (.S(comparator_1_eq), .R(comparator_2_eq), .Q(H));  // open: nQ
  RS_FF_AS V_SYNC (.S(comparator_4_eq), .R(comparator_5_eq), .Q(V));  // open: nQ
  not not_1 (inv_px_clk, px_clk);
  not not_2 (not_2_out, H);
  not not_3 (not_3_out, V);
  VGA vga_1 (.R(r), .G(g), .B({b, 1'b0}), .H(not_2_out), .V(not_3_out), .C(inv_px_clk));
  ROM #(.AddrBits(17), .Bits(8)) rom_1 (.A({y_pos[8:1], x_pos}), .sel(1'b1), .D(rom_1_d));
  or or_1 (or_1_out, H, V);
  Multiplexer #(.Bits(8)) multiplexer_1 (.sel(or_1_out), .in_0(rom_1_d), .in_1({8{1'b0}}), .out({r, g, b}));

  // Notes on the sheet:
  //   px_clk: Hz: 25175000
  //   rom_1 loads parrot.bin
endmodule
